// Digital circuit Assembly Workspace.dig as structural Verilog
module Assembly_Workspace (
  input  clk
);

  wire button_1_out, telescope_assembler_computer_1_output_write, telescope_assembler_computer_1_running,
       telescope_assembler_computer_1_terminal_write;
  wire [6:0] telescope_assembler_computer_1_terminal_data, Text_Input_d;
  wire [15:0] telescope_assembler_computer_1_output_address, telescope_assembler_computer_1_output_data;
  wire [23:0] telescope_assembler_computer_1_text_address;

  ROM #(.AddrBits(24), .Bits(7)) Text_Input (
    .A(telescope_assembler_computer_1_text_address), .sel(1'b1), .D(Text_Input_d));
  Button button_1 (.out(button_1_out));
  Telescope_Assembler_Computer telescope_assembler_computer_1 (
    .Assemble(button_1_out), .Clock(clk), .Text_Input(Text_Input_d),
    .Running(telescope_assembler_computer_1_running),
    .Text_Address(telescope_assembler_computer_1_text_address),
    .Output_Address(telescope_assembler_computer_1_output_address),
    .Output_Data(telescope_assembler_computer_1_output_data),
    .Output_Write(telescope_assembler_computer_1_output_write),
    .Terminal_Data(telescope_assembler_computer_1_terminal_data),
    .Terminal_Write(telescope_assembler_computer_1_terminal_write));
  LED led_1 (.in(telescope_assembler_computer_1_running));
  EEPROMDualPort #(.AddrBits(16), .Bits(16)) MC_Output (
    .A(telescope_assembler_computer_1_output_address), .Din(telescope_assembler_computer_1_output_data),
    .str(telescope_assembler_computer_1_output_write), .C(clk), .ld(1'b0));  // open: D
  Terminal #(.termWidth(130), .termHeight(40)) terminal_1 (
    .D(telescope_assembler_computer_1_terminal_data), .C(clk),
    .en(telescope_assembler_computer_1_terminal_write));

  // Notes on the sheet:
  //   clk: Hz: 15000
  //   contents of Text_Input (hex, n*v repeats v):
  //   4a,4d,50,20,3e,53,74,61,72,74,50,6f,69,6e,74,a,a,28,2f,20,43,6f
  //   ,6e,73,74,61,6e,74,73,2c,20,76,61,72,69,61,62,6c,65,73,2c,20,61
  //   ,6e,64,20,74,61,62,6c,65,73,2e,a,a,2f,53,45,54,20,54,4f,20,30
  //   ,20,49,46,20,41,53,53,45,4d,42,4c,49,4e,47,20,54,4f,20,50,4c,41
  //   ,49,4e,20,4d,41,43,48,49,4e,45,20,43,4f,44,45,2c,20,53,45,54,20
  //   ,54,4f,20,31,20,49,46,20,41,53,53,45,4d,42,4c,49,4e,47,20,54,4f
  //   ,20,4c,4f,41,44,41,42,4c,45,a,40,47,45,4e,4c,4f,41,44,41,42,4c
  //   ,45,20,3d,20,30,a,a,40,49,4e,46,4c,47,20,3d,20,30,a,40,4f,55,54
  //   ,46,4c,47,20,3d,20,30,78,38,30,30,a,a,40,54,41,42,4c,45,53,54
  //   ,4f,50,20,3d,20,30,78,4*46,20,20,2f,20,4d,75,73,74,20,73,74,61
  //   ,79,20,4e,55,4c,4c,2e,a,a,40,43,41,4c,48,41,53,48,20,3d,20,30
  //   ,78,62,30,32,33,a,a,2f,20,49,6e,73,74,72,75,63,74,69,6f,6e,20
  //   ,74,61,62,6c,65,20,65,6e,74,72,69,65,73,3a,20,28,6d,6e,65,6d,6f
  //   ,6e,69,63,5f,68,61,73,68,2c,20,74,72,61,6e,73,6c,61,74,69,6f,6e
  //   ,2c,20,6f,70,65,72,61,6e,64,5f,62,69,74,6d,61,70,29,a,23,49,6e
  //   ,73,74,54,61,62,6c,65,20,3d,20,28,30,78,64,39,65,64,2c,20,30,78
  //   ,33,30,30,30,2c,20,30,62,30,30,31,31,2c,20,20,2f,20,4d,4f,56,a
  //   ,14*20,30,78,39,39,32,61,2c,20,30,78,34,30,30,30,2c,20,30,62,30
  //   ,31,30,30,2c,20,20,2f,20,4a,49,46,a,14*20,30,78,61,34,38,63,2c
  //   ,20,30,78,35,30,30,30,2c,20,30,62,30,30,31,30,2c,20,20,2f,20,4c
  //   ,44,49,a,14*20,30,78,39,31,65,63,2c,20,30,78,36,30,30,30,2c,20
  //   ,30,62,30,30,31,31,2c,20,20,2f,20,4c,4f,44,a,14*20,30,78,63,61
  //   ,39,33,2c,20,30,78,37,30,30,30,2c,20,30,62,30,30,31,31,2c,20,20
  //   ,2f,20,53,54,52,a,14*20,30,78,39,39,38,31,2c,20,30,78,38,30,30,30
  //   ,2c,20,30,62,30,31,31,31,2c,20,20,2f,20,41,4c,46,a,14*20,30,78
  //   ,39,39,32,31,2c,20,30,78,39,30,30,30,2c,20,30,62,4*31,2c,20,20
  //   ,2f,20,41,49,46,a,14*20,30,78,64,35,38,31,2c,20,30,78,41,30,30,30
  //   ,2c,20,30,62,30,31,31,31,2c,20,20,2f,20,41,4c,55,a,14*20,30,78
  //   ,61,35,38,31,2c,20,30,78,42,30,30,30,2c,20,30,62,4*31,2c,20,20
  //   ,2f,20,41,4c,49,a,14*20,30,78,62,38,63,31,2c,20,30,78,43,30,30,30
  //   ,2c,20,30,62,30,31,31,31,2c,20,20,2f,20,41,46,4e,a,14*20,30,78
  //   ,62,39,32,31,2c,20,30,78,44,30,30,30,2c,20,30,62,4*31,2c,20,20
  //   ,2f,20,41,49,4e,a,9,9,9,20,20,30,78,64,30,62,32,2c,20,30,78,33
  //   ,30,38,37,2c,20,30,62,4*30,2c,20,20,2f,20,52,45,54,a,14*20,30
  //   ,78,62,65,35,61,2c,20,30,78,62,31,30,30,2c,20,30,62,30,30,31,30
  //   ,2c,20,20,2f,20,5a,52,4f,a,14*20,30,78,62,32,61,65,2c,20,30,78
  //   ,62,30,30,30,2c,20,30,62,30,30,31,30,2c,20,20,2f,20,4e,55,4c,a
  //   ,14*20,30,78,63,63,33,30,2c,20,30,78,39,32,30,30,2c,20,30,62,30,30
  //   ,31,30,2c,20,20,2f,20,50,41,53,a,9,9,9,20,20,30,78,38,64,63,39
  //   ,2c,20,30,78,39,39,30,31,2c,20,30,62,30,30,31,30,2c,20,20,2f,20
  //   ,49,4e,43,20,28,73,65,74,20,66,6c,61,67,73,29,a,14*20,30,78,38
  //   ,63,61,34,2c,20,30,78,39,62,30,31,2c,20,30,62,30,30,31,30,2c,20,20
  //   ,2f,20,44,45,43,20,28,73,65,74,20,66,6c,61,67,73,29,a,14*20,30
  //   ,78,61,32,37,30,2c,20,30,78,62,62,62,30,2c,20,30,62,31,30,30,31
  //   ,2c,20,20,2f,20,50,53,48,a,14*20,30,78,63,31,66,30,2c,20,30,78
  //   ,62,39,62,30,2c,20,30,62,31,30,30,31,2c,20,20,2f,20,50,4f,50,a
  //   ,14*20,30,78,63,31,61,33,2c,20,30,78,63,62,30,30,2c,20,30,62,30,30
  //   ,31,31,2c,20,20,2f,20,43,4d,50,a,14*20,30,78,63,31,61,61,2c,20
  //   ,30,78,34,36,30,30,2c,20,30,62,4*30,2c,20,20,2f,20,4a,4d,50,a
  //   ,14*20,30,78,63,34,61,61,2c,20,30,78,34,30,30,30,2c,20,30,62,4*30
  //   ,2c,20,20,2f,20,4a,45,51,a,14*20,30,78,39,35,63,61,2c,20,30,78
  //   ,34,38,30,30,2c,20,30,62,4*30,2c,20,20,2f,20,4a,4e,45,a,14*20
  //   ,30,78,64,31,38,61,2c,20,30,78,34,31,30,30,2c,20,30,62,4*30,2c
  //   ,20,20,2f,20,4a,4c,54,a,14*20,30,78,39,34,65,61,2c,20,30,78,34
  //   ,39,30,30,2c,20,30,62,4*30,2c,20,20,2f,20,4a,47,45,a,9,9,9,20,20
  //   ,30,78,63,66,33,33,2c,20,30,78,32,30,30,30,2c,20,30,62,4*30,2c
  //   ,20,20,2f,20,53,59,53,a,9,9,9,20,20,30,78,62,36,37,32,2c,20,30
  //   ,78,31,30,30,30,2c,20,30,62,4*30,2c,20,20,2f,20,52,53,4d,a,9,9,9
  //   ,20,20,30,78,64,31,38,38,2c,20,30,78,4*30,2c,20,30,62,4*30,2c
  //   ,20,20,2f,20,48,4c,54,a,9,9,9,20,20,30,78,63,31,65,65,2c,20,30
  //   ,78,46,30,30,30,2c,20,30,62,4*30,2c,20,20,2f,20,4e,4f,50,a,14*20
  //   ,3e,54,41,42,4c,45,53,54,4f,50,a,14*20,29,a,a,2f,20,52,65,67,69
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  //   Make sure MC Output is cleared (and make sure to press OK)
  //   contents of MC_Output (hex, n*v repeats v):
  //   4600,14b,d9ed,3000,3,992a,4000,4,a48c,5000,2,91ec,6000,3,ca93
  //   ,7000,3,9981,8000,7,9921,9000,f,d581,a000,7,a581,b000,f,b8c1,c000
  //   ,7,b921,d000,f,d0b2,3087,0,be5a,b100,2,b2ae,b000,2,cc30,9200,2
  //   ,8dc9,9901,2,8ca4,9b01,2,a270,bbb0,9,c1f0,b9b0,9,c1a3,cb00,3,c1aa
  //   ,4600,0,c4aa,4000,0,95ca,4800,0,d18a,4100,0,94ea,4900,0,cf33,2000
  //   ,0,b672,1000,0,d188,0,0,c1ee,f000,0,ffff,40f2,0,44f2,1,48f2,2
  //   ,4cf2,3,50f2,4,54f2,5,58f2,6,d2af,6,5cf2,7,32,7,70,8,1e9,9,9d86
  //   ,a,213,b,8988,c,9283,d,8e05,e,8705,f,ffff,d1ee,0,91c1,1,24f,2
  //   ,b0b3,6,9cae,8,9081,9,8ab3,b,c9f8,3,8993,4,8a53,5,b2ad,d,d924
  //   ,e,ea25,0,ea8c,1,c823,2,cacf,3,9250,4,d2f0,5,d654,6,e8ae,8,e8a7
  //   ,9,c86e,a,d9ee,b,c9d0,c,ddd0,d,91d2,7,8c81,a,8853,c,91ed,f,8dc5
  //   ,7,ffff,130*0,50a0,0,3069,3087,50a0,0,5090,0,3087,50a0,800,3090
  //   ,3087,50a0,0,5090,0,50b0,0,70bb,13d,4600,2e6,b120,6022,13c,b160
  //   ,cb12,4000,169,6031,bc,d636,4000,162,b939,b13f,ad60,a963,b911
  //   ,cb12,4800,15c,3087,b100,6000,13c,db01,4800,175,b160,6066,bc,b16f
  //   ,3087,5000,1,6000,bc,d606,4800,181,5000,a,b110,4600,155,5010,78
  //   ,cb01,4800,18c,5000,10,5010,2,4600,155,5010,62,cb01,4800,197,5000
  //   ,2,5010,2,4600,155,0,fff0,4600,14b,b100,b110,6011,13d,b130,6033
  //   ,13c,cb01,4100,1a9,0,fff1,4600,14b,6020,4c2,cb32,4800,1c4,5040
  //   ,1,cb42,4800,1b8,a902,6060,4c2,4600,1c8,3050,a954,6055,4c2,6064
  //   ,bc,cb56,4800,1c4,b941,4600,1b0,a902,b901,4600,1a2,3087,7077,1d2
  //   ,3061,5050,ffff,6046,0,cb40,4000,0,cb45,4000,1d9,a962,4600,1ce
  //   ,3065,3087,5030,3e,cb30,4000,1fe,5030,2c,cb30,4900,1ea,5030,3a
  //   ,cb03,4100,1fe,5030,23,cb30,4000,1fe,5030,27,cb30,4000,1fe,5030
  //   ,22,cb30,4000,1fe,9200,4000,1fe,b160,3087,b060,3087,5060,0,3059
  //   ,cb50,4000,209,cb56,4800,202,3087,bbb1,707b,0,50a0,0,3009,d606
  //   ,4800,22a,5070,20f,5010,25,cb01,4000,200,5010,2f,cb01,4800,223
  //   ,5000,a,4600,200,3078,b974,4600,1db,9260,4000,20f,5010,0,cb01
  //   ,4800,235,7000,bc,5040,1,4600,27f,b140,5010,27,cb01,4800,247,7004
  //   ,bc,3009,9941,7004,bc,3009,9941,7004,bc,4600,27f,5010,22,cb01
  //   ,4800,258,7004,bc,9941,3009,cb01,4800,24c,7004,bc,9941,4600,27f
  //   ,5070,263,7004,bc,b941,3009,d606,4800,25a,4600,1db,d260,4000,27f
  //   ,5030,25,cb03,4800,26f,5070,27f,4600,200,5030,2f,cb03,4800,27a
  //   ,5000,a,5070,27f,4600,200,5030,0,cb03,4800,25a,7044,13c,607b,0
  //   ,b9b1,3087,b110,6011,13d,b100,6000,13c,7001,4c2,b911,5020,1,6032
  //   ,bc,7031,4c2,b911,b921,cb20,4800,290,7011,13d,3087,5010,1f,b160
  //   ,5000,2,6000,bc,3060,a161,b46a,b606,b40f,a260,5000,1,6000,bc,a101
  //   ,b405,a260,b100,6000,bc,a101,a260,3087,bbb2,700b,0,707b,1,3078
  //   ,b974,4600,20a,b110,6011,13c,db12,4800,2cb,b120,7021,bc,b911,7011
  //   ,13c,3078,b974,4600,29c,3006,601b,0,5020,2,3078,b974,4600,1c9
  //   ,d961,4a00,2df,0,fff4,4600,14b,b961,6066,0,607b,1,b9b2,3087,b100
  //   ,bbb1,700b,0,3078,b974,4600,20a,b100,6000,bc,5010,0,cb01,4000
  //   ,3bb,5010,23,cb01,4800,30b,3078,b974,4600,285,600b,0,b110,6011
  //   ,13d,7001,4c2,b911,7011,13d,4600,2ea,5010,40,cb01,4800,334,3078
  //   ,b974,4600,285,3078,b974,4600,20a,b100,6000,bc,5010,27,cb01,4800
  //   ,326,5060,1,6066,bc,4600,32a,3078,b974,4600,16a,b100,6000,13d
  //   ,7060,4c2,b901,7000,13d,4600,2ea,5010,27,cb01,4800,340,600b,0
  //   ,b901,700b,0,4600,2ea,5010,22,cb01,4800,350,b110,6011,13c,bb11
  //   ,600b,0,a901,700b,0,4600,2ea,5010,7e,cb01,4800,364,5000,a,5010
  //   ,1,3078,b974,4600,155,600b,0,a906,700b,0,4600,2ea,d606,4800,36e
  //   ,600b,0,b901,700b,0,4600,2ea,3078,b974,4600,29c,5010,b023,cb16
  //   ,4800,37e,600b,0,b903,700b,0,4600,2ea,600b,0,b901,700b,0,3006
  //   ,5010,2,5020,3,3078,b974,4600,1c9,d961,4a00,393,0,fff3,4600,14b
  //   ,b962,6006,0,bbb1,d602,4000,3a2,700b,0,3078,b974,4600,20a,600b
  //   ,0,d601,4000,3ad,700b,0,3078,b974,4600,20a,600b,0,d600,4000,3b8
  //   ,700b,0,3078,b974,4600,20a,600b,0,b9b1,4600,2ea,5000,0,9200,4000
  //   ,3c7,600b,0,50a0,800,3090,50a0,0,5090,0,b9b1,4600,3cc,3078,b974
  //   ,4600,20a,b100,6000,bc,5010,23,cb01,4000,3cc,5010,0,cb01,4000
  //   ,4b7,5010,3e,cb01,4800,3ed,3078,b974,4600,19b,50a0,800,3096,50a0
  //   ,0,4600,3cc,5010,40,cb01,4800,3f6,5070,3cc,4600,20a,5010,27,cb01
  //   ,4800,406,5000,1,6000,bc,50a0,800,3090,50a0,0,4600,3cc,5010,22
  //   ,cb01,4800,420,b100,6010,13c,bb11,50a0,800,9901,cb01,4000,41a
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endmodule
