// Digital circuit CPU Testspace.dig as structural Verilog
module CPU_Testspace (
  input  clk,
  input  [15:0] in_2
);

  wire add_1_s, button_1_out, button_2_out, counter_1_out, glass_cpu_1_p11, glass_cpu_1_p14, glass_cpu_1_p15,
       glass_cpu_1_p16, glass_cpu_1_p17, register_1_q;
  wire [15:0] glass_cpu_1_p4, glass_cpu_1_p12, glass_cpu_1_p13;

  Button button_1 (.out(button_1_out));
  Button button_2 (.out(button_2_out));
  // Glass_CPU glass_cpu_1: pin names not known; wires that end beside it: button_1_out, button_2_out, clk, glass_cpu_1_p4, in_2, 4'b0000, 4'b0000, 4'b0000, 4'b0000, 1'b0, glass_cpu_1_p11, glass_cpu_1_p12, glass_cpu_1_p13, glass_cpu_1_p14, glass_cpu_1_p15, glass_cpu_1_p16, glass_cpu_1_p17
  RAMDualPort #(.AddrBits(16), .isProgramMemory("true"), .Bits(16)) Program_Memory (
    .A(glass_cpu_1_p12), .Din(glass_cpu_1_p13), .str(glass_cpu_1_p14), .C(clk), .ld(1'b1), .D(glass_cpu_1_p4));
  Counter counter_1 (.en(glass_cpu_1_p11), .C(clk), .clr(1'b0), .out(counter_1_out));  // open: ovf
  Add add_1 (.a(glass_cpu_1_p15), .b(1'b0), .c_i(1'b0), .s(add_1_s));  // open: c_o
  Register register_1 (.D(glass_cpu_1_p16), .C(clk), .en(glass_cpu_1_p17), .Q(register_1_q));
  // Probe Cycles Used on counter_1_out
  // Probe RLS Line on add_1_s
  // Probe Test Output on register_1_q
  // Pins of 1 and 16 bits meet at 16'h2
endmodule
