// Digital circuit REMC.dig as structural Verilog
// Rising edge monostable circuit. Generates a very short pulse.
module REMC (
  input  I,
  output O
);

  wire delay_1_out;

  Delay delay_1 (.in(I), .out(delay_1_out));
  and and_1 (O, I, ~delay_1_out);  // And
endmodule
