// Digital circuit TBOS Testing.dig as structural Verilog
module TBOS_Testing (
  input  clk
);

  wire button_1_out, button_2_out, button_3_out, telescope_computing_system_1_os_running;
  wire [15:0] Keyboard_0_d, Root_Drive_d, TBOS_1_0_d, telescope_computing_system_1_os_adr,
       telescope_computing_system_1_status_code, telescope_computing_system_1_tk1_out;
  wire [16:16] Keyboard_0_av;
  wire [18:16] telescope_computing_system_1_tk1_out_2;
  wire [33:0] telescope_computing_system_1_d0_out;

  LED OS_Is_Running (.in(telescope_computing_system_1_os_running));
  // Probe Status on telescope_computing_system_1_status_code
  Telescope_Computing_System telescope_computing_system_1 (
    .OS_Running(telescope_computing_system_1_os_running),
    .Status_Code(telescope_computing_system_1_status_code), .Power_On(button_1_out), .Clock_Input(clk),
    .Pause(button_2_out), .Pause_Mode(1'b1), .STOP(button_3_out),
    .OS_Adr(telescope_computing_system_1_os_adr), .OS_In(TBOS_1_0_d), .D0_In(Root_Drive_d),
    .D0_Out(telescope_computing_system_1_d0_out), .D1_In({16{1'b0}}), .D2_In({16{1'b0}}), .D3_In({16{1'b0}}),
    .TNET_I_0({20{1'b0}}), .TNET_I_1({20{1'b0}}), .TNET_I_2({20{1'b0}}), .TNET_I_3({20{1'b0}}),
    .K0_In({17{1'b0}}),
    .TK1_Out({telescope_computing_system_1_tk1_out_2, telescope_computing_system_1_tk1_out}),
    .K1_In({Keyboard_0_av[16], Keyboard_0_d}), .K2_In({17{1'b0}}), .K3_In({17{1'b0}}), .GPI_0({18{1'b0}}),
    .GPI_1({18{1'b0}}), .GPI_2({18{1'b0}}), .GPI_3({18{1'b0}}));  // open: D1_Out, D2_Out, D3_Out, TNET_O_0, TNET_O_1, TNET_O_2, TNET_O_3, TK0_Out, TK2_Out, TK3_Out, GPO_0, GPO_1, GPO_2, GPO_3
  Button button_1 (.out(button_1_out));
  Button button_2 (.out(button_2_out));
  Button button_3 (.out(button_3_out));
  Keyboard Keyboard_0 (
    .C(telescope_computing_system_1_tk1_out_2[18]), .en(telescope_computing_system_1_tk1_out_2[16]),
    .D(Keyboard_0_d), .av(Keyboard_0_av[16]));
  Terminal terminal_1 (
    .D(telescope_computing_system_1_tk1_out), .C(telescope_computing_system_1_tk1_out_2[18]),
    .en(telescope_computing_system_1_tk1_out_2[17]));
  // Probe OS Boot Drive Address on telescope_computing_system_1_os_adr
  ROM #(.AddrBits(16), .Bits(16)) TBOS_1_0 (.A(telescope_computing_system_1_os_adr), .sel(1'b1), .D(TBOS_1_0_d));
  // Probe Current Root Drive Address on telescope_computing_system_1_d0_out[31:16]
  EEPROMDualPort #(.AddrBits(16), .isProgramMemory("true"), .Bits(16)) Root_Drive (
    .A(telescope_computing_system_1_d0_out[31:16]), .Din(telescope_computing_system_1_d0_out[15:0]),
    .str(telescope_computing_system_1_d0_out[32]), .C(telescope_computing_system_1_d0_out[33]), .ld(1'b1),
    .D(Root_Drive_d));

  // Notes on the sheet:
  //   clk: Hz: 256
  //   contents of TBOS_1_0 (hex, n*v repeats v):
  //   4600,f,48,65,6c,6c,6f,20,57,6f,72,6c,64,21,ffff,50a0,4800,b100
  //   ,b010,6020,2,cb21,4000,1c,3092,9901,4600,13
  //   contents of Root_Drive (hex, n*v repeats v):
  //   1e,4600,f,48,65,6c,6c,6f,20,57,6f,72,6c,64,21,ffff,b100,5010,ffff
  //   ,50a0,4800,6020,2,cb21,4000,1d,3092,9901,4600,14
endmodule
