// Digital circuit GCPU ALU.dig as structural Verilog
module GCPU_ALU (
  input  Imm_Op,
  input  [15:0] A_In,
  input  Carry_In,
  input  [3:0] OpCode,
  input  ALU_En,
  input  [15:0] B_In,
  input  [3:0] Imm_Value,
  output [15:0] Out,
  output Zero,
  output Sign,
  output Carry_Out,
  output Overflow
);

  wire add_1_c_o, add_2_c_o, and_2_out, and_3_out, and_4_out, comparator_1_eq, comparator_2_lt,
       comparator_3_gt, comparator_4_gt, comparator_5_gt, comparator_6_lt, comparator_7_lt, nor_1_out,
       priorityencoder_1_any, sub_1_c_o, sub_2_c_o, xnor_1_out, xor_2_out, xor_3_out, xor_4_out;
  wire [0:0] bitselector_1_out;
  wire [3:0] multiplexer_1_out, priorityencoder_1_num, sub_3_s;
  wire [4:4] multiplexer_1_out_2;
  wire [15:0] add_1_s, add_2_s, and_1_out, barrelshifter_1_out, barrelshifter_2_out, barrelshifter_3_out,
       barrelshifter_4_out, div_1_q, div_1_r, multiplexer_2_out, neg_1_out, not_1_out, or_1_out, sub_1_s,
       sub_2_s, xor_1_out;
  wire [15:5] multiplexer_1_out_3;
  wire [31:0] mul_1_mul;

  Multiplexer #(.Bits(16)) multiplexer_1 (
    .sel(Imm_Op), .in_0(B_In), .in_1({{12{1'b0}}, Imm_Value}),
    .out({multiplexer_1_out_3, multiplexer_1_out_2[4], multiplexer_1_out}));
  PriorityEncoder #(.Selector_Bits(4)) priorityencoder_1 (
    .in0(multiplexer_1_out[0]), .in1(multiplexer_1_out[1]), .in2(multiplexer_1_out[2]),
    .in3(multiplexer_1_out[3]), .in4(multiplexer_1_out_2[4]), .in5(multiplexer_1_out_3[5]),
    .in6(multiplexer_1_out_3[6]), .in7(multiplexer_1_out_3[7]), .in8(multiplexer_1_out_3[8]),
    .in9(multiplexer_1_out_3[9]), .in10(multiplexer_1_out_3[10]), .in11(multiplexer_1_out_3[11]),
    .in12(multiplexer_1_out_3[12]), .in13(multiplexer_1_out_3[13]), .in14(multiplexer_1_out_3[14]),
    .in15(multiplexer_1_out_3[15]), .num(priorityencoder_1_num), .any(priorityencoder_1_any));
  Comparator #(.Bits(16)) comparator_1 (
    .a({16{1'b0}}), .b({multiplexer_1_out_3, multiplexer_1_out_2[4], multiplexer_1_out}), .eq(comparator_1_eq));  // open: gt, lt
  assign not_1_out = ~{multiplexer_1_out_3, multiplexer_1_out_2[4], multiplexer_1_out};  // Not not_1, 16 bits wide
  assign and_1_out = A_In & {multiplexer_1_out_3, multiplexer_1_out_2[4], multiplexer_1_out};  // And and_1, 16 bits wide
  assign or_1_out = A_In | {multiplexer_1_out_3, multiplexer_1_out_2[4], multiplexer_1_out};  // Or or_1, 16 bits wide
  assign xor_1_out = A_In ^ {multiplexer_1_out_3, multiplexer_1_out_2[4], multiplexer_1_out};  // XOr xor_1, 16 bits wide
  BarrelShifter #(.Bits(16)) barrelshifter_1 (
    .in(A_In), .shift({multiplexer_1_out_2[4], multiplexer_1_out}), .out(barrelshifter_1_out));
  BarrelShifter #(.Bits(16), .direction("right")) barrelshifter_2 (
    .in(A_In), .shift({multiplexer_1_out_2[4], multiplexer_1_out}), .out(barrelshifter_2_out));
  Neg #(.Bits(16)) neg_1 (.in({multiplexer_1_out_3, multiplexer_1_out_2[4], multiplexer_1_out}), .out(neg_1_out));
  Add #(.Bits(16)) add_1 (
    .a(A_In), .b({multiplexer_1_out_3, multiplexer_1_out_2[4], multiplexer_1_out}), .c_i(1'b0), .s(add_1_s),
    .c_o(add_1_c_o));
  Add #(.Bits(16)) add_2 (
    .a(A_In), .b({multiplexer_1_out_3, multiplexer_1_out_2[4], multiplexer_1_out}), .c_i(Carry_In),
    .s(add_2_s), .c_o(add_2_c_o));
  Sub #(.Bits(16)) sub_1 (
    .a(A_In), .b({multiplexer_1_out_3, multiplexer_1_out_2[4], multiplexer_1_out}), .c_i(1'b0), .s(sub_1_s),
    .c_o(sub_1_c_o));
  Sub #(.Bits(16)) sub_2 (
    .a(A_In), .b({multiplexer_1_out_3, multiplexer_1_out_2[4], multiplexer_1_out}), .c_i(Carry_In),
    .s(sub_2_s), .c_o(sub_2_c_o));
  Mul #(.Bits(16)) mul_1 (
    .a(A_In), .b({multiplexer_1_out_3, multiplexer_1_out_2[4], multiplexer_1_out}), .mul(mul_1_mul));
  Div #(.Bits(16)) div_1 (
    .a(A_In), .b({multiplexer_1_out_3, multiplexer_1_out_2[4], multiplexer_1_out}), .q(div_1_q), .r(div_1_r));
  xnor xnor_1 (xnor_1_out, Sign, multiplexer_1_out_3[15]);
  nor nor_1 (nor_1_out, A_In[15], multiplexer_1_out_3[15]);
  xor xor_2 (xor_2_out, A_In[15], multiplexer_1_out_3[15]);
  BitSelector #(.Selector_Bits(4)) bitselector_1 (.in(A_In), .sel(multiplexer_1_out), .out(bitselector_1_out[0]));
  xor xor_3 (xor_3_out, Sign, A_In[15]);
  Comparator #(.Bits(4)) comparator_2 (.a(4'b1101), .b(OpCode), .lt(comparator_2_lt));  // open: gt, eq
  and and_2 (and_2_out, comparator_1_eq, comparator_2_lt);
  and and_3 (and_3_out, nor_1_out, xor_3_out);
  and and_4 (and_4_out, xor_3_out, xor_2_out);
  xor xor_4 (xor_4_out, Sign, xor_2_out);
  Sub #(.Bits(4)) sub_3 (.a(4'b1111), .b(multiplexer_1_out), .c_i(1'b0), .s(sub_3_s));  // open: c_o
  Comparator #(.Bits(16)) comparator_3 (.a(mul_1_mul[31:16]), .b({16{1'b0}}), .gt(comparator_3_gt));  // open: eq, lt
  Comparator #(.Bits(16)) comparator_4 (.a(div_1_r), .b({16{1'b0}}), .gt(comparator_4_gt));  // open: eq, lt
  Comparator #(.Bits(16)) comparator_5 (.a(div_1_q), .b({16{1'b0}}), .gt(comparator_5_gt));  // open: eq, lt
  BarrelShifter #(.Bits(16), .direction("right")) barrelshifter_3 (
    .in(A_In), .shift({1'b0, sub_3_s}), .out(barrelshifter_3_out));
  BarrelShifter #(.Bits(16)) barrelshifter_4 (.in(A_In), .shift({1'b0, sub_3_s}), .out(barrelshifter_4_out));
  Multiplexer #(.Selector_Bits(4), .Bits(16)) multiplexer_2 (
    .sel(OpCode), .in_0(not_1_out), .in_1(and_1_out), .in_2(or_1_out), .in_3(xor_1_out),
    .in_4(barrelshifter_1_out), .in_5(barrelshifter_2_out), .in_6({{15{1'b0}}, bitselector_1_out[0]}),
    .in_7({{12{1'b0}}, priorityencoder_1_num}), .in_8(neg_1_out), .in_9(add_1_s), .in_10(add_2_s),
    .in_11(sub_1_s), .in_12(sub_2_s), .in_13(mul_1_mul[15:0]), .in_14(div_1_q), .in_15(div_1_r),
    .out(multiplexer_2_out));
  Comparator #(.Bits(16)) comparator_6 (.a({16{1'b0}}), .b(barrelshifter_3_out), .lt(comparator_6_lt));  // open: gt, eq
  Comparator #(.Bits(16)) comparator_7 (.a({16{1'b0}}), .b(barrelshifter_4_out), .lt(comparator_7_lt));  // open: gt, eq
  Multiplexer #(.Selector_Bits(4)) multiplexer_3 (
    .sel(OpCode), .in_0(1'b0), .in_1(1'b0), .in_2(1'b0), .in_3(1'b0), .in_4(xor_3_out), .in_5(xor_3_out),
    .in_6(1'b0), .in_7(1'b0), .in_8(xnor_1_out), .in_9(and_3_out), .in_10(and_3_out), .in_11(and_4_out),
    .in_12(and_4_out), .in_13(xor_4_out), .in_14(and_2_out), .in_15(and_2_out), .out(Overflow));
  Comparator #(.Signed("true"), .Bits(16)) comparator_8 (
    .a(multiplexer_2_out), .b({16{1'b0}}), .eq(Zero), .lt(Sign));  // open: gt
  Multiplexer #(.Selector_Bits(4)) multiplexer_4 (
    .sel(OpCode), .in_0(1'b0), .in_1(1'b0), .in_2(1'b0), .in_3(1'b0), .in_4(comparator_6_lt),
    .in_5(comparator_7_lt), .in_6(1'b0), .in_7(priorityencoder_1_any), .in_8(1'b0), .in_9(add_1_c_o),
    .in_10(add_2_c_o), .in_11(sub_1_c_o), .in_12(sub_2_c_o), .in_13(comparator_3_gt),
    .in_14(comparator_4_gt), .in_15(comparator_5_gt), .out(Carry_Out));
  assign Out = ALU_En ? multiplexer_2_out : 16'bz;  // Driver driver_1
  // Probe ALU on Out

  // Notes on the sheet:
  //   Sign
  //   Div is unsigned, so we use DIV0 instead
  //   DIV0
  //   Shift Over/Under
  //   -B
  //   Shift
  //   Add
  //   Sub
  //   Mul
endmodule
