// Digital circuit GCPU Addressing.dig as structural Verilog
module GCPU_Addressing (
  input  [1:0] State,
  input  Adder_En,
  input  [1:0] Cur_UE,
  input  LO_En,
  input  [15:0] HLB_In,
  input  Clock,
  input  PC_plus_1,
  input  PC_plus_2,
  input  [15:0] Data_In,
  input  Write_PC,
  output OOB,
  output [15:0] RAM_Addr,
  output [15:0] PC_Out
);

  wire demultiplexer_1_out_0, demultiplexer_1_out_1, demultiplexer_1_out_2, OOB_Check_gt, or_1_out;
  wire [15:0] Adder_Addr_q, Adder_s, Buffer_q, multiplexer_1_out, multiplexer_2_out, Offs_Addr_s, PC_Adder_s;

  or or_1 (or_1_out, PC_plus_2, PC_plus_1, Write_PC);
  Demultiplexer #(.Selector_Bits(2)) demultiplexer_1 (
    .sel(State), .in(Adder_En), .out_0(demultiplexer_1_out_0), .out_1(demultiplexer_1_out_1),
    .out_2(demultiplexer_1_out_2));  // open: out_3
  Add #(.Bits(16)) PC_Adder (.a(PC_Out), .b(16'h1), .c_i(PC_plus_2), .s(PC_Adder_s));  // open: c_o
  Register #(.Bits(16)) Buffer (.D(Data_In), .C(Clock), .en(demultiplexer_1_out_0), .Q(Buffer_q));
  Multiplexer #(.Bits(16)) multiplexer_1 (.sel(Write_PC), .in_0(PC_Adder_s), .in_1(Data_In), .out(multiplexer_1_out));
  Add #(.Bits(16)) Adder (.a(Buffer_q), .b(Data_In), .c_i(1'b0), .s(Adder_s));  // open: c_o
  Register #(.Bits(16), .isProgramCounter("true")) PC (.D(multiplexer_1_out), .C(Clock), .en(or_1_out), .Q(PC_Out));
  Register #(.Bits(16)) Adder_Addr (.D(Adder_s), .C(Clock), .en(demultiplexer_1_out_1), .Q(Adder_Addr_q));
  Multiplexer #(.Bits(16)) multiplexer_2 (
    .sel(demultiplexer_1_out_2), .in_0(PC_Out), .in_1(Adder_Addr_q), .out(multiplexer_2_out));
  Add #(.Bits(16)) Offs_Addr (
    .a({HLB_In[7:0], {8{1'b0}}}), .b(multiplexer_2_out), .c_i(1'b0), .s(Offs_Addr_s));  // open: c_o
  Comparator #(.Bits(16)) OOB_Check (
    .a(multiplexer_2_out), .b({HLB_In[15:8], {8{1'b0}}}), .gt(OOB_Check_gt));  // open: eq, lt
  Multiplexer #(.Bits(16)) multiplexer_3 (.sel(LO_En), .in_0(multiplexer_2_out), .in_1(Offs_Addr_s), .out(RAM_Addr));
  and and_1 (OOB, Cur_UE[1], OOB_Check_gt);
  // Probe RAM Address on RAM_Addr

  // Notes on the sheet:
  //   HLB > 0xLO00 + 0xHI00
endmodule
