// Digital circuit GCPU CISC Decoder.dig as structural Verilog
module GCPU_CISC_Decoder (
  input  Start,
  input  Pause,
  input  EX,
  input  [1:0] UE,
  input  Non_Ignorable_EX,
  input  [15:0] RAM_Input,
  input  Clock_In,
  input  [7:0] Jump_Cnds,
  input  HLT,
  input  Reset_State,
  input  Hard_Reset,
  output Non_Ign,
  output [3:0] RISC_Out,
  output Any,
  output STR,
  output [3:0] Op1,
  output [3:0] Op0,
  output [3:0] Mod,
  output [2:0] ALU_Type,
  output Clock_Output,
  output [1:0] State,
  output Is_On
);

  wire and_1_out, and_2_out, and_4_out, and_5_out, and_7_out, and_8_out, and_9_out, and_10_out, and_11_out,
       decoder_1_out_0, decoder_1_out_1, decoder_1_out_2, delay_1_out, delay_2_out, delay_3_out, delay_6_out,
       demultiplexer_1_out_0, demultiplexer_1_out_1, demultiplexer_2_out_0, demultiplexer_2_out_1,
       demultiplexer_3_out_0, demultiplexer_3_out_1, demultiplexer_3_out_2, demultiplexer_3_out_3,
       demultiplexer_3_out_4, demultiplexer_3_out_5, demultiplexer_3_out_6, demultiplexer_4_out_0,
       demultiplexer_4_out_1, demultiplexer_5_out_0, demultiplexer_5_out_1, demultiplexer_6_out_0,
       demultiplexer_6_out_1, demultiplexer_7_out_0, demultiplexer_7_out_1, demultiplexer_8_out_0,
       demultiplexer_8_out_1, demultiplexer_9_out_0, demultiplexer_9_out_1, EX_q, multiplexer_2_out,
       not_1_out, not_2_out, ON_Buff_nq, ON_Buff_q, or_1_out, or_2_out, or_3_out, or_4_out, or_5_out,
       or_6_out, priorityencoder_1_any, xor_1_out;
  wire [1:0] State_out;
  wire [15:0] Fetch_q, multiplexer_1_out;
  wire [15:15] delay_4_out;

  or or_1 (or_1_out, Pause, Hard_Reset, and_2_out);
  Delay #(.delayTime(3)) delay_1 (.in(HLT), .out(delay_1_out));
  and and_1 (and_1_out, delay_1_out, HLT);
  RS_FF_AS ON_Buff (.S(Start), .R(or_1_out), .Q(ON_Buff_q), .nQ(ON_Buff_nq));
  and and_2 (and_2_out, and_1_out, Is_On, ~Clock_In);  // And
  or or_2 (or_2_out, ON_Buff_nq, Hard_Reset);
  Delay delay_2 (.in(decoder_1_out_0), .out(delay_2_out));
  or or_3 (or_3_out, Reset_State, Hard_Reset);
  RS_FF ON (.S(ON_Buff_q), .C(~Clock_In), .R(or_2_out), .Q(Is_On));  // open: nQ
  Register #(.Bits(16)) Fetch (.D(RAM_Input), .C(Clock_In), .en(delay_2_out), .Q(Fetch_q));
  Multiplexer #(.Bits(16)) multiplexer_1 (.sel(not_1_out), .in_0(RAM_Input), .in_1(Fetch_q), .out(multiplexer_1_out));
  Counter #(.Bits(2)) u_State (.en(delay_3_out), .C(Clock_Output), .clr(or_3_out), .out(State_out));  // open: ovf
  Delay #(.delayTime(2)) delay_3 (.in(Is_On), .out(delay_3_out));
  and and_3 (Clock_Output, Clock_In, Is_On);
  Delay #(.Bits(16), .delayTime(2)) delay_4 (.in(multiplexer_1_out), .out({delay_4_out[15], ALU_Type, Mod, Op0, Op1}));
  Delay #(.Bits(2), .delayTime(2)) delay_5 (.in(State_out), .out(State));
  Decoder #(.Selector_Bits(2)) decoder_1 (
    .sel(State), .out_0(decoder_1_out_0), .out_1(decoder_1_out_1), .out_2(decoder_1_out_2));  // open: out_3
  Delay #(.delayTime(4)) delay_6 (.in(Clock_Output), .out(delay_6_out));
  not not_1 (not_1_out, decoder_1_out_0);
  and and_4 (and_4_out, Is_On, ~EX_q);  // And
  Register u_EX (.D(EX), .C(delay_6_out), .en(decoder_1_out_0), .Q(EX_q));
  Multiplexer #(.Selector_Bits(3)) multiplexer_2 (
    .sel(Mod[2:0]), .in_0(Jump_Cnds[0]), .in_1(Jump_Cnds[1]), .in_2(Jump_Cnds[2]), .in_3(Jump_Cnds[3]),
    .in_4(Jump_Cnds[4]), .in_5(Jump_Cnds[5]), .in_6(Jump_Cnds[6]), .in_7(Jump_Cnds[7]),
    .out(multiplexer_2_out));
  and and_5 (and_5_out, Is_On, EX_q);
  and and_6 (Non_Ign, ~EX_q, Non_Ignorable_EX);  // And
  xor xor_1 (xor_1_out, multiplexer_2_out, Mod[3]);
  Demultiplexer demultiplexer_1 (
    .sel(delay_4_out[15]), .in(and_4_out), .out_0(demultiplexer_1_out_0), .out_1(demultiplexer_1_out_1));
  Demultiplexer demultiplexer_2 (
    .sel(decoder_1_out_1), .in(and_5_out), .out_0(demultiplexer_2_out_0), .out_1(demultiplexer_2_out_1));
  Demultiplexer #(.Selector_Bits(3)) demultiplexer_3 (
    .sel(ALU_Type), .in(demultiplexer_1_out_0), .out_0(demultiplexer_3_out_0), .out_1(demultiplexer_3_out_1),
    .out_2(demultiplexer_3_out_2), .out_3(demultiplexer_3_out_3), .out_4(demultiplexer_3_out_4),
    .out_5(demultiplexer_3_out_5), .out_6(demultiplexer_3_out_6), .out_7(STR));
  Demultiplexer demultiplexer_4 (
    .sel(UE[1]), .in(demultiplexer_3_out_0), .out_0(demultiplexer_4_out_0), .out_1(demultiplexer_4_out_1));
  Demultiplexer demultiplexer_5 (
    .sel(UE[1]), .in(demultiplexer_3_out_1), .out_0(demultiplexer_5_out_0), .out_1(demultiplexer_5_out_1));
  not not_2 (not_2_out, decoder_1_out_2);
  or or_4 (or_4_out, demultiplexer_3_out_6, STR);
  or or_5 (or_5_out, demultiplexer_4_out_1, demultiplexer_5_out_1);
  and and_7 (and_7_out, not_2_out, demultiplexer_3_out_4);
  and and_8 (and_8_out, not_2_out, demultiplexer_3_out_5);
  and and_9 (and_9_out, not_2_out, or_4_out);
  Demultiplexer demultiplexer_6 (
    .sel(xor_1_out), .in(demultiplexer_7_out_0), .out_0(demultiplexer_6_out_0), .out_1(demultiplexer_6_out_1));
  Demultiplexer demultiplexer_7 (
    .sel(decoder_1_out_1), .in(and_7_out), .out_0(demultiplexer_7_out_0), .out_1(demultiplexer_7_out_1));
  Demultiplexer demultiplexer_8 (
    .sel(decoder_1_out_1), .in(and_8_out), .out_0(demultiplexer_8_out_0), .out_1(demultiplexer_8_out_1));
  Demultiplexer demultiplexer_9 (
    .sel(decoder_1_out_1), .in(and_9_out), .out_0(demultiplexer_9_out_0), .out_1(demultiplexer_9_out_1));
  and and_10 (and_10_out, demultiplexer_3_out_6, decoder_1_out_2);
  and and_11 (and_11_out, decoder_1_out_2, STR);
  or or_6 (or_6_out, demultiplexer_6_out_1, demultiplexer_8_out_0);
  PriorityEncoder #(.Selector_Bits(4)) priorityencoder_1 (
    .in0(demultiplexer_4_out_0), .in1(demultiplexer_5_out_0), .in2(demultiplexer_3_out_2),
    .in3(demultiplexer_3_out_3), .in4(demultiplexer_6_out_0), .in5(or_6_out), .in6(demultiplexer_7_out_1),
    .in7(demultiplexer_8_out_1), .in8(demultiplexer_9_out_0), .in9(demultiplexer_9_out_1), .in10(and_10_out),
    .in11(and_11_out), .in12(demultiplexer_1_out_1), .in13(demultiplexer_2_out_0),
    .in14(demultiplexer_2_out_1), .in15(or_5_out), .num(RISC_Out), .any(priorityencoder_1_any));
  and and_12 (Any, priorityencoder_1_any, Is_On);
  // Probe RISC Code on RISC_Out

  // Notes on the sheet:
  //   Start: Signal from outside the CPU telling it to start/resume
  //   Pause: Signal from outside the CPU telling it to pause.
  //   Non_Ign: Do not read or write anything.
  //   Any: If any instruction are attempting to execute.
  //   STR: The STR instruction is currently executing.
  //   HLT: Only on if a HLT instruction is properly executing.
  //   ALU_Type: If it is an ALU instruction, this is which type of ALU instruction it is.
  //   Hard_Reset: Despite the lack of a reset pin on Digital's registers, this should theoretically reset a critical number of components to restart the CPU.
  //   No writing
endmodule
