// Digital circuit GCPU Flags.dig as structural Verilog
module GCPU_Flags (
  input  UE_Push,
  input  UE_Pop,
  input  [15:0] Input,
  input  [3:0] ALU_Flags,
  input  W_ALUF,
  input  Write_All,
  input  Set_LOEn,
  input  Reset_LOEn,
  input  Clr_EXC_Buff,
  input  [7:0] Ex_Lines,
  input  Clock,
  output [1:0] Cur_UE,
  output [4:0] IOP,
  output [3:0] ALUF,
  output LOEn,
  output Non_Ign,
  output Exception,
  output [15:0] Output
);

  wire and_2_out, or_2_out, or_3_out, or_4_out;
  wire [1:0] multiplexer_1_out, multiplexer_2_out, multiplexer_3_out, multiplexer_4_out;
  wire [2:0] EXC_q, multiplexer_5_out, priorityencoder_1_num;
  wire [3:0] multiplexer_6_out;
  wire [3:2] UEp_q;
  wire [7:0] and_1_out, EXC_Buffer_q, or_1_out, pulldown_1_out;
  wire [15:0] and_3_out;

  assign and_1_out = Ex_Lines & {4'b1111, {4{Cur_UE[0]}}};  // And and_1, 8 bits wide
  assign or_1_out = and_1_out | EXC_Buffer_q;  // Or or_1, 8 bits wide
  or or_2 (or_2_out, UE_Pop, and_2_out, UE_Push);
  Multiplexer #(.Bits(2)) multiplexer_1 (.sel(UE_Push), .in_0(2'b00), .in_1(Cur_UE), .out(multiplexer_1_out));
  and and_2 (and_2_out, Write_All, ~Cur_UE[1]);  // And
  PullDown #(.Bits(8)) pulldown_1 (.out(pulldown_1_out));
  assign pulldown_1_out = ~Clr_EXC_Buff ? or_1_out : 8'bz;  // DriverInvSel driverinvsel_1
  Multiplexer #(.Bits(2)) multiplexer_2 (
    .sel(and_2_out), .in_0(multiplexer_1_out), .in_1(Input[3:2]), .out(multiplexer_2_out));
  RS_FF u_LOEn (.S(Set_LOEn), .C(Clock), .R(Reset_LOEn), .Q(LOEn));  // open: nQ
  Register #(.Bits(8)) EXC_Buffer (.D(pulldown_1_out), .C(~Clock), .en(1'b1), .Q(EXC_Buffer_q));
  Register #(.Bits(2)) UEp (.D(multiplexer_2_out), .C(Clock), .en(or_2_out), .Q(UEp_q));
  PriorityEncoder #(.Selector_Bits(3)) priorityencoder_1 (
    .in0(EXC_Buffer_q[0]), .in1(EXC_Buffer_q[1]), .in2(EXC_Buffer_q[2]), .in3(EXC_Buffer_q[3]),
    .in4(EXC_Buffer_q[4]), .in5(EXC_Buffer_q[5]), .in6(EXC_Buffer_q[6]), .in7(EXC_Buffer_q[7]),
    .num(priorityencoder_1_num), .any(Exception));
  Comparator #(.Bits(8)) comparator_1 (.a(EXC_Buffer_q), .b(8'h3f), .gt(Non_Ign));  // open: eq, lt
  Multiplexer #(.Bits(2)) multiplexer_3 (.sel(UE_Push), .in_0(UEp_q), .in_1(2'b00), .out(multiplexer_3_out));
  or or_3 (or_3_out, Write_All, W_ALUF);
  Multiplexer #(.Bits(2)) multiplexer_4 (
    .sel(and_2_out), .in_0(multiplexer_3_out), .in_1(Input[1:0]), .out(multiplexer_4_out));
  Multiplexer #(.Bits(3)) multiplexer_5 (
    .sel(and_2_out), .in_0(priorityencoder_1_num), .in_1(Input[10:8]), .out(multiplexer_5_out));
  or or_4 (or_4_out, and_2_out, Exception);
  Multiplexer #(.Bits(4)) multiplexer_6 (.sel(W_ALUF), .in_0(Input[7:4]), .in_1(ALU_Flags), .out(multiplexer_6_out));
  Register #(.Bits(2)) UEc (.D(multiplexer_4_out), .C(Clock), .en(or_2_out), .Q(Cur_UE));
  Register #(.Bits(4)) u_ALUF (.D(multiplexer_6_out), .C(Clock), .en(or_3_out), .Q(ALUF));
  Register #(.Bits(5)) u_IOP (.D(Input[15:11]), .C(Clock), .en(Write_All), .Q(IOP));
  Register #(.Bits(3)) EXC (.D(multiplexer_5_out), .C(Clock), .en(or_4_out), .Q(EXC_q));
  // Probe FLG on {IOP, EXC_q, ALUF, UEp_q, Cur_UE}
  assign and_3_out = {IOP, EXC_q, ALUF, UEp_q, Cur_UE} & 16'hf8f0;  // And and_3, 16 bits wide
  Multiplexer #(.Bits(16)) multiplexer_7 (
    .sel(Cur_UE[1]), .in_0({IOP, EXC_q, ALUF, UEp_q, Cur_UE}), .in_1(and_3_out), .out(Output));

  // Notes on the sheet:
  //   UE_Push: Set UEp to UEc and set UEc to 00
  //   UE_Pop: Set UEc to the value in UEp and set UEp to 00
  //   Input: Flags input from the selector
  //   0-1: UEc
  //   2-3: UEp
  //   4-7: ALUF
  //   8-10: EXC
  //   11-15: IOP
  //   Cur_UE: Current IsUser/InterruptsEnabled flags.
  //   ALU_Flags: The output flags of the ALU are sent to here.
  //   W_ALUF: Write the ALU flags to ALUF.
  //   Write_All: Write "Input" to all of the flags.
  //   IOP: The IO device number currently selected
  //   ALUF: The previous ALU operation's flags.
  //   LOEn: Whether or not LO is used as an address offset.
  //   Non_Ign: A non-ignorable exception is currently happening
  //   Exception: An exception is happening
  //   Write
endmodule
