// Digital circuit GCPU RISC Controller.dig as structural Verilog
module GCPU_RISC_Controller (
  input  Non_Ign,
  input  [3:0] RISC_Code,
  input  Any,
  input  STR,
  input  [3:0] Op1,
  input  [3:0] Op0,
  input  [3:0] Mod,
  input  [2:0] ALU_Type,
  input  Hard_Reset,
  output PC_plus_1,
  output PC_plus_2,
  output RAM_to_Bus,
  output Read0_to_RAM,
  output Read1_to_Bus,
  output To_Process,
  output To_Kernel,
  output ALU_Enable,
  output ALU_Flag_Write,
  output ALU_Immediate,
  output [3:0] ALU_OpCode,
  output [3:0] Write,
  output Write_2,
  output [3:0] Read0,
  output Read0_2,
  output [3:0] Read1,
  output Read1_2,
  output SYS,
  output PRIN,
  output Adder_Enable,
  output HLT,
  output Reset_State
);

  wire and_1_out, and_4_out, and_5_out, and_6_out, and_9_out, comparator_1_eq, or_2_out,
       priorityencoder_1_any, priorityencoder_2_any;
  wire [1:0] priorityencoder_1_num, priorityencoder_2_num;
  wire [9:0] RISC_Decoder_d;

  and and_1 (and_1_out, Any, ~Hard_Reset);  // And
  ROM #(.AddrBits(4), .Bits(18)) RISC_Decoder (
    .A(RISC_Code), .sel(and_1_out),
    .D({Reset_State, PC_plus_1, PC_plus_2, HLT, SYS, ALU_Enable, Adder_Enable, PRIN, RISC_Decoder_d[9:5], Read0_to_RAM, Read1_to_Bus, RAM_to_Bus, To_Process, RISC_Decoder_d[0]}));
  PullDown #(.Bits(18)) pulldown_1 (.out({Reset_State, PC_plus_1, PC_plus_2, HLT, SYS, ALU_Enable, Adder_Enable, PRIN, RISC_Decoder_d[9:5], Read0_to_RAM, Read1_to_Bus, RAM_to_Bus, To_Process, RISC_Decoder_d[0]}));
  or or_1 (To_Kernel, RISC_Decoder_d[0], Hard_Reset);
  or or_2 (or_2_out, RISC_Decoder_d[6], Hard_Reset);
  PriorityEncoder #(.Selector_Bits(2)) priorityencoder_1 (
    .in0(RISC_Decoder_d[8]), .in1(RISC_Decoder_d[5]), .in2(To_Process), .in3(RISC_Decoder_d[0]),
    .num(priorityencoder_1_num), .any(priorityencoder_1_any));
  PriorityEncoder #(.Selector_Bits(2)) priorityencoder_2 (
    .in0(RISC_Decoder_d[7]), .in1(or_2_out), .in2(RISC_Decoder_d[5]), .in3(1'b0),
    .num(priorityencoder_2_num), .any(priorityencoder_2_any));
  Comparator #(.Bits(4)) comparator_1 (.a(Op0), .b(Op1), .eq(comparator_1_eq));  // open: gt, lt
  Multiplexer #(.Selector_Bits(2), .Bits(4)) multiplexer_1 (
    .sel(priorityencoder_1_num), .in_0(Op1), .in_1(4'b1000), .in_2(4'b1110), .in_3(4'b1111), .out(Read1));
  Multiplexer #(.Selector_Bits(2), .Bits(4)) multiplexer_2 (
    .sel(priorityencoder_2_num), .in_0(Op0), .in_1(4'b1000), .in_2(4'b1110), .in_3(4'b0000), .out(Write));
  and and_2 (ALU_Flag_Write, ALU_Enable, ~ALU_Type[1]);  // And
  and and_3 (ALU_Immediate, ALU_Enable, ALU_Type[0]);
  and and_4 (and_4_out, ALU_Type[1], ALU_Enable, ALU_Type[2]);
  and and_5 (and_5_out, STR, Adder_Enable, comparator_1_eq);
  and and_6 (and_6_out, ALU_Enable, ALU_Type[2]);
  and and_7 (Read0_2, ~Non_Ign, ~and_4_out, RISC_Decoder_d[9]);  // And
  and and_8 (Read1_2, ~ALU_Immediate, ~Non_Ign, ~and_4_out, priorityencoder_1_any, ~and_5_out);  // And
  and and_9 (and_9_out, ~and_6_out, ~Non_Ign, priorityencoder_2_any);  // And
  or or_3 (Write_2, and_9_out, Hard_Reset);

  assign ALU_OpCode = Mod;
  assign Read0 = Op0;

  // Notes on the sheet:
  //   Hard_Reset: Clears enough values in the CPU to effectively reset it.
  //   The small MUX inputs are:
  //   8 - PC
  //   E - EPC
  //   F - EXA
  //   contents of RISC_Decoder (hex, n*v repeats v):
  //   34000,2004a,32000,30188,28000,10000,20044,30084,10908,10804,20884
  //   ,20a10,31380,28,20049,30400
  //   ALF
  //   ALI
  //   NOP
  //   Direct
  //   STR
  //   ALN
  //   OR
  //   reset
endmodule
