// Digital circuit Glass CPU.dig as structural Verilog
module Glass_CPU (
  input  Start,
  input  Pause,
  input  Clock_In,
  input  [15:0] RAM_Input,
  input  [15:0] I_O_In,
  input  I_O_Reading,
  input  I_O_Writing,
  input  [3:0] Int_Lines,
  input  [3:0] Interrupt_Mask,
  input  Hard_Reset,
  output [15:0] RAM_Addr,
  output [15:0] RAM_Output,
  output RAM_Write,
  output [15:0] PC,
  output [4:0] IOP,
  output [15:0] HLB,
  output Clock_Out,
  output Is_Running,
  output Is_Kernel,
  output Reading_I_O,
  output [15:0] I_O_Out,
  output Writing_I_O
);

  wire and_1_out, and_2_out, and_4_out, delay_1_out, delay_2_out, delay_6_out, delay_7_out,
       gcpu_cisc_decoder_1_any, gcpu_cisc_decoder_1_clock_output, gcpu_cisc_decoder_1_non_ign,
       gcpu_cisc_decoder_1_str, gcpu_flags_1_exception, gcpu_flags_1_loen, gcpu_flags_1_non_ign,
       gcpu_risc_controller_1_adder_enable, gcpu_risc_controller_1_alu_enable,
       gcpu_risc_controller_1_alu_flag_write, gcpu_risc_controller_1_alu_immediate,
       gcpu_risc_controller_1_hlt, gcpu_risc_controller_1_pc_plus_1, gcpu_risc_controller_1_pc_plus_2,
       gcpu_risc_controller_1_prin, gcpu_risc_controller_1_ram_to_bus, gcpu_risc_controller_1_read0_2,
       gcpu_risc_controller_1_read1_2, gcpu_risc_controller_1_read1_to_bus,
       gcpu_risc_controller_1_reset_state, gcpu_risc_controller_1_to_kernel,
       gcpu_risc_controller_1_to_process, gcpu_risc_controller_1_write_2, gcpu_selection___registers_1_pror,
       gcpu_selection___registers_1_read_i_o, gcpu_selection___registers_1_write_flg,
       gcpu_selection___registers_1_write_io, gcpu_selection___registers_1_write_pc, or_1_out;
  wire [1:0] gcpu_cisc_decoder_1_state, gcpu_flags_1_cur_ue;
  wire [2:0] gcpu_cisc_decoder_1_alu_type;
  wire [3:0] and_3_out, gcpu_alu_1_zero, gcpu_cisc_decoder_1_mod, gcpu_cisc_decoder_1_op0,
       gcpu_cisc_decoder_1_op1, gcpu_cisc_decoder_1_risc_out, gcpu_risc_controller_1_alu_opcode,
       gcpu_risc_controller_1_read0, gcpu_risc_controller_1_read1, gcpu_risc_controller_1_write, pullup_1_out;
  wire [7:0] gcpu_flags_1_aluf;
  wire [7:4] or_2_out;
  wire [15:0] delay_3_out, delay_4_out, delay_5_out, gcpu_flags_1_output, gcpu_selection___registers_1_out0,
       gcpu_selection___registers_1_out1;

  Delay #(.delayTime(2)) delay_1 (.in(Start), .out(delay_1_out));
  Delay #(.delayTime(2)) delay_2 (.in(Pause), .out(delay_2_out));
  and and_1 (and_1_out, ~delay_1_out, Start);  // And
  and and_2 (and_2_out, ~delay_2_out, Pause);  // And
  PRNG prng_1 (.S(1'b0), .se(1'b0), .ne(1'b1), .C(Clock_In), .R(gcpu_flags_1_aluf[7]));
  // Probe IO on I_O_In
  PullUp #(.Bits(4)) pullup_1 (.out(pullup_1_out));
  assign pullup_1_out = ~gcpu_flags_1_cur_ue[0] ? Interrupt_Mask : 4'bz;  // DriverInvSel driverinvsel_1
  assign and_3_out = pullup_1_out & Int_Lines;  // And and_3, 4 bits wide
  GCPU_CISC_Decoder gcpu_cisc_decoder_1 (
    .Start(and_1_out), .Pause(and_2_out), .EX(gcpu_flags_1_exception), .UE(gcpu_flags_1_cur_ue),
    .Non_Ignorable_EX(gcpu_flags_1_non_ign), .RAM_Input(RAM_Input), .Clock_In(Clock_In),
    .Jump_Cnds({gcpu_flags_1_aluf[7], 1'b1, I_O_Writing, I_O_Reading, gcpu_flags_1_aluf[3:0]}),
    .HLT(gcpu_risc_controller_1_hlt), .Reset_State(gcpu_risc_controller_1_reset_state),
    .Hard_Reset(Hard_Reset), .Non_Ign(gcpu_cisc_decoder_1_non_ign), .RISC_Out(gcpu_cisc_decoder_1_risc_out),
    .Any(gcpu_cisc_decoder_1_any), .STR(gcpu_cisc_decoder_1_str), .Op1(gcpu_cisc_decoder_1_op1),
    .Op0(gcpu_cisc_decoder_1_op0), .Mod(gcpu_cisc_decoder_1_mod), .ALU_Type(gcpu_cisc_decoder_1_alu_type),
    .Clock_Output(gcpu_cisc_decoder_1_clock_output), .State(gcpu_cisc_decoder_1_state), .Is_On(Is_Running));
  GCPU_RISC_Controller gcpu_risc_controller_1 (
    .Non_Ign(gcpu_cisc_decoder_1_non_ign), .RISC_Code(gcpu_cisc_decoder_1_risc_out),
    .Any(gcpu_cisc_decoder_1_any), .STR(gcpu_cisc_decoder_1_str), .Op1(gcpu_cisc_decoder_1_op1),
    .Op0(gcpu_cisc_decoder_1_op0), .Mod(gcpu_cisc_decoder_1_mod), .ALU_Type(gcpu_cisc_decoder_1_alu_type),
    .Hard_Reset(Hard_Reset), .PC_plus_1(gcpu_risc_controller_1_pc_plus_1),
    .PC_plus_2(gcpu_risc_controller_1_pc_plus_2), .RAM_to_Bus(gcpu_risc_controller_1_ram_to_bus),
    .Read0_to_RAM(RAM_Write), .Read1_to_Bus(gcpu_risc_controller_1_read1_to_bus),
    .To_Process(gcpu_risc_controller_1_to_process), .To_Kernel(gcpu_risc_controller_1_to_kernel),
    .ALU_Enable(gcpu_risc_controller_1_alu_enable), .ALU_Flag_Write(gcpu_risc_controller_1_alu_flag_write),
    .ALU_Immediate(gcpu_risc_controller_1_alu_immediate), .ALU_OpCode(gcpu_risc_controller_1_alu_opcode),
    .Write(gcpu_risc_controller_1_write), .Write_2(gcpu_risc_controller_1_write_2),
    .Read0(gcpu_risc_controller_1_read0), .Read0_2(gcpu_risc_controller_1_read0_2),
    .Read1(gcpu_risc_controller_1_read1), .Read1_2(gcpu_risc_controller_1_read1_2), .SYS(or_2_out[5]),
    .PRIN(gcpu_risc_controller_1_prin), .Adder_Enable(gcpu_risc_controller_1_adder_enable),
    .HLT(gcpu_risc_controller_1_hlt), .Reset_State(gcpu_risc_controller_1_reset_state));
  and and_4 (and_4_out, Hard_Reset, Clock_In);
  Delay #(.Bits(16), .delayTime(2)) delay_3 (.in(RAM_Input), .out(delay_3_out));
  or or_1 (or_1_out, gcpu_cisc_decoder_1_clock_output, and_4_out);
  or or_2 (or_2_out[6], gcpu_risc_controller_1_prin, gcpu_selection___registers_1_pror);
  assign RAM_Output = gcpu_risc_controller_1_ram_to_bus ? delay_3_out : 16'bz;  // Driver driver_1
  PullDown #(.Bits(16)) pulldown_1 (.out(RAM_Output));
  // Probe Data Bus on RAM_Output
  GCPU_Flags gcpu_flags_1 (
    .UE_Push(gcpu_risc_controller_1_to_kernel), .UE_Pop(gcpu_risc_controller_1_to_process),
    .Input(RAM_Output), .ALU_Flags(gcpu_alu_1_zero), .W_ALUF(gcpu_risc_controller_1_alu_flag_write),
    .Write_All(gcpu_selection___registers_1_write_flg), .Set_LOEn(gcpu_risc_controller_1_to_process),
    .Reset_LOEn(gcpu_risc_controller_1_to_kernel), .Clr_EXC_Buff(gcpu_risc_controller_1_to_kernel),
    .Ex_Lines({or_2_out, and_3_out}), .Clock(or_1_out), .Cur_UE(gcpu_flags_1_cur_ue), .IOP(IOP),
    .ALUF(gcpu_flags_1_aluf[3:0]), .LOEn(gcpu_flags_1_loen), .Non_Ign(gcpu_flags_1_non_ign),
    .Exception(gcpu_flags_1_exception), .Output(gcpu_flags_1_output));
  GCPU_Addressing gcpu_addressing_1 (
    .State(gcpu_cisc_decoder_1_state), .Adder_En(gcpu_risc_controller_1_adder_enable),
    .Cur_UE(gcpu_flags_1_cur_ue), .LO_En(gcpu_flags_1_loen), .HLB_In(HLB), .Clock(or_1_out),
    .PC_plus_1(gcpu_risc_controller_1_pc_plus_1), .PC_plus_2(gcpu_risc_controller_1_pc_plus_2),
    .Data_In(RAM_Output), .Write_PC(gcpu_selection___registers_1_write_pc), .OOB(or_2_out[7]),
    .RAM_Addr(RAM_Addr), .PC_Out(PC));
  GCPU_Selection___Registers gcpu_selection___registers_1 (
    .Data_In(RAM_Output), .Clock(or_1_out), .Cur_UE(gcpu_flags_1_cur_ue), .PC_In(PC), .IO_In(I_O_In),
    .FLG_In(gcpu_flags_1_output), .Write(gcpu_risc_controller_1_write),
    .Write_2(gcpu_risc_controller_1_write_2), .Read0(gcpu_risc_controller_1_read0),
    .Read0_2(gcpu_risc_controller_1_read0_2), .Read1(gcpu_risc_controller_1_read1),
    .Read1_2(gcpu_risc_controller_1_read1_2), .CTDZ(or_2_out[4]),
    .Write_PC(gcpu_selection___registers_1_write_pc), .Write_FLG(gcpu_selection___registers_1_write_flg),
    .Out0(gcpu_selection___registers_1_out0), .Out1(gcpu_selection___registers_1_out1),
    .PROR(gcpu_selection___registers_1_pror), .HLB(HLB), .Read_I_O(gcpu_selection___registers_1_read_i_o),
    .Write_IO(gcpu_selection___registers_1_write_io));
  GCPU_ALU gcpu_alu_1 (
    .Imm_Op(gcpu_risc_controller_1_alu_immediate), .A_In(delay_4_out), .Carry_In(gcpu_flags_1_aluf[2]),
    .OpCode(gcpu_risc_controller_1_alu_opcode), .ALU_En(gcpu_risc_controller_1_alu_enable),
    .B_In(delay_5_out), .Imm_Value(gcpu_risc_controller_1_read1), .Out(RAM_Output),
    .Zero(gcpu_alu_1_zero[0]), .Sign(gcpu_alu_1_zero[1]), .Carry_Out(gcpu_alu_1_zero[2]),
    .Overflow(gcpu_alu_1_zero[3]));
  Delay #(.Bits(16)) delay_4 (.in(gcpu_selection___registers_1_out0), .out(delay_4_out));
  Delay #(.Bits(16)) delay_5 (.in(gcpu_selection___registers_1_out1), .out(delay_5_out));
  and and_5 (Clock_Out, or_1_out, Is_Running);
  Delay #(.delayTime(6)) delay_6 (.in(gcpu_selection___registers_1_read_i_o), .out(delay_6_out));
  Delay #(.delayTime(6)) delay_7 (.in(gcpu_selection___registers_1_write_io), .out(delay_7_out));
  not not_1 (Is_Kernel, gcpu_flags_1_cur_ue[1]);
  assign RAM_Output = RAM_Write ? delay_4_out : 16'bz;  // Driver driver_2
  and and_6 (Reading_I_O, gcpu_selection___registers_1_read_i_o, delay_6_out);
  and and_7 (Writing_I_O, gcpu_selection___registers_1_write_io, delay_7_out);
  assign RAM_Output = gcpu_risc_controller_1_read1_to_bus ? delay_5_out : 16'bz;  // Driver driver_3
  assign I_O_Out = Writing_I_O ? RAM_Output : 16'bz;  // Driver driver_4

  // Notes on the sheet:
  //   Start: Starts/Resumes the execution of program memory.
  //   Only starts/resumes on rising edge (so if Start is held high the CPU can still halt)
  //   Pause: Pauses the execution of program memory.
  //   Only pauses on rising edge.
  //   RAM_Addr: The current memory address.
  //   RAM_Output: Data output to RAM
  //   RAM_Input: RAM data input
  //   I_O_In: The Input portion of I/O
  //   I_O_Reading: Should be high if the I/O wants to read from the CPU.
  //   Is a jump condition (PIR/PNR)
  //   RAM_Write: On if writing to RAM.
  //   I_O_Writing: Should be high if the I/O wants to write to the CPU.
  //   Is a jump condition (PIW/PNW).
  //   PC: The current value of the program counter.
  //   IOP: The currently selected I/O device.
  //   Note: I/O must be multiplexed according to this signal *outside* the CPU.
  //   HLB: The contents of the HI/LOW Bounds register.
  //   Clock_Out: The status of the internal clock wire.
  //   Is_Running: Only on if the CPU is currently executing program memory.
  //   Is_Kernel: On if the current process is kernel.
  //   I/O devices can choose whether they respond to non-kernel processes.
  //   Reading_I_O: On if the CPU is currently reading from Input.
  //   I_O_Out: The Output portion of I/O
  //   Writing_I_O: On if the CPU is currently writing to output.
  //   Interrupt_Mask: Each bit corresponds to one interrupt line.
  //   If the bit is on, then that interrupt is non-maskable.
  //   Hard_Reset: Effectively resets the CPU.
  //   Only clears the state counter, PC, and parts of FLG.
  //   It must be held down for at least 2 full clock cycles to work.
  //   Jump conditions
  //   Interrupt Masking
  //   Exception Lines
  //   I/O Signal Corrections
endmodule
