// Digital circuit Telescope Testspace.dig as structural Verilog
module Telescope_Testspace (
  input  clk,
  input  clk_2
);

  wire button_1_out, button_2_out, button_3_out, button_4_out, button_5_out, button_6_out,
       telescope_computing_system_1_os_running, telescope_computing_system_2_os_running;
  wire [15:0] Drive_0_d, Keyboard_0_d, register_1_q, telescope_computing_system_1_gpo_0,
       telescope_computing_system_1_os_adr, telescope_computing_system_1_status_code,
       telescope_computing_system_1_tk0_out, telescope_computing_system_2_os_adr,
       telescope_computing_system_2_status_code, TelescopeTest_d, TestServe_d;
  wire [16:16] Keyboard_0_av;
  wire [18:0] telescope_computing_system_1_tnet_o_0, telescope_computing_system_2_tnet_o_0;
  wire [18:16] telescope_computing_system_1_gpo_0_2, telescope_computing_system_1_tk0_out_2;
  wire [33:0] telescope_computing_system_1_d0_out;

  // Probe Status on telescope_computing_system_1_status_code
  Keyboard Keyboard_0 (
    .C(telescope_computing_system_1_tk0_out_2[18]), .en(telescope_computing_system_1_tk0_out_2[16]),
    .D(Keyboard_0_d), .av(Keyboard_0_av[16]));
  Terminal terminal_1 (
    .D(telescope_computing_system_1_tk0_out), .C(telescope_computing_system_1_tk0_out_2[18]),
    .en(telescope_computing_system_1_tk0_out_2[17]));
  Telescope_Computing_System telescope_computing_system_1 (
    .OS_Running(telescope_computing_system_1_os_running),
    .Status_Code(telescope_computing_system_1_status_code), .Power_On(button_1_out), .Clock_Input(clk),
    .Pause(button_2_out), .Pause_Mode(1'b1), .STOP(button_3_out),
    .OS_Adr(telescope_computing_system_1_os_adr), .OS_In(TelescopeTest_d), .D0_In(Drive_0_d),
    .D0_Out(telescope_computing_system_1_d0_out), .D1_In({16{1'b0}}), .D2_In({16{1'b0}}), .D3_In({16{1'b0}}),
    .TNET_O_0(telescope_computing_system_1_tnet_o_0), .TNET_I_0(telescope_computing_system_2_tnet_o_0),
    .TNET_I_1({19{1'b0}}), .TNET_I_2({19{1'b0}}), .TNET_I_3({19{1'b0}}),
    .TK0_Out({telescope_computing_system_1_tk0_out_2, telescope_computing_system_1_tk0_out}),
    .K0_In({Keyboard_0_av[16], Keyboard_0_d}), .K1_In({17{1'b0}}), .K2_In({17{1'b0}}), .K3_In({17{1'b0}}),
    .GPO_0({telescope_computing_system_1_gpo_0_2, telescope_computing_system_1_gpo_0}),
    .GPI_0({2'b11, register_1_q}), .GPI_1({18{1'b0}}), .GPI_2({18{1'b0}}), .GPI_3({18{1'b0}}));  // open: D1_Out, D2_Out, D3_Out, TNET_O_1, TNET_O_2, TNET_O_3, TK1_Out, TK2_Out, TK3_Out, GPO_1, GPO_2, GPO_3
  LED led_1 (.in(telescope_computing_system_1_os_running));
  Button button_1 (.out(button_1_out));
  Button button_2 (.out(button_2_out));
  Button button_3 (.out(button_3_out));
  ROM #(.AddrBits(16), .Bits(16)) TelescopeTest (
    .A(telescope_computing_system_1_os_adr), .sel(1'b1), .D(TelescopeTest_d));
  Register #(.Bits(16)) register_1 (
    .D(telescope_computing_system_1_gpo_0), .C(telescope_computing_system_1_gpo_0_2[18]),
    .en(telescope_computing_system_1_gpo_0_2[17]), .Q(register_1_q));
  EEPROMDualPort #(.AddrBits(16), .Bits(16)) Drive_0 (
    .A(telescope_computing_system_1_d0_out[31:16]), .Din(telescope_computing_system_1_d0_out[15:0]),
    .str(telescope_computing_system_1_d0_out[32]), .C(telescope_computing_system_1_d0_out[33]), .ld(1'b1),
    .D(Drive_0_d));
  // Probe on telescope_computing_system_1_d0_out[31:16]
  // Probe Status on telescope_computing_system_2_status_code
  Telescope_Computing_System telescope_computing_system_2 (
    .OS_Running(telescope_computing_system_2_os_running),
    .Status_Code(telescope_computing_system_2_status_code), .Power_On(button_4_out), .Clock_Input(clk_2),
    .Pause(button_5_out), .Pause_Mode(1'b1), .STOP(button_6_out),
    .OS_Adr(telescope_computing_system_2_os_adr), .OS_In(TestServe_d), .D0_In({16{1'b0}}),
    .D1_In({16{1'b0}}), .D2_In({16{1'b0}}), .D3_In({16{1'b0}}),
    .TNET_O_0(telescope_computing_system_2_tnet_o_0), .TNET_I_0(telescope_computing_system_1_tnet_o_0),
    .TNET_I_1({19{1'b0}}), .TNET_I_2({19{1'b0}}), .TNET_I_3({19{1'b0}}), .K0_In({17{1'b0}}),
    .K1_In({17{1'b0}}), .K2_In({17{1'b0}}), .K3_In({17{1'b0}}), .GPI_0({18{1'b0}}), .GPI_1({18{1'b0}}),
    .GPI_2({18{1'b0}}), .GPI_3({18{1'b0}}));  // open: D0_Out, D1_Out, D2_Out, D3_Out, TNET_O_1, TNET_O_2, TNET_O_3, TK0_Out, TK1_Out, TK2_Out, TK3_Out, GPO_0, GPO_1, GPO_2, GPO_3
  LED led_2 (.in(telescope_computing_system_2_os_running));
  Button button_4 (.out(button_4_out));
  Button button_5 (.out(button_5_out));
  Button button_6 (.out(button_6_out));
  ROM #(.AddrBits(16), .Bits(16)) TestServe (.A(telescope_computing_system_2_os_adr), .sel(1'b1), .D(TestServe_d));

  // Notes on the sheet:
  //   clk: Hz: 256
  //   clk_2: Hz: 256
  //   contents of TelescopeTest (hex, n*v repeats v):
  //   fd,4600,c,1,2,3,61,62,63,31,32,33,ffff,50a0,f000,5090,1,50a0,e000
  //   ,3090,5000,1,50a0,2000,3090,3019,cb10,4800,d5,50a0,0,3009,3019
  //   ,3029,50a0,2000,3039,5040,1,ab34,db33,4800,d5,5030,0,6043,2,cb04
  //   ,4800,da,9931,6043,2,cb14,4800,da,9931,6043,2,cb24,4800,da,5000
  //   ,4,3090,3019,cb01,4000,da,50a0,2000,5090,4,50a0,0,3019,cb01,4800
  //   ,da,4600,50,50a0,4000,b100,6010,5,4d00,55,cb19,4800,df,9901,6010
  //   ,5,4d00,5d,cb19,4800,df,9901,6010,5,4d00,65,cb19,4800,df,b100
  //   ,6090,8,9901,6090,8,9901,6090,8,4600,75,b100,50c0,500,50f0,84
  //   ,50a0,6002,4500,83,4400,83,9901,3090,9b01,0,9200,4000,e4,4d00
  //   ,e9,4c00,e9,5000,23,3090,3019,cb01,4800,e9,4600,94,50a0,8000,4500
  //   ,ee,4c00,ee,5090,1,4400,ee,4d00,9e,3009,4500,ee,4c00,ee,5010,2
  //   ,cb01,4800,ee,4600,ac,50a0,e000,3009,f000,f000,f000,3019,ab10
  //   ,db14,4800,f3,50a0,e800,3090,50a0,e000,3009,f000,3019,cb01,4800
  //   ,f3,50a0,e800,9290,4800,f3,50a0,f000,3009,3019,cb01,4000,f8,4600
  //   ,d0,50a0,f000,5090,2,0,50a0,f000,5090,f002,0,50a0,f000,5090,f001
  //   ,0,50a0,f000,5090,f003,0,50a0,f000,5090,f005,0,50a0,f000,5090
  //   ,f006,0,50a0,f000,5090,f007,0,50a0,f000,5090,f008,0,50a0,f000
  //   ,5090,f009
  //   contents of Drive_0 (hex, n*v repeats v):
  //   0,1,2,3,4
  //   contents of TestServe (hex, n*v repeats v):
  //   1c,4600,2,50a0,8000,4d00,4,3009,5010,1,cb01,4800,13,5090,2,50a0
  //   ,f000,5090,2,0,50a0,8000,5090,ffff,50a0,f000,5090,ffff
endmodule
