// Digital circuit Test Sandbox.dig as structural Verilog
module Test_Sandbox (
  input  clk
);

  wire and_1_out, and_2_out, and_3_out, and_4_out, comparator_1_eq, delay_1_out, glass_cpu_1_p13,
       glass_cpu_1_p15, glass_cpu_1_p16, glass_cpu_1_p17, glass_cpu_1_p18, glass_cpu_1_p19, glass_cpu_1_p20,
       or_1_out, or_2_out, Pause_CPU_out, Power_On_Computer_out, Resume_CPU_out, rs_ff_as_1_q, rs_ff_as_2_q;
  wire [15:0] add_1_s, BOOT_d, counter_1_out, counter_2_out, glass_cpu_1_p4, glass_cpu_1_p11,
       glass_cpu_1_p12, glass_cpu_1_p14, multiplexer_1_out, multiplexer_2_out, Program_d;
  wire [31:0] counter_3_out;

  Button Power_On_Computer (.out(Power_On_Computer_out));
  Delay #(.delayTime(3)) delay_1 (.in(Power_On_Computer_out), .out(delay_1_out));
  Button Pause_CPU (.out(Pause_CPU_out));
  Button Resume_CPU (.out(Resume_CPU_out));
  Counter #(.Bits(16)) counter_1 (.en(glass_cpu_1_p18), .C(clk), .clr(1'b0), .out(counter_1_out));  // open: ovf
  and and_1 (and_1_out, Power_On_Computer_out, delay_1_out);
  and and_2 (and_2_out, Pause_CPU_out, rs_ff_as_1_q);
  and and_3 (and_3_out, Resume_CPU_out, rs_ff_as_1_q);
  ROM #(.AddrBits(16), .Bits(16)) Program (.A(counter_1_out), .sel(1'b1), .D(Program_d));
  RS_FF_AS rs_ff_as_1 (.S(comparator_1_eq), .R(1'b0), .Q(rs_ff_as_1_q));  // open: nQ
  RS_FF_AS rs_ff_as_2 (.S(and_1_out), .R(comparator_1_eq), .Q(rs_ff_as_2_q));  // open: nQ
  and and_4 (and_4_out, rs_ff_as_2_q, comparator_1_eq);
  or or_1 (or_1_out, and_4_out, and_3_out);
  Counter #(.Bits(16)) counter_2 (.en(rs_ff_as_2_q), .C(clk), .clr(1'b0), .out(counter_2_out));  // open: ovf
  // Glass_CPU glass_cpu_1: pin names not known; wires that end beside it: or_1_out, and_2_out, clk, glass_cpu_1_p4, Program_d, 1'b1, 1'b1, 4'b0000, 4'b0000, 1'b0, glass_cpu_1_p11, glass_cpu_1_p12, glass_cpu_1_p13, glass_cpu_1_p14, glass_cpu_1_p15, glass_cpu_1_p16, glass_cpu_1_p17, glass_cpu_1_p18, glass_cpu_1_p19, glass_cpu_1_p20
  ROM #(.AddrBits(16), .Bits(16)) BOOT (.A(counter_2_out), .sel(1'b1), .D(BOOT_d));
  LED led_1 (.in(glass_cpu_1_p17));
  Comparator #(.Bits(16)) comparator_1 (.a(16'hfaba), .b(BOOT_d), .eq(comparator_1_eq));  // open: gt, lt
  Terminal terminal_1 (.D(glass_cpu_1_p19), .C(clk), .en(glass_cpu_1_p20));
  Multiplexer #(.Bits(16)) multiplexer_1 (
    .sel(rs_ff_as_2_q), .in_0(glass_cpu_1_p11), .in_1(counter_2_out), .out(multiplexer_1_out));
  Multiplexer #(.Bits(16)) multiplexer_2 (
    .sel(rs_ff_as_2_q), .in_0(glass_cpu_1_p12), .in_1(BOOT_d), .out(multiplexer_2_out));
  or or_2 (or_2_out, rs_ff_as_2_q, glass_cpu_1_p13);
  Counter #(.Bits(32)) counter_3 (.en(1'b1), .C(glass_cpu_1_p16), .clr(1'b0), .out(counter_3_out));  // open: ovf
  Add #(.Bits(16)) add_1 (.a(glass_cpu_1_p14), .b(16'h2), .c_i(1'b0), .s(add_1_s));  // open: c_o
  // Probe Test IOP on glass_cpu_1_p15
  // Probe Memory Address on glass_cpu_1_p11
  // Probe Cycles Used on counter_3_out
  // Probe RTL Line on add_1_s
  RAMDualPort #(.AddrBits(16), .isProgramMemory("true"), .Bits(16)) RAM (
    .A(multiplexer_1_out), .Din(multiplexer_2_out), .str(or_2_out), .C(clk), .ld(1'b1), .D(glass_cpu_1_p4));

  // Notes on the sheet:
  //   clk: Hz: 16
  //   contents of Program (hex, n*v repeats v):
  //   1c,4600,f,48,65,6c,6c,6f,20,57,6f,72,6c,64,a,ffff,50a0,0,b110
  //   ,6001,2,d901,4200,1b,3090,9911,4600,12
  //   contents of BOOT (hex, n*v repeats v):
  //   4600,1f,b100,b110,5020,34,7001,100,b911,cb12,4100,6,50a0,f800
  //   ,b110,3029,3009,7001,100,b911,cb12,4100,10,b100,b110,b120,b1a0
  //   ,b1f0,0,2000,f33d,5010,2,5000,1f,ab01,b110,6021,2,7021,ff02,b911
  //   ,cb10,4100,25,50c0,ff,b1a0,50e0,2,1000,faba
endmodule
