// Logisim project Glass CPU Work.circ as structural Verilog: 9 circuits, main circuit CPU Test Space
module CPU_Test_Space (
);

  wire clock_1_out, glass_cpu_1_clock_out, glass_cpu_1_cpu_is_reading_i_o, glass_cpu_1_cpu_is_writing_i_o,
       glass_cpu_1_current_process_is_kernel, glass_cpu_1_is_on, glass_cpu_1_ram_write, Off_out, On_out,
       Ready_q, Ready_qn, Rst_out;
  wire [4:0] glass_cpu_1_selected_i_o_device;
  wire [15:0] adder_1_out, Cycles_Used_q, glass_cpu_1_i_o_output, glass_cpu_1_program_counter,
       glass_cpu_1_ram_address, glass_cpu_1_ram_data_output, ram_1_data, Test_Interface_q;

  Clock clock_1 (.out(clock_1_out));
  Button Rst (.out(Rst_out));
  Button On (.out(On_out));
  Button Off (.out(Off_out));
  LED led_1 (.in(glass_cpu_1_is_on));
  Glass_CPU glass_cpu_1 (
    .Clock_Input(clock_1_out), .Reset_CPU(Rst_out), .Start_CPU(On_out), .Pause_CPU(Off_out),
    .RAM_Data_Input(ram_1_data), .RAM_Data_Output(glass_cpu_1_ram_data_output),
    .RAM_Write(glass_cpu_1_ram_write), .RAM_Address(glass_cpu_1_ram_address), .I_O_Is_Reading_CPU(Ready_qn),
    .CPU_Is_Writing_I_O(glass_cpu_1_cpu_is_writing_i_o), .I_O_Output(glass_cpu_1_i_o_output),
    .I_O_Input(Test_Interface_q), .CPU_Is_Reading_I_O(glass_cpu_1_cpu_is_reading_i_o),
    .I_O_Is_Writing_CPU(Ready_q), .Selected_I_O_Device(glass_cpu_1_selected_i_o_device),
    .Current_Process_Is_Kernel(glass_cpu_1_current_process_is_kernel),
    .Program_Counter(glass_cpu_1_program_counter), .Is_On(glass_cpu_1_is_on),
    .Clock_Out(glass_cpu_1_clock_out), .Mask_Int_Lines(3'b000), .Non_Msk_Int(1'b0));  // open: HLB_For_Current_Process
  RAM #(.addrWidth(16), .dataWidth(16), .bus("separate")) ram_1 (
    .addr(glass_cpu_1_ram_address), .din(glass_cpu_1_ram_data_output), .data(ram_1_data),
    .str(glass_cpu_1_ram_write), .clk(clock_1_out));  // open: sel, ld, clr
  // Probe on glass_cpu_1_selected_i_o_device
  // Probe on adder_1_out
  Adder #(.width(16)) adder_1 (.a(16'h2), .b(glass_cpu_1_program_counter), .out(adder_1_out));  // open: cin, cout
  Counter #(.width(16), .max('hffff)) Cycles_Used (
    .Q(Cycles_Used_q), .clk(glass_cpu_1_clock_out), .clr(Rst_out));  // open: load, D, count, carry
  LED led_2 (.in(glass_cpu_1_current_process_is_kernel));
  // Probe on Cycles_Used_q
  Register #(.width(16)) Test_Interface (
    .D(glass_cpu_1_i_o_output), .en(glass_cpu_1_cpu_is_writing_i_o), .Q(Test_Interface_q), .clk(clock_1_out));  // open: clr
  // Probe on Test_Interface_q
  S_R_Flip_Flop Ready (
    .S(1'b0), .clk(clock_1_out), .R(glass_cpu_1_cpu_is_reading_i_o), .Q(Ready_q), .Qn(Ready_qn),
    .reset(Rst_out));  // open: preset, en
  LED led_3 (.in(Ready_q));
endmodule

module Assembler_Workspace (
);

  wire clock_1_out, demultiplexer_2_out0, demultiplexer_2_out1, glass_cpu_1_clock_out,
       glass_cpu_1_cpu_is_reading_i_o, glass_cpu_1_cpu_is_writing_i_o, glass_cpu_1_is_on,
       glass_cpu_1_ram_write, Reset_out, Start_out, Stop_out;
  wire [4:0] glass_cpu_1_selected_i_o_device;
  wire [6:0] bit_extender_1_out;
  wire [15:0] counter_1_q, Current_Char_num_q, demultiplexer_1_out0, demultiplexer_1_out1,
       glass_cpu_1_i_o_output, glass_cpu_1_ram_address, glass_cpu_1_ram_data_output, Output_PC_q, ram_1_data,
       rom_1_data;

  Counter #(.width(16), .max('hffff)) Current_Char_num (
    .D(demultiplexer_1_out0), .count(glass_cpu_1_cpu_is_reading_i_o), .Q(Current_Char_num_q),
    .clk(clock_1_out), .clr(demultiplexer_2_out0));  // open: load, carry
  Clock clock_1 (.out(clock_1_out));
  ROM #(.addrWidth(16), .dataWidth(16)) rom_1 (.addr(Current_Char_num_q), .data(rom_1_data));  // open: sel
  Button Reset (.out(Reset_out));
  Button Start (.out(Start_out));
  Button Stop (.out(Stop_out));
  LED On (.in(glass_cpu_1_is_on));
  Glass_CPU glass_cpu_1 (
    .Clock_Input(clock_1_out), .Reset_CPU(Reset_out), .Start_CPU(Start_out), .Pause_CPU(Stop_out),
    .RAM_Data_Input(ram_1_data), .RAM_Data_Output(glass_cpu_1_ram_data_output),
    .RAM_Write(glass_cpu_1_ram_write), .RAM_Address(glass_cpu_1_ram_address),
    .CPU_Is_Writing_I_O(glass_cpu_1_cpu_is_writing_i_o), .I_O_Output(glass_cpu_1_i_o_output),
    .I_O_Input(rom_1_data), .CPU_Is_Reading_I_O(glass_cpu_1_cpu_is_reading_i_o),
    .Selected_I_O_Device(glass_cpu_1_selected_i_o_device), .Is_On(glass_cpu_1_is_on),
    .Clock_Out(glass_cpu_1_clock_out), .Mask_Int_Lines(3'b000), .Non_Msk_Int(1'b0));  // open: I_O_Is_Reading_CPU, I_O_Is_Writing_CPU, HLB_For_Current_Process, Current_Process_Is_Kernel, Program_Counter
  Demultiplexer #(.width(16), .disabled(0), .enable("false")) demultiplexer_1 (
    .out0(demultiplexer_1_out0), .out1(demultiplexer_1_out1), .in(glass_cpu_1_i_o_output),
    .sel(glass_cpu_1_selected_i_o_device[0]));
  Demultiplexer #(.disabled(0), .enable("false")) demultiplexer_2 (
    .out0(demultiplexer_2_out0), .out1(demultiplexer_2_out1), .in(glass_cpu_1_cpu_is_writing_i_o),
    .sel(glass_cpu_1_selected_i_o_device[0]));
  RAM #(.addrWidth(16), .dataWidth(16), .bus("separate")) ram_1 (
    .addr(glass_cpu_1_ram_address), .din(glass_cpu_1_ram_data_output), .data(ram_1_data),
    .str(glass_cpu_1_ram_write), .clk(clock_1_out));  // open: sel, ld, clr
  Bit_Extender #(.in_width(16), .out_width(7)) bit_extender_1 (.in(rom_1_data), .out(bit_extender_1_out));
  TTY #(.rows(16), .cols(90)) tty_1 (
    .data(bit_extender_1_out), .clk(clock_1_out), .we(glass_cpu_1_cpu_is_reading_i_o), .clr(Reset_out));
  // Probe on counter_1_q
  Counter #(.width(16), .max('hffff)) counter_1 (
    .count(1'b1), .Q(counter_1_q), .clk(glass_cpu_1_clock_out), .clr(Reset_out));  // open: load, D, carry
  Counter #(.width(16), .max('hffff)) Output_PC (
    .count(demultiplexer_2_out1), .Q(Output_PC_q), .clk(clock_1_out), .clr(demultiplexer_2_out0));  // open: load, D, carry
  RAM #(.addrWidth(16), .dataWidth(16), .bus("separate")) ram_2 (
    .addr(Output_PC_q), .din(demultiplexer_1_out1), .str(demultiplexer_2_out1), .clk(clock_1_out));  // open: data, sel, ld, clr

  // Notes on the sheet:
  //   INPUT ASCII FILE
  //   contents of rom_1 (hex, n*v repeats v):
  //   2f 20 4c 61 72 67 65 20 74 65 73 74 20 6f 66 20 74 68 65 20 54 41 53 4c 20 76 31 20 73 70 65 63 69
  //   66 69 63 61 74 69 6f 6e 73 2e a 2f 20 4d 65 61 6e 74 20 74 6f 20 65 6e 73 75 72 65 20 74 68 65 20 43
  //   50 55 20 28 61 6e 64 2f 6f 72 20 61 73 73 65 6d 62 6c 65 72 29 20 69 73 20 77 6f 72 6b 69 6e 67 20
  //   70 72 6f 70 65 72 6c 79 2e a 2f 20 54 68 69 73 20 69 6e 63 6c 75 64 65 73 20 61 6c 6c 20 69 6e 73 74
  //   72 75 63 74 69 6f 6e 73 2c 20 61 20 66 65 77 20 72 65 67 69 73 74 65 72 73 2c 20 61 6e 64 20 61 20
  //   63 6f 75 70 6c 65 20 41 4c 55 20 6f 70 73 2e a a 2f 20 49 74 20 6d 75 6c 74 69 70 6c 69 65 73 20 38
  //   20 62 79 20 36 20 69 6e 20 74 68 72 65 65 20 64 69 66 66 65 72 65 6e 74 20 77 61 79 73 2e a 2f 20 54
  //   68 65 20 6f 75 74 70 75 74 20 69 73 20 77 72 69 74 74 65 6e 20 74 6f 20 74 68 65 20 49 2f 4f 20 65
  //   61 63 68 20 74 69 6d 65 2e a 2f 20 49 66 20 74 68 65 20 6e 75 6d 62 65 72 20 69 73 20 69 6e 63 6f 72
  //   72 65 63 74 2c 20 69 74 20 77 69 6c 6c 20 61 6c 73 6f 20 77 72 69 74 65 20 4e 55 4c 4c 20 74 6f 20
  //   74 68 65 20 73 74 6f 70 20 6c 69 6e 65 20 69 6e 20 52 41 4d 2e a 2f 20 49 66 20 69 74 20 77 6f 72 6b
  //   73 20 65 76 65 72 79 20 74 69 6d 65 2c 20 74 68 65 20 61 6e 73 77 65 72 20 77 69 6c 6c 20 62 65 20
  //   77 72 69 74 74 65 6e 20 74 6f 20 74 68 65 20 73 74 6f 70 20 6c 69 6e 65 2e a a 2f 20 52 47 30 20 61
  //   6e 64 20 31 20 63 6f 6e 74 61 69 6e 20 74 68 65 20 74 77 6f 20 6e 75 6d 62 65 72 73 2e a 2f 20 52 47
  //   32 20 63 6f 6e 74 61 69 6e 73 20 74 68 65 20 61 6e 73 77 65 72 20 6f 66 20 74 68 65 20 70 72 65 76
  //   69 6f 75 73 20 61 74 74 65 6d 70 74 2e a 2f 20 52 47 33 20 63 6f 6e 74 61 69 6e 73 20 61 20 72 65 74
  //   75 72 6e 20 61 64 64 72 65 73 73 20 28 66 6f 72 20 74 68 65 20 66 75 6e 63 74 69 6f 6e 29 2e a 2f 20
  //   52 47 34 20 63 6f 6e 74 61 69 6e 73 20 74 68 65 20 6e 75 6d 62 65 72 20 6f 66 20 73 75 63 63 65 73
  //   73 66 75 6c 20 6f 70 65 72 61 74 69 6f 6e 73 2e a 2f 20 52 47 37 20 63 6f 6e 74 61 69 6e 73 20 74 68
  //   65 20 65 78 70 65 63 74 65 64 20 72 65 73 75 6c 74 20 66 6f 72 20 71 75 69 63 6b 20 61 63 63 65 73
  //   73 2e a a 2f 20 41 6e 64 20 74 6f 20 72 65 61 6c 6c 79 20 6d 61 6b 65 20 73 75 72 65 20 74 68 61 74
  //   20 79 6f 75 20 70 61 73 73 65 64 20 74 68 65 20 74 65 73 74 2c 20 74 68 65 20 72 65 67 69 73 74 65
  //   72 73 20 73 68 6f 75 6c 64 20 65 6e 64 20 61 73 3a a 2f 20 38 20 36 20 33 30 20 32 34 20 33 20 30 20
  //   30 20 33 30 20 35 20 30 20 30 20 32 30 20 33 39 a 2f 20 48 65 78 61 64 65 63 69 6d 61 6c 2c 20 69 6e
  //   20 74 68 65 20 72 65 67 69 73 74 65 72 73 20 26 20 73 65 6c 65 63 74 69 6f 6e 20 63 69 72 63 75 69
  //   74 2e a a 4a 49 46 20 54 52 55 20 3e 4d 61 69 6e 2e 49 6e 69 74 a a 2f 20 41 6c 6c 20 76 61 72 69 61
  //   62 6c 65 73 20 61 72 65 20 69 6e 20 6d 65 6d 6f 72 79 2c 20 74 6f 20 65 78 65 72 63 69 73 65 20 74
  //   68 65 20 6d 65 6d 6f 72 79 20 61 63 63 65 73 73 20 63 69 72 63 75 69 74 73 2e a 23 6e 75 6d 4f 6e 65
  //   20 3d 20 30 78 30 30 30 38 a 23 6e 75 6d 54 77 6f 20 3d 20 30 78 30 30 30 36 a 23 65 78 70 65 63 74
  //   65 64 52 65 73 75 6c 74 20 3d 20 30 78 30 30 33 30 a 23 72 65 74 75 72 6e 42 75 66 66 65 72 20 3d 20
  //   30 78 4*30 a a 2f 20 71*2d a a 23 4d 61 69 6e 2e 49 6e 69 74 a 4*20 2f 20 57 65 27 72 65 20 67 6f 69
  //   6e 67 20 74 6f 20 6c 6f 61 64 20 74 68 65 20 76 61 72 69 61 62 6c 65 73 2e a 4*20 4c 4f 44 20 52 47
  //   30 20 52 47 30 20 3e 6e 75 6d 4f 6e 65 a 4*20 4c 4f 44 20 52 47 31 20 52 47 31 20 3e 6e 75 6d 54 77
  //   6f a 4*20 4c 4f 44 20 52 47 37 20 52 47 37 20 3e 65 78 70 65 63 74 65 64 52 65 73 75 6c 74 a 4*20 2f
  //   20 4e 6f 72 6d 61 6c 6c 79 20 61 74 20 74 68 65 20 73 74 61 72 74 20 6f 66 20 66 75 6e 63 74 69 6f
  //   6e 73 2c 20 77 65 20 77 72 69 74 65 20 74 6f 20 74 68 65 20 73 74 61 63 6b 2e a 4*20 2f 20 53 6f 20
  //   77 65 27 72 65 20 67 6f 69 6e 67 20 74 6f 20 64 6f 20 74 68 61 74 20 68 65 72 65 2c 20 62 75 74 20
  //   77 69 74 68 20 73 6f 6d 65 20 66 61 6e 63 79 20 74 72 69 63 6b 65 72 79 2e a 4*20 2f 20 4f 75 72 20
  //   73 74 61 63 6b 20 77 69 6c 6c 20 69 6e 73 74 65 61 64 20 62 65 20 74 68 65 20 52 65 74 75 72 6e 42
  //   75 66 66 65 72 20 76 61 72 69 61 62 6c 65 2e a 4*20 2f 20 57 65 20 75 73 65 20 4c 44 49 20 74 6f 20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
  //   THE ASSEMBLER
  //   OUTPUT MACHINE CODE
endmodule

module ASCII_Import_Workspace (
  input  Enable
);

  wire and_1_out, C_out, clock_1_out, R_out;
  wire [6:0] bit_extender_1_out;
  wire [15:0] counter_1_q, rom_1_data;

  Clock clock_1 (.out(clock_1_out));
  Counter #(.width(16), .max('hffff)) counter_1 (
    .count(Enable), .Q(counter_1_q), .clk(and_1_out), .clr(R_out));  // open: load, D, carry
  and and_1 (and_1_out, C_out, clock_1_out);
  Button R (.out(R_out));
  ROM #(.addrWidth(16), .dataWidth(16)) rom_1 (.addr(counter_1_q), .data(rom_1_data), .sel(Enable));
  Button C (.out(C_out));
  Bit_Extender #(.in_width(16), .out_width(7)) bit_extender_1 (.in(rom_1_data), .out(bit_extender_1_out));
  TTY #(.rows(48), .cols(96)) tty_1 (.data(bit_extender_1_out), .clk(and_1_out), .we(Enable), .clr(R_out));

  // Notes on the sheet:
  //   contents of rom_1 (hex, n*v repeats v):
  //   4a 49 46 20 54 52 55 20 3e 53 74 61 72 74 50 6f 69 6e 74 a a 28 2f 20 43 6f 6e 73 74 61 6e 74 73 2c
  //   20 76 61 72 69 61 62 6c 65 73 2c 20 61 6e 64 20 74 61 62 6c 65 73 2e a 40 49 4e 46 4c 47 20 3d 20 30
  //   a 40 4f 55 54 46 4c 47 20 3d 20 30 78 38 30 30 a a 40 54 41 42 4c 45 53 54 4f 50 20 3d 20 30 78 4*46
  //   20 20 2f 20 4d 75 73 74 20 73 74 61 79 20 4e 55 4c 4c 2e a a 2f 20 49 6e 73 74 72 75 63 74 69 6f 6e
  //   20 74 61 62 6c 65 20 65 6e 74 72 69 65 73 3a 20 28 6d 6e 65 6d 6f 6e 69 63 5f 68 61 73 68 2c 20 74
  //   72 61 6e 73 6c 61 74 69 6f 6e 2c 20 6f 70 65 72 61 6e 64 5f 62 69 74 6d 61 70 29 a 28 23 49 6e 73 74
  //   54 61 62 6c 65 20 3d 20 5b 30 78 64 31 38 38 2c 20 30 78 4*30 2c 20 30 62 4*30 2c 20 20 2f 20 48 4c
  //   54 a 15*20 30 78 62 36 37 32 2c 20 30 78 31 30 30 30 2c 20 30 62 4*30 2c 20 20 2f 20 52 53 4d a
  //   15*20 30 78 63 66 33 33 2c 20 30 78 32 30 30 30 2c 20 30 62 4*30 2c 20 20 2f 20 53 59 53 a 15*20 30
  //   78 64 39 65 64 2c 20 30 78 33 30 30 30 2c 20 30 62 30 30 31 31 2c 20 20 2f 20 4d 4f 56 a 15*20 30 78
  //   39 39 32 61 2c 20 30 78 34 30 30 30 2c 20 30 62 30 31 30 30 2c 20 20 2f 20 4a 49 46 a 15*20 30 78 61
  //   34 38 63 2c 20 30 78 35 30 30 30 2c 20 30 62 30 30 31 30 2c 20 20 2f 20 4c 44 49 a 15*20 30 78 39 31
  //   65 63 2c 20 30 78 36 30 30 30 2c 20 30 62 30 30 31 31 2c 20 20 2f 20 4c 4f 44 a 15*20 30 78 63 61 39
  //   33 2c 20 30 78 37 30 30 30 2c 20 30 62 30 30 31 31 2c 20 20 2f 20 53 54 52 a 15*20 30 78 39 39 38 31
  //   2c 20 30 78 38 30 30 30 2c 20 30 62 30 31 31 31 2c 20 20 2f 20 41 4c 46 a 15*20 30 78 39 39 32 31 2c
  //   20 30 78 39 30 30 30 2c 20 30 62 4*31 2c 20 20 2f 20 41 49 46 a 15*20 30 78 64 35 38 31 2c 20 30 78
  //   41 30 30 30 2c 20 30 62 30 31 31 31 2c 20 20 2f 20 41 4c 55 a 15*20 30 78 61 35 38 31 2c 20 30 78 42
  //   30 30 30 2c 20 30 62 4*31 2c 20 20 2f 20 41 4c 49 a 15*20 30 78 62 38 63 31 2c 20 30 78 43 30 30 30
  //   2c 20 30 62 30 31 31 31 2c 20 20 2f 20 41 46 4e a 15*20 30 78 62 39 32 31 2c 20 30 78 44 30 30 30 2c
  //   20 30 62 4*31 2c 20 20 2f 20 41 49 4e a 15*20 30 78 63 31 65 65 2c 20 30 78 4*46 2c 20 30 62 4*30 2c
  //   20 20 2f 20 4e 4f 50 a 15*20 3e 54 41 42 4c 45 53 54 4f 50 a 15*20 5d 29 a a 2f 20 52 65 67 69 73 74
  //   65 72 20 74 61 62 6c 65 20 65 6e 74 72 69 65 73 3a 20 28 6d 6e 65 6d 6f 6e 69 63 5f 68 61 73 68 2c
  //   20 74 72 61 6e 73 6c 61 74 69 6f 6e 29 a 28 23 52 65 67 54 61 62 6c 65 20 3d 20 5b 30 78 34 30 46 32
  //   2c 20 30 78 30 2c 20 20 2f 20 52 47 30 a 14*20 30 78 34 34 46 32 2c 20 30 78 31 2c 20 20 2f 20 52 47
  //   31 a 14*20 30 78 34 38 46 32 2c 20 30 78 32 2c 20 20 2f 20 52 47 32 a 14*20 30 78 34 43 46 32 2c 20
  //   30 78 33 2c 20 20 2f 20 52 47 33 a 14*20 30 78 35 30 46 32 2c 20 30 78 34 2c 20 20 2f 20 52 47 34 a
  //   14*20 30 78 35 34 46 32 2c 20 30 78 35 2c 20 20 2f 20 52 47 35 a 14*20 30 78 35 38 46 32 2c 20 30 78
  //   36 2c 20 20 2f 20 52 47 36 a 14*20 30 78 44 32 41 46 2c 20 30 78 36 2c 20 20 2f 20 4f 55 54 a 14*20
  //   30 78 35 43 46 32 2c 20 30 78 37 2c 20 20 2f 20 52 47 37 a 14*20 30 78 30 30 33 32 2c 20 30 78 37 2c
  //   20 20 2f 20 52 41 a 14*20 30 78 30 30 37 30 2c 20 30 78 38 2c 20 20 2f 20 50 43 a 14*20 30 78 30 31
  //   45 39 2c 20 30 78 39 2c 20 20 2f 20 49 4f a 14*20 30 78 39 44 38 36 2c 20 30 78 41 2c 20 20 2f 20 46
  //   4c 47 a 14*20 30 78 30 32 31 33 2c 20 30 78 42 2c 20 20 2f 20 53 50 a 14*20 30 78 38 39 38 38 2c 20
  //   30 78 43 2c 20 20 2f 20 48 4c 42 a 14*20 30 78 39 32 38 33 2c 20 30 78 44 2c 20 20 2f 20 43 54 44 a
  //   14*20 30 78 38 45 30 35 2c 20 30 78 45 2c 20 20 2f 20 45 50 43 a 14*20 30 78 38 37 30 35 2c 20 30 78
  //   46 2c 20 20 2f 20 45 58 41 a 14*20 3e 54 41 42 4c 45 53 54 4f 50 a 14*20 5d 29 a a 2f 20 4d 6f 64 69
  //   66 69 65 72 20 74 61 62 6c 65 20 65 6e 74 72 69 65 73 3a 20 28 6d 6e 65 6d 6f 6e 69 63 5f 68 61 73
  //   68 2c 20 74 72 61 6e 73 6c 61 74 69 6f 6e 29 a 28 23 4d 6f 64 54 61 62 6c 65 20 3d 20 5b 30 78 44 31
  //   45 45 2c 20 30 78 30 2c 20 20 2f 20 4e 4f 54 a 14*20 30 78 39 31 43 31 2c 20 30 78 31 2c 20 20 2f 20
  //   41 4e 44 a 14*20 30 78 30 32 34 46 2c 20 30 78 32 2c 20 20 2f 20 4f 52 a 14*20 30 78 43 39 46 38 2c
  //   20 30 78 33 2c 20 20 2f 20 58 4f 52 a 14*20 30 78 38 39 39 33 2c 20 30 78 34 2c 20 20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
endmodule

module Glass_CPU (
  input  [15:0] RAM_Data_Input,
  input  Clock_Input,
  input  Reset_CPU,
  input  Start_CPU,
  input  Pause_CPU,
  input  [2:0] Mask_Int_Lines,
  input  Non_Msk_Int,
  input  I_O_Is_Reading_CPU,
  input  [15:0] I_O_Input,
  input  I_O_Is_Writing_CPU,
  output [15:0] RAM_Data_Output,
  output RAM_Write,
  output [15:0] RAM_Address,
  output Is_On,
  output Clock_Out,
  output Current_Process_Is_Kernel,
  output [15:0] HLB_For_Current_Process,
  output [15:0] Program_Counter,
  output CPU_Is_Writing_I_O,
  output [15:0] I_O_Output,
  output CPU_Is_Reading_I_O,
  output [4:0] Selected_I_O_Device
);

  wire control_unit_1_adder_enable, control_unit_1_alu_enable, control_unit_1_alu_flag_write,
       control_unit_1_alu_immediate, control_unit_1_pc_1, control_unit_1_pc_2, control_unit_1_prin_exception,
       control_unit_1_ram_to_bus, control_unit_1_read0, control_unit_1_read1, control_unit_1_read1_to_bus,
       control_unit_1_to_kernel, control_unit_1_to_process, control_unit_1_write,
       registers_selection_1_flg_write, registers_selection_1_pc_write, registers_selection_1_pror,
       system_flags_1_exception, system_flags_1_lo_enabled, system_flags_1_non_ignorable_exception;
  wire [1:0] control_unit_1_state_out, system_flags_1_current_isuser_inten_flags;
  wire [2:0] controlled_buffer_1_out;
  wire [3:0] alu_1_zero, control_unit_1_alu_opcode, control_unit_1_read0_code, control_unit_1_read1_code,
       control_unit_1_write_code;
  wire [7:0] pull_resistor_3_node;
  wire [7:3] registers_selection_1_ctdz_event;
  wire [15:0] registers_selection_1_bus_0_output, registers_selection_1_bus_1_output, system_flags_1_output;

  Pull_Resistor pull_resistor_1 (.node(RAM_Data_Output));
  assign controlled_buffer_1_out = system_flags_1_current_isuser_inten_flags[0] ? Mask_Int_Lines : 3'bz;  // Controlled_Buffer controlled_buffer_1
  Pull_Resistor pull_resistor_2 (.node(controlled_buffer_1_out));
  or or_1 (registers_selection_1_ctdz_event[6], control_unit_1_prin_exception, registers_selection_1_pror);
  Pull_Resistor pull_resistor_3 (.node({pull_resistor_3_node[7:6], I_O_Is_Writing_CPU, I_O_Is_Reading_CPU, pull_resistor_3_node[3:0]}));
  assign RAM_Data_Output = control_unit_1_ram_to_bus ? RAM_Data_Input : 16'bz;  // Controlled_Buffer controlled_buffer_2
  Random #(.width(1), .seed(5623189)) random_1 (.clk(Clock_Input), .out(pull_resistor_3_node[7]));  // open: next, clr
  Control_Unit control_unit_1 (
    .Jump_Conditions({pull_resistor_3_node[7:6], I_O_Is_Writing_CPU, I_O_Is_Reading_CPU, pull_resistor_3_node[3:0]}),
    .RAM_Input(RAM_Data_Input), .Reset_All(Reset_CPU), .Clock_In(Clock_Input), .Start(Start_CPU),
    .Pause(Pause_CPU), .EX(system_flags_1_exception), .UE(system_flags_1_current_isuser_inten_flags),
    .Non_Ignorable_EX(system_flags_1_non_ignorable_exception), .PC_1(control_unit_1_pc_1),
    .PC_2(control_unit_1_pc_2), .RAM_to_Bus(control_unit_1_ram_to_bus), .Read0_to_RAM(RAM_Write),
    .Read1_to_Bus(control_unit_1_read1_to_bus), .To_Process(control_unit_1_to_process),
    .To_Kernel(control_unit_1_to_kernel), .ALU_Enable(control_unit_1_alu_enable),
    .ALU_Flag_Write(control_unit_1_alu_flag_write), .ALU_Immediate(control_unit_1_alu_immediate),
    .ALU_OpCode(control_unit_1_alu_opcode), .Write_Code(control_unit_1_write_code),
    .Write(control_unit_1_write), .Read0_Code(control_unit_1_read0_code), .Read0(control_unit_1_read0),
    .Read1_Code(control_unit_1_read1_code), .Read1(control_unit_1_read1),
    .SYS_Exception(registers_selection_1_ctdz_event[4]), .PRIN_Exception(control_unit_1_prin_exception),
    .Adder_Enable(control_unit_1_adder_enable), .Clock_Out(Clock_Out), .State_Out(control_unit_1_state_out),
    .Is_On(Is_On));
  System_Flags system_flags_1 (
    .UE_Push(control_unit_1_to_kernel), .UE_Pop(control_unit_1_to_process),
    .Exception_Lines({registers_selection_1_ctdz_event[7:6], Non_Msk_Int, registers_selection_1_ctdz_event[4:3], controlled_buffer_1_out}),
    .Input(RAM_Data_Output), .Write_Flags_Async(registers_selection_1_flg_write), .Clock(Clock_Out),
    .Reset_All(Reset_CPU), .Set_LOEn(control_unit_1_to_process), .Reset_LOEn(control_unit_1_to_kernel),
    .Current_IsUser_IntEn_Flags(system_flags_1_current_isuser_inten_flags), .Output(system_flags_1_output),
    .LO_Enabled(system_flags_1_lo_enabled), .ALU_Flag_In(alu_1_zero),
    .Write_ALU_Flags(control_unit_1_alu_flag_write), .ALU_Flags_Out(pull_resistor_3_node[3:0]),
    .Non_Ignorable_Exception(system_flags_1_non_ignorable_exception),
    .Clear_EX_Buffer(control_unit_1_to_kernel), .Exception(system_flags_1_exception),
    .IOP_Output(Selected_I_O_Device));
  assign I_O_Output = CPU_Is_Writing_I_O ? RAM_Data_Output : 16'bz;  // Controlled_Buffer controlled_buffer_3
  ALU alu_1 (
    .Input_A(registers_selection_1_bus_0_output), .Input_B(registers_selection_1_bus_1_output),
    .Immediate(control_unit_1_read1_code), .Output(RAM_Data_Output),
    .Immediate_Op(control_unit_1_alu_immediate), .Carry_Input(pull_resistor_3_node[2]),
    .OpCode(control_unit_1_alu_opcode), .ALU_Enable(control_unit_1_alu_enable), .Overflow(alu_1_zero[3]),
    .Carry_Out(alu_1_zero[2]), .Sign(alu_1_zero[1]), .Zero(alu_1_zero[0]));
  Registers___Selection registers_selection_1 (
    .Write(control_unit_1_write), .Write_Code(control_unit_1_write_code), .Reset_All(Reset_CPU),
    .Clock(Clock_Out), .Current_UE(system_flags_1_current_isuser_inten_flags), .PC_Input(Program_Counter),
    .IO_Input(I_O_Input), .FLG_Input(system_flags_1_output), .Read0_Code(control_unit_1_read0_code),
    .Read0(control_unit_1_read0), .Read1_Code(control_unit_1_read1_code), .Read1(control_unit_1_read1),
    .PC_Write(registers_selection_1_pc_write), .IO_Write(CPU_Is_Writing_I_O),
    .FLG_Write(registers_selection_1_flg_write), .HLB_Output(HLB_For_Current_Process),
    .CTDZ_Event(registers_selection_1_ctdz_event[3]), .PROR(registers_selection_1_pror),
    .Write_Bus_Input(RAM_Data_Output), .Bus_0_Output(registers_selection_1_bus_0_output),
    .Bus_1_Output(registers_selection_1_bus_1_output), .I_O_Read(CPU_Is_Reading_I_O));
  assign RAM_Data_Output = control_unit_1_read1_to_bus ? registers_selection_1_bus_1_output : 16'bz;  // Controlled_Buffer controlled_buffer_4
  assign RAM_Data_Output = RAM_Write ? registers_selection_1_bus_0_output : 16'bz;  // Controlled_Buffer controlled_buffer_5
  Addressing addressing_1 (
    .HLB_Input(HLB_For_Current_Process), .Data_Bus_Input(RAM_Data_Output), .Clock(Clock_Out),
    .Reset(Reset_CPU), .Write_to_PC(registers_selection_1_pc_write), .PC_1(control_unit_1_pc_1),
    .PC_2(control_unit_1_pc_2), .RAM_Address(RAM_Address), .OOB(registers_selection_1_ctdz_event[7]),
    .PC_Out(Program_Counter), .State_Number(control_unit_1_state_out),
    .Adder_Enable(control_unit_1_adder_enable), .Current_UE(system_flags_1_current_isuser_inten_flags),
    .LO_Enabled(system_flags_1_lo_enabled));
  not not_1 (Current_Process_Is_Kernel, system_flags_1_current_isuser_inten_flags[1]);
  // also tied to VCC on the sheet: pull_resistor_3_node[6]

  // Notes on the sheet:
  //   PRIV
endmodule

module Registers___Selection (
  input  Write,
  input  [15:0] Write_Bus_Input,
  input  [3:0] Write_Code,
  input  Reset_All,
  input  Clock,
  input  [1:0] Current_UE,
  input  [15:0] PC_Input,
  input  [15:0] IO_Input,
  input  [15:0] FLG_Input,
  input  Read0,
  input  [3:0] Read0_Code,
  input  Read1,
  input  [3:0] Read1_Code,
  output PC_Write,
  output IO_Write,
  output FLG_Write,
  output [15:0] HLB_Output,
  output CTDZ_Event,
  output PROR,
  output I_O_Read,
  output [15:0] Bus_0_Output,
  output [15:0] Bus_1_Output
);

  wire and_1_out, and_4_out, and_5_out, comparator_1_eq, comparator_2_gt, comparator_3_gt, comparator_4_gt,
       comparator_5_eq, comparator_6_eq, decoder_1_out0, decoder_1_out1, decoder_1_out2, decoder_1_out3,
       decoder_1_out4, decoder_1_out5, decoder_1_out6, decoder_1_out7, decoder_1_out11, decoder_1_out12,
       decoder_1_out13, decoder_1_out14, decoder_1_out15, not_1_out, or_1_out;
  wire [7:0] controlled_buffer_1_out;
  wire [15:0] CTD_q, EPC_q, EXA_q, RG0_q, RG1_q, RG2_q, RG3_q, RG4_q, RG5_q, RG6_q, RG7_q, SP_q;

  Decoder #(.select(4), .disabled(0)) decoder_1 (
    .out0(decoder_1_out0), .out1(decoder_1_out1), .out2(decoder_1_out2), .out3(decoder_1_out3),
    .out4(decoder_1_out4), .out5(decoder_1_out5), .out6(decoder_1_out6), .out7(decoder_1_out7),
    .out8(PC_Write), .out9(IO_Write), .out10(FLG_Write), .out11(decoder_1_out11), .out12(decoder_1_out12),
    .out13(decoder_1_out13), .out14(decoder_1_out14), .out15(decoder_1_out15), .sel(Write_Code), .en(Write));
  Register #(.width(16)) RG0 (.D(Write_Bus_Input), .en(decoder_1_out0), .Q(RG0_q), .clk(Clock), .clr(Reset_All));
  Register #(.width(16)) RG1 (.D(Write_Bus_Input), .en(decoder_1_out1), .Q(RG1_q), .clk(Clock), .clr(Reset_All));
  Register #(.width(16)) RG2 (.D(Write_Bus_Input), .en(decoder_1_out2), .Q(RG2_q), .clk(Clock), .clr(Reset_All));
  Register #(.width(16)) RG3 (.D(Write_Bus_Input), .en(decoder_1_out3), .Q(RG3_q), .clk(Clock), .clr(Reset_All));
  Register #(.width(16)) RG4 (.D(Write_Bus_Input), .en(decoder_1_out4), .Q(RG4_q), .clk(Clock), .clr(Reset_All));
  Register #(.width(16)) RG5 (.D(Write_Bus_Input), .en(decoder_1_out5), .Q(RG5_q), .clk(Clock), .clr(Reset_All));
  Register #(.width(16)) RG6 (.D(Write_Bus_Input), .en(decoder_1_out6), .Q(RG6_q), .clk(Clock), .clr(Reset_All));
  Register #(.width(16)) RG7 (.D(Write_Bus_Input), .en(decoder_1_out7), .Q(RG7_q), .clk(Clock), .clr(Reset_All));
  Register #(.width(16)) SP (.D(Write_Bus_Input), .en(decoder_1_out11), .Q(SP_q), .clk(Clock), .clr(Reset_All));
  Register #(.width(16)) HLB (.D(Write_Bus_Input), .en(decoder_1_out12), .Q(HLB_Output), .clk(Clock), .clr(Reset_All));
  Counter #(.width(16), .max('hffff), .ongoal("stay")) CTD (
    .load(Current_UE[0]), .D(Write_Bus_Input), .count(and_1_out), .Q(CTD_q), .clk(Clock), .clr(Reset_All));  // open: carry
  and and_1 (and_1_out, ~decoder_1_out13, Current_UE[0]);  // AND_Gate
  Register #(.width(16)) EPC (.D(Write_Bus_Input), .en(decoder_1_out14), .Q(EPC_q), .clk(Clock), .clr(Reset_All));
  Register #(.width(16)) EXA (.D(Write_Bus_Input), .en(decoder_1_out15), .Q(EXA_q), .clk(Clock), .clr(Reset_All));
  Multiplexer #(.select(4), .width(16), .disabled(0)) multiplexer_1 (
    .in0(RG0_q), .in1(RG1_q), .in2(RG2_q), .in3(RG3_q), .in4(RG4_q), .in5(RG5_q), .in6(RG6_q), .in7(RG7_q),
    .in8(PC_Input), .in9(IO_Input), .in10(FLG_Input), .in11(SP_q),
    .in12({HLB_Output[15:8], controlled_buffer_1_out}), .in13(CTD_q), .in14(EPC_q), .in15(EXA_q),
    .out(Bus_0_Output), .sel(Read0_Code), .en(Read0));
  not not_1 (not_1_out, Current_UE[1]);
  assign controlled_buffer_1_out = not_1_out ? HLB_Output[7:0] : 8'bz;  // Controlled_Buffer controlled_buffer_1
  Pull_Resistor pull_resistor_1 (.node(controlled_buffer_1_out));
  Comparator #(.width(16)) comparator_1 (.a(CTD_q), .b({16{1'b0}}), .eq(comparator_1_eq));  // open: gt, lt
  and and_2 (CTDZ_Event, comparator_1_eq, Current_UE[0]);
  Comparator #(.width(4), .mode("unsigned")) comparator_2 (
    .a(Write_Code), .b(4'b1011), .gt(comparator_2_gt));  // open: eq, lt
  Comparator #(.width(4), .mode("unsigned")) comparator_3 (
    .a(Read0_Code), .b(4'b1101), .gt(comparator_3_gt));  // open: eq, lt
  Comparator #(.width(4), .mode("unsigned")) comparator_4 (
    .a(Read1_Code), .b(4'b1101), .gt(comparator_4_gt));  // open: eq, lt
  Multiplexer #(.select(4), .width(16), .disabled(0)) multiplexer_2 (
    .in0(RG0_q), .in1(RG1_q), .in2(RG2_q), .in3(RG3_q), .in4(RG4_q), .in5(RG5_q), .in6(RG6_q), .in7(RG7_q),
    .in8(PC_Input), .in9(IO_Input), .in10(FLG_Input), .in11(SP_q),
    .in12({HLB_Output[15:8], controlled_buffer_1_out}), .in13(CTD_q), .in14(EPC_q), .in15(EXA_q),
    .out(Bus_1_Output), .sel(Read1_Code), .en(Read1));
  and and_3 (PROR, Current_UE[1], Current_UE[0], or_1_out);
  or or_1 (or_1_out, comparator_2_gt, comparator_3_gt, comparator_4_gt);
  Comparator #(.width(4), .mode("unsigned")) comparator_5 (
    .a(Read0_Code), .b(4'b1001), .eq(comparator_5_eq));  // open: gt, lt
  Comparator #(.width(4), .mode("unsigned")) comparator_6 (
    .a(Read1_Code), .b(4'b1001), .eq(comparator_6_eq));  // open: gt, lt
  and and_4 (and_4_out, Read0, comparator_5_eq);
  or or_2 (I_O_Read, and_4_out, and_5_out);
  and and_5 (and_5_out, comparator_6_eq, Read1);

  // Notes on the sheet:
  //   IntEn
  //   Is User
  //   HLB Masking
  //   CTDZ Detection
  //   PROR Detection
endmodule

module ALU (
  input  Immediate_Op,
  input  [15:0] Input_A,
  input  Carry_Input,
  input  [3:0] OpCode,
  input  ALU_Enable,
  input  [15:0] Input_B,
  input  [3:0] Immediate,
  output [15:0] Output,
  output Overflow,
  output Carry_Out,
  output Sign,
  output Zero
);

  wire adder_1_cout, adder_2_cout, and_2_out, and_3_out, and_4_out, bitselector_1_out, comparator_1_lt,
       comparator_2_lt, comparator_3_lt, comparator_4_lt, comparator_5_eq, comparator_6_lt, comparator_7_lt,
       comparator_8_lt, subtractor_1_bout, subtractor_2_bout, xnor_1_out, xnor_2_out, xor_2_out, xor_3_out,
       xor_4_out, xor_5_out, xor_6_out;
  wire [3:0] bit_extender_1_out, bit_extender_4_out, bit_extender_5_out, bit_extender_7_out,
       priority_encoder_1_out;
  wire [15:0] adder_1_out, adder_2_out, and_1_out, bit_extender_2_out, bit_extender_3_out,
       bit_extender_6_out, divider_1_rem, divider_2_out, divider_2_rem, multiplexer_1_out, multiplexer_2_out,
       multiplier_1_cout, multiplier_2_cout, multiplier_2_out, negator_1_out, not_1_out, or_1_out,
       shifter_1_out, shifter_2_out, shifter_3_out, subtractor_1_out, subtractor_2_out, xor_1_out;

  Bit_Extender #(.in_width(16), .out_width(4)) bit_extender_1 (.in(multiplexer_1_out), .out(bit_extender_1_out));
  Multiplexer #(.width(16), .enable("false")) multiplexer_1 (
    .in0(Input_B), .in1(bit_extender_2_out), .out(multiplexer_1_out), .sel(Immediate_Op));
  assign bit_extender_2_out = {{12{1'b0}}, Immediate};  // Bit_Extender bit_extender_2
  Shifter #(.width(16)) shifter_1 (.in(16'h1), .\dist (bit_extender_1_out), .out(shifter_1_out));
  Comparator #(.width(16)) comparator_1 (.a(Input_A), .b({16{1'b0}}), .lt(comparator_1_lt));  // open: gt, eq
  Comparator #(.width(16)) comparator_2 (.a(multiplexer_1_out), .b({16{1'b0}}), .lt(comparator_2_lt));  // open: gt, eq
  Priority_Encoder #(.select(4), .disabled(0)) priority_encoder_1 (
    .in0(multiplexer_1_out[0]), .in1(multiplexer_1_out[1]), .in2(multiplexer_1_out[2]),
    .in3(multiplexer_1_out[3]), .in4(multiplexer_1_out[4]), .in5(multiplexer_1_out[5]),
    .in6(multiplexer_1_out[6]), .in7(multiplexer_1_out[7]), .in8(multiplexer_1_out[8]),
    .in9(multiplexer_1_out[9]), .in10(multiplexer_1_out[10]), .in11(multiplexer_1_out[11]),
    .in12(multiplexer_1_out[12]), .in13(multiplexer_1_out[13]), .in14(multiplexer_1_out[14]),
    .in15(multiplexer_1_out[15]), .out(priority_encoder_1_out));  // open: gs, en_out, en_in
  Multiplier #(.width(16)) multiplier_1 (.a(Input_A), .b(shifter_1_out), .cout(multiplier_1_cout));  // open: out, cin
  Comparator #(.width(16), .mode("unsigned")) comparator_3 (
    .a({16{1'b0}}), .b(multiplier_1_cout), .lt(comparator_3_lt));  // open: gt, eq
  Comparator #(.width(16), .mode("unsigned")) comparator_4 (
    .a({16{1'b0}}), .b(divider_1_rem), .lt(comparator_4_lt));  // open: gt, eq
  Divider #(.width(16)) divider_1 (.a(Input_A), .b(shifter_1_out), .rem(divider_1_rem));  // open: out, upper
  assign bit_extender_3_out = {{12{1'b0}}, priority_encoder_1_out};  // Bit_Extender bit_extender_3
  assign and_1_out = multiplexer_1_out & Input_A;  // AND_Gate and_1, 16 bits wide
  assign or_1_out = Input_A | multiplexer_1_out;  // OR_Gate or_1, 16 bits wide
  assign xor_1_out = multiplexer_1_out ^ Input_A;  // XOR_Gate xor_1, 16 bits wide
  Shifter #(.width(16)) shifter_2 (.in(Input_A), .\dist (bit_extender_4_out), .out(shifter_2_out));
  Bit_Extender #(.in_width(16), .out_width(4)) bit_extender_4 (.in(multiplexer_1_out), .out(bit_extender_4_out));
  Shifter #(.width(16), .shift("lr")) shifter_3 (.in(Input_A), .\dist (bit_extender_5_out), .out(shifter_3_out));
  Bit_Extender #(.in_width(16), .out_width(4)) bit_extender_5 (.in(multiplexer_1_out), .out(bit_extender_5_out));
  assign bit_extender_6_out = {{15{1'b0}}, bitselector_1_out};  // Bit_Extender bit_extender_6
  BitSelector #(.width(16)) bitselector_1 (.in(Input_A), .out(bitselector_1_out), .sel(bit_extender_7_out));
  Bit_Extender #(.in_width(16), .out_width(4)) bit_extender_7 (.in(multiplexer_1_out), .out(bit_extender_7_out));
  Negator #(.width(16)) negator_1 (.in(multiplexer_1_out), .out(negator_1_out));
  Adder #(.width(16)) adder_1 (
    .a(Input_A), .b(multiplexer_1_out), .out(adder_1_out), .cout(adder_1_cout));  // open: cin
  Subtractor #(.width(16)) subtractor_1 (
    .a(Input_A), .b(multiplexer_1_out), .out(subtractor_1_out), .bout(subtractor_1_bout));  // open: bin
  Multiplier #(.width(16)) multiplier_2 (
    .a(Input_A), .b(multiplexer_1_out), .out(multiplier_2_out), .cout(multiplier_2_cout));  // open: cin
  Divider #(.width(16)) divider_2 (
    .a(Input_A), .b(multiplexer_1_out), .out(divider_2_out), .rem(divider_2_rem));  // open: upper
  xnor xnor_1 (xnor_1_out, comparator_1_lt, comparator_2_lt);
  xor xor_2 (xor_2_out, Sign, comparator_1_lt);
  xor xor_3 (xor_3_out, comparator_1_lt, comparator_2_lt);
  Adder #(.width(16)) adder_2 (
    .a(Input_A), .b(multiplexer_1_out), .out(adder_2_out), .cin(Carry_Input), .cout(adder_2_cout));
  Subtractor #(.width(16)) subtractor_2 (
    .a(Input_A), .b(multiplexer_1_out), .out(subtractor_2_out), .bin(Carry_Input), .bout(subtractor_2_bout));
  and and_2 (and_2_out, xnor_1_out, xor_2_out);
  and and_3 (and_3_out, xor_2_out, xor_3_out);
  xor xor_4 (xor_4_out, comparator_1_lt, comparator_2_lt);
  Comparator #(.width(16), .mode("unsigned")) comparator_5 (
    .a({16{1'b0}}), .b(multiplexer_1_out), .eq(comparator_5_eq));  // open: gt, lt
  assign not_1_out = ~multiplexer_1_out;  // NOT_Gate not_1, 16 bits wide
  xor xor_5 (xor_5_out, Sign, comparator_1_lt);
  xnor xnor_2 (xnor_2_out, comparator_1_lt, Sign);
  xor xor_6 (xor_6_out, Sign, xor_4_out);
  Comparator #(.width(4), .mode("unsigned")) comparator_6 (
    .a(4'b1101), .b(OpCode), .lt(comparator_6_lt));  // open: gt, eq
  Multiplexer #(.select(4), .width(16), .disabled(0), .enable("false")) multiplexer_2 (
    .in0(not_1_out), .in1(and_1_out), .in2(or_1_out), .in3(xor_1_out), .in4(shifter_2_out),
    .in5(shifter_3_out), .in6(bit_extender_6_out), .in7(bit_extender_3_out), .in8(negator_1_out),
    .in9(adder_1_out), .in10(adder_2_out), .in11(subtractor_1_out), .in12(subtractor_2_out),
    .in13(multiplier_2_out), .in14(divider_2_out), .in15(divider_2_rem), .out(multiplexer_2_out), .sel(OpCode));
  Comparator #(.width(16), .mode("unsigned")) comparator_7 (
    .a({16{1'b0}}), .b(multiplier_2_cout), .lt(comparator_7_lt));  // open: gt, eq
  Comparator #(.width(16), .mode("unsigned")) comparator_8 (
    .a({16{1'b0}}), .b(divider_2_rem), .lt(comparator_8_lt));  // open: gt, eq
  Multiplexer #(.select(4), .enable("false")) multiplexer_3 (
    .in0(1'b0), .in1(1'b0), .in2(1'b0), .in3(1'b0), .in4(xor_5_out), .in5(xor_5_out), .in6(1'b0), .in7(1'b0),
    .in8(xnor_2_out), .in9(and_2_out), .in10(and_2_out), .in11(and_3_out), .in12(and_3_out),
    .in13(xor_6_out), .in14(and_4_out), .in15(and_4_out), .out(Overflow), .sel(OpCode));
  and and_4 (and_4_out, comparator_5_eq, comparator_6_lt);
  Multiplexer #(.select(4), .enable("false")) multiplexer_4 (
    .in0(1'b0), .in1(1'b0), .in2(1'b0), .in3(1'b0), .in4(comparator_3_lt), .in5(comparator_4_lt), .in6(1'b0),
    .in7(1'b0), .in8(1'b0), .in9(adder_1_cout), .in10(adder_2_cout), .in11(subtractor_1_bout),
    .in12(subtractor_2_bout), .in13(comparator_7_lt), .in14(comparator_8_lt), .in15(1'b0), .out(Carry_Out),
    .sel(OpCode));
  assign Output = ALU_Enable ? multiplexer_2_out : 16'bz;  // Controlled_Buffer controlled_buffer_1
  Comparator #(.width(16)) comparator_9 (.a(multiplexer_2_out), .b({16{1'b0}}), .eq(Zero), .lt(Sign));  // open: gt

  // Notes on the sheet:
  //   Bit shifting over/under detection
  //   A
  //   B
  //   Arithmetic overflow logic
  //   Add
  //   Sub
  //   Shift
  //   -A
  //   Mul
  //   Div is always unsigned
  //   So we use divide-by-zero instead
  //   DIV0
endmodule

module Addressing (
  input  [1:0] State_Number,
  input  Adder_Enable,
  input  [1:0] Current_UE,
  input  LO_Enabled,
  input  [15:0] HLB_Input,
  input  [15:0] Data_Bus_Input,
  input  Clock,
  input  Reset,
  input  Write_to_PC,
  input  PC_1,
  input  PC_2,
  output [15:0] RAM_Address,
  output OOB,
  output [15:0] PC_Out
);

  wire comparator_1_gt, decoder_1_out0, decoder_1_out1, decoder_1_out2, or_1_out;
  wire [15:0] adder_1_out, adder_2_out, adder_3_out, Adder_Addr_q, and_1_out, bit_extender_1_out, Buffer_q,
       multiplexer_1_out, multiplexer_2_out, shifter_1_out;

  Decoder #(.select(2), .disabled(0)) decoder_1 (
    .out0(decoder_1_out0), .out1(decoder_1_out1), .out2(decoder_1_out2), .sel(State_Number), .en(Adder_Enable));  // open: out3
  Register #(.width(16)) Buffer (.D(Data_Bus_Input), .en(decoder_1_out0), .Q(Buffer_q), .clk(Clock), .clr(Reset));
  Adder #(.width(16)) adder_1 (.a(PC_Out), .b(16'h1), .out(adder_1_out), .cin(PC_2));  // open: cout
  assign bit_extender_1_out = {{8{1'b0}}, HLB_Input[7:0]};  // Bit_Extender bit_extender_1
  Shifter #(.width(16)) shifter_1 (.in(bit_extender_1_out), .\dist (4'b1000), .out(shifter_1_out));
  assign and_1_out = HLB_Input & 16'hff00;  // AND_Gate and_1, 16 bits wide
  Adder #(.width(16)) adder_2 (.a(Buffer_q), .b(Data_Bus_Input), .out(adder_2_out));  // open: cin, cout
  Multiplexer #(.width(16), .disabled(0), .enable("false")) multiplexer_1 (
    .in0(adder_1_out), .in1(Data_Bus_Input), .out(multiplexer_1_out), .sel(Write_to_PC));
  Register #(.width(16)) PC (.D(multiplexer_1_out), .en(or_1_out), .Q(PC_Out), .clk(Clock), .clr(Reset));
  or or_1 (or_1_out, Write_to_PC, PC_1, PC_2);
  Adder #(.width(16)) adder_3 (.a(shifter_1_out), .b(multiplexer_2_out), .out(adder_3_out));  // open: cin, cout
  Multiplexer #(.width(16), .disabled(0), .enable("false")) multiplexer_2 (
    .in0(PC_Out), .in1(Adder_Addr_q), .out(multiplexer_2_out), .sel(decoder_1_out2));
  Register #(.width(16)) Adder_Addr (.D(adder_2_out), .en(decoder_1_out1), .Q(Adder_Addr_q), .clk(Clock), .clr(Reset));
  Multiplexer #(.width(16), .disabled(0), .enable("false")) multiplexer_3 (
    .in0(multiplexer_2_out), .in1(adder_3_out), .out(RAM_Address), .sel(LO_Enabled));
  Comparator #(.width(16), .mode("unsigned")) comparator_1 (
    .a(multiplexer_2_out), .b(and_1_out), .gt(comparator_1_gt));  // open: eq, lt
  and and_2 (OOB, Current_UE[0], Current_UE[1], comparator_1_gt);
endmodule

module System_Flags (
  input  UE_Push,
  input  UE_Pop,
  input  [15:0] Input,
  input  Write_Flags_Async,
  input  Write_ALU_Flags,
  input  [3:0] ALU_Flag_In,
  input  Clock,
  input  Reset_All,
  input  Set_LOEn,
  input  Reset_LOEn,
  input  [7:0] Exception_Lines,
  input  Clear_EX_Buffer,
  output [1:0] Current_IsUser_IntEn_Flags,
  output [15:0] Output,
  output [3:0] ALU_Flags_Out,
  output [4:0] IOP_Output,
  output LO_Enabled,
  output Exception,
  output Non_Ignorable_Exception
);

  wire and_1_out, KWrite, or_2_out, or_3_out, or_4_out, or_5_out;
  wire [1:0] multiplexer_1_out, multiplexer_2_out, multiplexer_3_out, multiplexer_6_out, UiEp_q;
  wire [2:0] EXC_q, multiplexer_5_out, priority_encoder_1_out;
  wire [3:0] multiplexer_4_out;
  wire [7:0] Exception_Buffer_q, or_1_out;
  wire [15:0] and_3_out;

  Pull_Resistor pull_resistor_1 (.node(Exception_Lines));
  Multiplexer #(.width(2), .disabled(0), .enable("false")) multiplexer_1 (
    .in0(2'b00), .in1(Current_IsUser_IntEn_Flags), .out(multiplexer_1_out), .sel(UE_Push));
  assign or_1_out = Exception_Lines | Exception_Buffer_q;  // OR_Gate or_1, 8 bits wide
  or or_2 (or_2_out, and_1_out, Reset_All);
  and and_1 (and_1_out, ~Clock, Clear_EX_Buffer);  // AND_Gate
  Multiplexer #(.width(2), .disabled(0), .enable("false")) multiplexer_2 (
    .in0(multiplexer_1_out), .in1(Input[3:2]), .out(multiplexer_2_out), .sel(KWrite));
  Register #(.width(2)) UiEp (.D(multiplexer_2_out), .en(or_3_out), .Q(UiEp_q), .clk(Clock), .clr(Reset_All));
  or or_3 (or_3_out, KWrite, UE_Pop, UE_Push);
  and and_2 (KWrite, ~Current_IsUser_IntEn_Flags[1], ~Exception, Write_Flags_Async);  // AND_Gate
  Register #(.trigger("low")) Exception_Buffer (
    .D(or_1_out), .en(1'b1), .Q(Exception_Buffer_q), .clk(Clock), .clr(or_2_out));
  Multiplexer #(.width(2), .disabled(0), .enable("false")) multiplexer_3 (
    .in0(UiEp_q), .in1(2'b00), .out(multiplexer_3_out), .sel(UE_Push));
  Multiplexer #(.width(4), .disabled(0), .enable("false")) multiplexer_4 (
    .in0(Input[7:4]), .in1(ALU_Flag_In), .out(multiplexer_4_out), .sel(Write_ALU_Flags));
  or or_4 (or_4_out, Write_Flags_Async, Write_ALU_Flags);
  S_R_Flip_Flop LOEn (
    .S(Set_LOEn), .clk(Clock), .R(Reset_LOEn), .Q(LO_Enabled), .reset(Reset_All), .en(1'b1));  // open: Qn, preset
  Multiplexer #(.width(3), .disabled(0), .enable("false")) multiplexer_5 (
    .in0(priority_encoder_1_out), .in1(Input[10:8]), .out(multiplexer_5_out), .sel(KWrite));
  or or_5 (or_5_out, KWrite, Exception);
  Priority_Encoder #(.disabled(0)) priority_encoder_1 (
    .in0(Exception_Buffer_q[0]), .in1(Exception_Buffer_q[1]), .in2(Exception_Buffer_q[2]),
    .in3(Exception_Buffer_q[3]), .in4(Exception_Buffer_q[4]), .in5(Exception_Buffer_q[5]),
    .in6(Exception_Buffer_q[6]), .in7(Exception_Buffer_q[7]), .out(priority_encoder_1_out), .en_in(1'b1),
    .gs(Exception));  // open: en_out
  Comparator #(.mode("unsigned")) comparator_1 (
    .a(Exception_Buffer_q), .b(8'h3f), .gt(Non_Ignorable_Exception));  // open: eq, lt
  Register #(.width(2)) UiEc (
    .D(multiplexer_6_out), .en(or_3_out), .Q(Current_IsUser_IntEn_Flags), .clk(Clock), .clr(Reset_All));
  Multiplexer #(.width(2), .disabled(0), .enable("false")) multiplexer_6 (
    .in0(multiplexer_3_out), .in1(Input[1:0]), .out(multiplexer_6_out), .sel(KWrite));
  Register #(.width(4)) ALUF (.D(multiplexer_4_out), .en(or_4_out), .Q(ALU_Flags_Out), .clk(Clock), .clr(Reset_All));
  Register #(.width(5)) IOP (.D(Input[15:11]), .en(Write_Flags_Async), .Q(IOP_Output), .clk(Clock), .clr(Reset_All));
  Register #(.width(3)) EXC (.D(multiplexer_5_out), .en(or_5_out), .Q(EXC_q), .clk(Clock), .clr(Reset_All));
  Multiplexer #(.width(16), .disabled(0), .enable("false")) multiplexer_7 (
    .in0({IOP_Output, EXC_q, ALU_Flags_Out, UiEp_q, Current_IsUser_IntEn_Flags}), .in1(and_3_out),
    .out(Output), .sel(Current_IsUser_IntEn_Flags[1]));
  assign and_3_out = {IOP_Output, EXC_q, ALU_Flags_Out, UiEp_q, Current_IsUser_IntEn_Flags} & 16'hf8f0;  // AND_Gate and_3, 16 bits wide

  // Other names for the same wires on the sheet: U = Current_IsUser_IntEn_Flags[1]

  // Notes on the sheet:
  //   write
  //   write
  //   write
  //   EXC contains the code for the current highest-priority exception.
  //   NOTE: If EXtr, do not block writing! Very bad!
  //   Exceptions: The lines are fed through an accumulation buffer, which is fed through a priority encoder.
  //   EXtr disables interrupts and clears the buffer, which has the effect of "freezing" EXC.
  //   This means that only the highest priority exception is dealt with each time EXtr occurs.
  //   This also means EXtr can occur multiple times in a row if an exception needs taken care of.
  //   Non-ignorable exceptions block all writing from happening in the CPU.
endmodule

module Control_Unit (
  input  [7:0] Jump_Conditions,
  input  [15:0] RAM_Input,
  input  Clock_In,
  input  Reset_All,
  input  Start,
  input  Pause,
  input  EX,
  input  [1:0] UE,
  input  Non_Ignorable_EX,
  output PC_1,
  output PC_2,
  output RAM_to_Bus,
  output [1:0] State_Out,
  output Read0_to_RAM,
  output Read1_to_Bus,
  output To_Process,
  output To_Kernel,
  output ALU_Enable,
  output Clock_Out,
  output ALU_Flag_Write,
  output ALU_Immediate,
  output [3:0] ALU_OpCode,
  output Is_On,
  output [3:0] Write_Code,
  output Write,
  output [3:0] Read0_Code,
  output Read0,
  output [3:0] Read1_Code,
  output Read1,
  output SYS_Exception,
  output PRIN_Exception,
  output Adder_Enable
);

  wire and_1_out, and_2_out, and_3_out, and_5_out, and_6_out, and_7_out, and_8_out, and_11_out, and_15_out,
       comparator_1_eq, decoder_1_out0, decoder_1_out1, decoder_1_out2, decoder_2_out0, decoder_2_out1,
       decoder_3_out0, decoder_3_out1, decoder_3_out2, decoder_3_out3, decoder_3_out4, decoder_3_out5,
       decoder_3_out6, decoder_3_out7, demultiplexer_1_out0, demultiplexer_1_out1, demultiplexer_2_out0,
       demultiplexer_2_out1, demultiplexer_3_out0, demultiplexer_3_out1, demultiplexer_4_out0,
       demultiplexer_4_out1, demultiplexer_5_out0, demultiplexer_5_out1, demultiplexer_6_out0,
       demultiplexer_6_out1, demultiplexer_7_out0, demultiplexer_7_out1, EX_q, multiplexer_1_out, not_1_out,
       not_2_out, ON_Buffer_q, ON_Buffer_qn, or_1_out, or_2_out, or_3_out, or_4_out, or_5_out,
       priority_encoder_1_gs, priority_encoder_2_gs, priority_encoder_3_gs, xor_1_out;
  wire [1:0] priority_encoder_3_out, pull_resistor_3_node;
  wire [3:0] pull_resistor_1_node;
  wire [15:0] Fetch_q;
  wire [17:5] pull_resistor_2_node;

  S_R_Flip_Flop ON_Buffer (
    .Q(ON_Buffer_q), .Qn(ON_Buffer_qn), .preset(Start), .reset(or_1_out));  // open: S, clk, R, en
  or or_1 (or_1_out, Pause, and_3_out, Reset_All);
  Register #(.width(16), .trigger("high")) Fetch (
    .D(RAM_Input), .en(or_2_out), .Q({Fetch_q[15:12], ALU_OpCode, Read0_Code, Fetch_q[3:0]}), .clk(Clock_In),
    .clr(Reset_All));
  or or_2 (or_2_out, decoder_1_out0, ~Is_On);  // OR_Gate
  and and_1 (and_1_out, pull_resistor_2_node[17], Is_On);
  Counter #(.width(2), .max('h3), .ongoal("stay")) State (
    .load(and_1_out), .D(2'b00), .count(and_2_out), .Q(State_Out), .clk(Clock_Out), .clr(Reset_All));  // open: carry
  and and_2 (and_2_out, Is_On, ~pull_resistor_2_node[17]);  // AND_Gate
  S_R_Flip_Flop #(.trigger("falling")) ON (
    .S(ON_Buffer_q), .clk(Clock_In), .R(ON_Buffer_qn), .Q(Is_On), .reset(Reset_All));  // open: Qn, preset, en
  and and_3 (and_3_out, ~Clock_Out, Is_On, pull_resistor_2_node[14]);  // AND_Gate
  Decoder #(.select(2), .disabled(0)) decoder_1 (
    .out0(decoder_1_out0), .out1(decoder_1_out1), .out2(decoder_1_out2), .sel(State_Out), .en(Is_On));  // open: out3
  and and_4 (Clock_Out, Clock_In, Is_On);
  D_Flip_Flop #(.trigger("high")) u_EX (
    .clk(Clock_Out), .D(EX), .Q(EX_q), .en(decoder_1_out0), .reset(Reset_All));  // open: Qn, preset
  Decoder #(.disabled(0)) decoder_2 (.out0(decoder_2_out0), .out1(decoder_2_out1), .sel(Fetch_q[15]), .en(and_5_out));
  and and_5 (and_5_out, Is_On, ~EX_q);  // AND_Gate
  Demultiplexer #(.disabled(0)) demultiplexer_1 (
    .out0(demultiplexer_1_out0), .out1(demultiplexer_1_out1), .in(EX_q), .sel(decoder_1_out1), .en(Is_On));
  and and_6 (and_6_out, ~EX_q, Non_Ignorable_EX);  // AND_Gate
  Multiplexer #(.select(3), .disabled(0), .enable("false")) multiplexer_1 (
    .in0(Jump_Conditions[0]), .in1(Jump_Conditions[1]), .in2(Jump_Conditions[2]), .in3(Jump_Conditions[3]),
    .in4(Jump_Conditions[4]), .in5(Jump_Conditions[5]), .in6(Jump_Conditions[6]), .in7(Jump_Conditions[7]),
    .out(multiplexer_1_out), .sel(ALU_OpCode[2:0]));
  xor xor_1 (xor_1_out, multiplexer_1_out, ALU_OpCode[3]);
  Decoder #(.select(3), .disabled(0)) decoder_3 (
    .out0(decoder_3_out0), .out1(decoder_3_out1), .out2(decoder_3_out2), .out3(decoder_3_out3),
    .out4(decoder_3_out4), .out5(decoder_3_out5), .out6(decoder_3_out6), .out7(decoder_3_out7),
    .sel(Fetch_q[14:12]), .en(decoder_2_out0));
  Demultiplexer #(.disabled(0)) demultiplexer_2 (
    .out0(demultiplexer_2_out0), .out1(demultiplexer_2_out1), .in(decoder_3_out4), .sel(decoder_1_out1),
    .en(not_1_out));
  Demultiplexer #(.disabled(0), .enable("false")) demultiplexer_3 (
    .out0(demultiplexer_3_out0), .out1(demultiplexer_3_out1), .in(decoder_3_out0), .sel(UE[1]));
  Demultiplexer #(.disabled(0), .enable("false")) demultiplexer_4 (
    .out0(demultiplexer_4_out0), .out1(demultiplexer_4_out1), .in(decoder_3_out1), .sel(UE[1]));
  Demultiplexer #(.disabled(0), .enable("false")) demultiplexer_5 (
    .out0(demultiplexer_5_out0), .out1(demultiplexer_5_out1), .in(demultiplexer_2_out0), .sel(xor_1_out));
  or or_3 (or_3_out, demultiplexer_5_out1, demultiplexer_6_out0);
  Demultiplexer #(.disabled(0)) demultiplexer_6 (
    .out0(demultiplexer_6_out0), .out1(demultiplexer_6_out1), .in(decoder_3_out5), .sel(decoder_1_out1),
    .en(not_1_out));
  not not_1 (not_1_out, decoder_1_out2);
  Demultiplexer #(.disabled(0)) demultiplexer_7 (
    .out0(demultiplexer_7_out0), .out1(demultiplexer_7_out1), .in(or_4_out), .sel(decoder_1_out1),
    .en(not_1_out));
  or or_4 (or_4_out, decoder_3_out6, decoder_3_out7);
  and and_7 (and_7_out, decoder_3_out6, decoder_1_out2);
  and and_8 (and_8_out, decoder_1_out2, decoder_3_out7);
  or or_5 (or_5_out, demultiplexer_4_out1, demultiplexer_3_out1);
  Pull_Resistor pull_resistor_1 (.node(pull_resistor_1_node));
  Priority_Encoder #(.select(4)) priority_encoder_1 (
    .in0(demultiplexer_3_out0), .in1(demultiplexer_4_out0), .in2(decoder_3_out2), .in3(decoder_3_out3),
    .in4(demultiplexer_5_out0), .in5(or_3_out), .in6(demultiplexer_2_out1), .in7(demultiplexer_6_out1),
    .in8(demultiplexer_7_out0), .in9(demultiplexer_7_out1), .in10(and_7_out), .in11(and_8_out),
    .in12(decoder_2_out1), .in13(demultiplexer_1_out0), .in14(demultiplexer_1_out1), .in15(or_5_out),
    .out(pull_resistor_1_node), .gs(priority_encoder_1_gs), .en_in(Is_On));  // open: en_out
  Pull_Resistor pull_resistor_2 (.node({pull_resistor_2_node[17], PC_1, PC_2, pull_resistor_2_node[14], SYS_Exception, ALU_Enable, Adder_Enable, PRIN_Exception, pull_resistor_2_node[9:5], Read0_to_RAM, Read1_to_Bus, RAM_to_Bus, To_Process, To_Kernel}));
  ROM #(.addrWidth(4), .dataWidth(18)) rom_1 (
    .addr(pull_resistor_1_node),
    .data({pull_resistor_2_node[17], PC_1, PC_2, pull_resistor_2_node[14], SYS_Exception, ALU_Enable, Adder_Enable, PRIN_Exception, pull_resistor_2_node[9:5], Read0_to_RAM, Read1_to_Bus, RAM_to_Bus, To_Process, To_Kernel}),
    .sel(priority_encoder_1_gs));
  Pull_Resistor pull_resistor_3 (.node(pull_resistor_3_node));
  Priority_Encoder #(.select(2), .disabled(0)) priority_encoder_2 (
    .in0(pull_resistor_2_node[7]), .in1(pull_resistor_2_node[6]), .in2(pull_resistor_2_node[5]),
    .out(pull_resistor_3_node), .gs(priority_encoder_2_gs));  // open: in3, en_out, en_in
  Priority_Encoder #(.select(2)) priority_encoder_3 (
    .in0(pull_resistor_2_node[8]), .in1(pull_resistor_2_node[5]), .in2(To_Process), .in3(To_Kernel),
    .out(priority_encoder_3_out), .gs(priority_encoder_3_gs));  // open: en_out, en_in
  Pull_Resistor pull_resistor_4 (.node(priority_encoder_3_out));
  not not_2 (not_2_out, Fetch_q[13]);
  and and_9 (ALU_Flag_Write, not_2_out, ALU_Enable);
  and and_10 (ALU_Immediate, ALU_Enable, Fetch_q[12]);
  and and_11 (and_11_out, ALU_Enable, Fetch_q[14]);
  Multiplexer #(.select(2), .width(4), .disabled(0), .enable("false")) multiplexer_2 (
    .in0(Read0_Code), .in1(4'b1000), .in2(4'b1110), .out(Write_Code), .sel(pull_resistor_3_node));  // open: in3
  Multiplexer #(.select(2), .width(4), .disabled(0), .enable("false")) multiplexer_3 (
    .in0(Fetch_q[3:0]), .in1(4'b1000), .in2(4'b1110), .in3(4'b1111), .out(Read1_Code),
    .sel(priority_encoder_3_out));
  Comparator #(.width(4), .mode("unsigned")) comparator_1 (
    .a(Read0_Code), .b(Fetch_q[3:0]), .eq(comparator_1_eq));  // open: gt, lt
  and and_12 (Write, ~and_6_out, ~and_11_out, priority_encoder_2_gs);  // AND_Gate
  and and_13 (Read0, ~and_6_out, pull_resistor_2_node[9]);  // AND_Gate
  and and_14 (Read1, ~ALU_Immediate, ~and_6_out, priority_encoder_3_gs, ~and_15_out);  // AND_Gate
  and and_15 (and_15_out, Adder_Enable, decoder_3_out7, comparator_1_eq);

  // Notes on the sheet:
  //   Halt
  //   ALU
  //   No writing
  //   HLT
  //   RSM
  //   SYS
  //   MOV
  //   JIF
  //   LDI
  //   LOD
  //   STR
  //   SYS
  //   MOV
  //   JIF Fail
  //   PC+1
  //   JMP
  //   LDI St1
  //   MEM St0
  //   MEM St1
  //   LOD St2
  //   STR St2
  //   ALU
  //   ExTr St0
  //   HLT
  //   RSM
  //   Instruction Decoder
  //   contents of rom_1 (hex, n*v repeats v):
  //   34000 2004a 32000 30188 28000 10000 20044 30084 10908 10804 20884 20a10 31380 28 20049 30400
  //   ________________
  //   ________________
  //   ________________
  //   ________________
  //   For storing directly to an address.
  //   PC
  //   EPC
  //   PC
  //   EPC
  //   EXA
endmodule
