// Digital circuit Assembly Workspace.dig as structural Verilog
module Assembly_Workspace (
  input  clk
);

  wire button_1_out, telescope_assembler_computer_1_output_write, telescope_assembler_computer_1_running,
       telescope_assembler_computer_1_terminal_write;
  wire [6:0] telescope_assembler_computer_1_terminal_data, Text_Input_d;
  wire [15:0] telescope_assembler_computer_1_output_address, telescope_assembler_computer_1_output_data;
  wire [23:0] telescope_assembler_computer_1_text_address;

  ROM #(.AddrBits(24), .Bits(7)) Text_Input (
    .A(telescope_assembler_computer_1_text_address), .sel(1'b1), .D(Text_Input_d));
  Button button_1 (.out(button_1_out));
  Telescope_Assembler_Computer telescope_assembler_computer_1 (
    .Assemble(button_1_out), .Clock(clk), .Text_Input(Text_Input_d),
    .Running(telescope_assembler_computer_1_running),
    .Text_Address(telescope_assembler_computer_1_text_address),
    .Output_Address(telescope_assembler_computer_1_output_address),
    .Output_Data(telescope_assembler_computer_1_output_data),
    .Output_Write(telescope_assembler_computer_1_output_write),
    .Terminal_Data(telescope_assembler_computer_1_terminal_data),
    .Terminal_Write(telescope_assembler_computer_1_terminal_write));
  LED led_1 (.in(telescope_assembler_computer_1_running));
  EEPROMDualPort #(.AddrBits(16), .Bits(16)) MC_Output (
    .A(telescope_assembler_computer_1_output_address), .Din(telescope_assembler_computer_1_output_data),
    .str(telescope_assembler_computer_1_output_write), .C(clk), .ld(1'b0));  // open: D
  Terminal #(.termWidth(130), .termHeight(40)) terminal_1 (
    .D(telescope_assembler_computer_1_terminal_data), .C(clk),
    .en(telescope_assembler_computer_1_terminal_write));

  // Notes on the sheet:
  //   clk: Hz: 2147483647
  //   Make sure MC Output is cleared (and make sure to press OK)
endmodule
