// Digital circuit TNET.dig as structural Verilog
module TNET (
  input  [15:0] PC_Di,
  input  PC_Ri,
  input  PC_Wi,
  input  [15:0] IO_Di,
  input  IO_Ri,
  input  IO_Wi,
  input  Ovr,
  input  Clk_Outb,
  input  Clk_Inb,
  output PC_Ro,
  output PC_Wo,
  output [15:0] PC_Do,
  output IO_Ro,
  output IO_Wo,
  output [15:0] IO_Do
);

  wire Inb_Full_nq, Inb_Full_q, multiplexer_3_out, multiplexer_5_out;
  wire [15:0] driver_1_out, driver_2_out, Inb_q, Out_q;

  Multiplexer #(.Bits(16)) multiplexer_1 (.sel(Ovr), .in_0(driver_2_out), .in_1(driver_1_out), .out(PC_Do));
  Multiplexer multiplexer_2 (.sel(Ovr), .in_0(Inb_Full_q), .in_1(IO_Wi), .out(PC_Wo));
  assign driver_1_out = IO_Wi ? IO_Di : 16'bz;  // Driver driver_1
  PullDown #(.Bits(16)) pulldown_1 (.out(driver_1_out));
  Multiplexer multiplexer_3 (.sel(IO_Wo), .in_0(Clk_Outb), .in_1(Clk_Inb), .out(multiplexer_3_out));
  assign driver_2_out = Inb_Full_q ? Inb_q : 16'bz;  // Driver driver_2
  PullDown #(.Bits(16)) pulldown_2 (.out(driver_2_out));
  Register #(.Bits(16)) Out (.D(PC_Di), .C(Clk_Outb), .en(PC_Wi), .Q(Out_q));
  RS_FF Out_Full (.S(PC_Wi), .C(multiplexer_3_out), .R(IO_Ri), .Q(IO_Wo), .nQ(PC_Ro));
  Register #(.Bits(16)) Inb (.D(IO_Di), .C(multiplexer_5_out), .en(IO_Wi), .Q(Inb_q));
  RS_FF Inb_Full (.S(IO_Wi), .C(Clk_Inb), .R(PC_Ri), .Q(Inb_Full_q), .nQ(Inb_Full_nq));
  Multiplexer multiplexer_4 (.sel(Ovr), .in_0(Inb_Full_nq), .in_1(PC_Ri), .out(IO_Ro));
  assign IO_Do = IO_Wo ? Out_q : 16'bz;  // Driver driver_3
  PullDown #(.Bits(16)) pulldown_3 (.out(IO_Do));
  Multiplexer multiplexer_5 (.sel(Inb_Full_q), .in_0(Clk_Inb), .in_1(Clk_Outb), .out(multiplexer_5_out));

  // Notes on the sheet:
  //   Ovr: Override inbound buffer
  //   All inbound related pin/bus inputs are passed straight to their corresponding output pin/bus.
  //   Inbound
  //   Outbound
endmodule
