// Digital circuit GCPU ALU.dig as structural Verilog
module GCPU_ALU (
  input  Imm_Op,
  input  [15:0] A_In,
  input  Carry_In,
  input  [3:0] OpCode,
  input  ALU_En,
  input  [15:0] B_In,
  input  [3:0] Imm_Value,
  output [15:0] Out,
  output Zero,
  output Sign,
  output Carry_Out,
  output Overflow
);

  wire add_1_c_o, add_2_c_o, and_3_out, and_4_out, and_5_out, and_6_out, bitselector_1_out, comparator_1_eq,
       comparator_2_lt, comparator_3_lt, comparator_4_gt, comparator_5_gt, comparator_6_gt, comparator_7_lt,
       comparator_8_lt, nor_1_out, or_3_out, or_4_out, sub_1_c_o, sub_2_c_o, sub_3_c_o, xnor_1_out,
       xor_2_out, xor_3_out, xor_4_out;
  wire [3:0] multiplexer_1_out;
  wire [4:0] sub_3_s;
  wire [4:4] multiplexer_1_out_2;
  wire [15:0] add_1_s, add_2_s, and_1_out, and_2_out, barrelshifter_1_out, barrelshifter_2_out,
       barrelshifter_3_out, barrelshifter_4_out, decoder_1_out_0, div_1_q, div_1_r, multiplexer_2_out,
       neg_1_out, not_1_out, or_1_out, or_2_out, sub_1_s, sub_2_s, xor_1_out;
  wire [15:5] multiplexer_1_out_3;
  wire [31:0] mul_1_mul;

  Decoder #(.Selector_Bits(4)) decoder_1 (
    .sel(multiplexer_1_out), .out_0(decoder_1_out_0[0]), .out_1(decoder_1_out_0[1]),
    .out_2(decoder_1_out_0[2]), .out_3(decoder_1_out_0[3]), .out_4(decoder_1_out_0[4]),
    .out_5(decoder_1_out_0[5]), .out_6(decoder_1_out_0[6]), .out_7(decoder_1_out_0[7]),
    .out_8(decoder_1_out_0[8]), .out_9(decoder_1_out_0[9]), .out_10(decoder_1_out_0[10]),
    .out_11(decoder_1_out_0[11]), .out_12(decoder_1_out_0[12]), .out_13(decoder_1_out_0[13]),
    .out_14(decoder_1_out_0[14]), .out_15(decoder_1_out_0[15]));
  BitSelector #(.Selector_Bits(4)) bitselector_1 (.in(A_In), .sel(multiplexer_1_out), .out(bitselector_1_out));
  Multiplexer #(.Bits(16)) multiplexer_1 (
    .sel(Imm_Op), .in_0(B_In), .in_1({{12{1'b0}}, Imm_Value}),
    .out({multiplexer_1_out_3, multiplexer_1_out_2[4], multiplexer_1_out}));
  assign or_1_out = A_In | decoder_1_out_0;  // Or or_1, 16 bits wide
  assign and_1_out = A_In & ~decoder_1_out_0;  // And and_1, 16 bits wide
  Comparator #(.Bits(16)) comparator_1 (
    .a({16{1'b0}}), .b({multiplexer_1_out_3, multiplexer_1_out_2[4], multiplexer_1_out}), .eq(comparator_1_eq));  // open: gt, lt
  assign not_1_out = ~{multiplexer_1_out_3, multiplexer_1_out_2[4], multiplexer_1_out};  // Not not_1, 16 bits wide
  assign and_2_out = A_In & {multiplexer_1_out_3, multiplexer_1_out_2[4], multiplexer_1_out};  // And and_2, 16 bits wide
  assign or_2_out = A_In | {multiplexer_1_out_3, multiplexer_1_out_2[4], multiplexer_1_out};  // Or or_2, 16 bits wide
  assign xor_1_out = A_In ^ {multiplexer_1_out_3, multiplexer_1_out_2[4], multiplexer_1_out};  // XOr xor_1, 16 bits wide
  BarrelShifter #(.Bits(16)) barrelshifter_1 (
    .in(A_In), .shift({multiplexer_1_out_2[4], multiplexer_1_out}), .out(barrelshifter_1_out));
  BarrelShifter #(.Bits(16), .direction("right")) barrelshifter_2 (
    .in(A_In), .shift({multiplexer_1_out_2[4], multiplexer_1_out}), .out(barrelshifter_2_out));
  Neg #(.Bits(16)) neg_1 (.in({multiplexer_1_out_3, multiplexer_1_out_2[4], multiplexer_1_out}), .out(neg_1_out));
  Add #(.Bits(16)) add_1 (
    .a(A_In), .b({multiplexer_1_out_3, multiplexer_1_out_2[4], multiplexer_1_out}), .c_i(1'b0), .s(add_1_s),
    .c_o(add_1_c_o));
  Add #(.Bits(16)) add_2 (
    .a(A_In), .b({multiplexer_1_out_3, multiplexer_1_out_2[4], multiplexer_1_out}), .c_i(Carry_In),
    .s(add_2_s), .c_o(add_2_c_o));
  Sub #(.Bits(16)) sub_1 (
    .a(A_In), .b({multiplexer_1_out_3, multiplexer_1_out_2[4], multiplexer_1_out}), .c_i(1'b0), .s(sub_1_s),
    .c_o(sub_1_c_o));
  Sub #(.Bits(16)) sub_2 (
    .a(A_In), .b({multiplexer_1_out_3, multiplexer_1_out_2[4], multiplexer_1_out}), .c_i(Carry_In),
    .s(sub_2_s), .c_o(sub_2_c_o));
  Mul #(.Bits(16)) mul_1 (
    .a(A_In), .b({multiplexer_1_out_3, multiplexer_1_out_2[4], multiplexer_1_out}), .mul(mul_1_mul));
  Div #(.Bits(16)) div_1 (
    .a(A_In), .b({multiplexer_1_out_3, multiplexer_1_out_2[4], multiplexer_1_out}), .q(div_1_q), .r(div_1_r));
  xnor xnor_1 (xnor_1_out, Sign, multiplexer_1_out_3[15]);
  nor nor_1 (nor_1_out, A_In[15], multiplexer_1_out_3[15]);
  xor xor_2 (xor_2_out, A_In[15], multiplexer_1_out_3[15]);
  xor xor_3 (xor_3_out, Sign, A_In[15]);
  Comparator #(.Bits(4)) comparator_2 (.a(4'b1101), .b(OpCode), .lt(comparator_2_lt));  // open: gt, eq
  and and_3 (and_3_out, comparator_1_eq, comparator_2_lt);
  and and_4 (and_4_out, nor_1_out, xor_3_out);
  and and_5 (and_5_out, xor_3_out, xor_2_out);
  xor xor_4 (xor_4_out, Sign, xor_2_out);
  Comparator #(.Bits(16)) comparator_3 (.a({16{1'b0}}), .b(A_In), .lt(comparator_3_lt));  // open: gt, eq
  Sub #(.Bits(5)) sub_3 (
    .a(5'b10000), .b({multiplexer_1_out_2[4], multiplexer_1_out}), .c_i(1'b0), .s(sub_3_s), .c_o(sub_3_c_o));
  Comparator #(.Bits(16)) comparator_4 (.a(mul_1_mul[31:16]), .b({16{1'b0}}), .gt(comparator_4_gt));  // open: eq, lt
  Comparator #(.Bits(16)) comparator_5 (.a(div_1_r), .b({16{1'b0}}), .gt(comparator_5_gt));  // open: eq, lt
  Comparator #(.Bits(16)) comparator_6 (.a(div_1_q), .b({16{1'b0}}), .gt(comparator_6_gt));  // open: eq, lt
  and and_6 (and_6_out, comparator_3_lt, sub_3_c_o);
  BarrelShifter #(.Bits(16), .direction("right")) barrelshifter_3 (
    .in(A_In), .shift(sub_3_s), .out(barrelshifter_3_out));
  BarrelShifter #(.Bits(16)) barrelshifter_4 (.in(A_In), .shift(sub_3_s), .out(barrelshifter_4_out));
  Multiplexer #(.Selector_Bits(4), .Bits(16)) multiplexer_2 (
    .sel(OpCode), .in_0(not_1_out), .in_1(and_2_out), .in_2(or_2_out), .in_3(xor_1_out),
    .in_4(barrelshifter_1_out), .in_5(barrelshifter_2_out), .in_6(or_1_out), .in_7(and_1_out),
    .in_8(neg_1_out), .in_9(add_1_s), .in_10(add_2_s), .in_11(sub_1_s), .in_12(sub_2_s),
    .in_13(mul_1_mul[15:0]), .in_14(div_1_q), .in_15(div_1_r), .out(multiplexer_2_out));
  Comparator #(.Bits(16)) comparator_7 (.a({16{1'b0}}), .b(barrelshifter_3_out), .lt(comparator_7_lt));  // open: gt, eq
  Comparator #(.Bits(16)) comparator_8 (.a({16{1'b0}}), .b(barrelshifter_4_out), .lt(comparator_8_lt));  // open: gt, eq
  Multiplexer #(.Selector_Bits(4)) multiplexer_3 (
    .sel(OpCode), .in_0(1'b0), .in_1(1'b0), .in_2(1'b0), .in_3(1'b0), .in_4(xor_3_out), .in_5(xor_3_out),
    .in_6(1'b0), .in_7(1'b0), .in_8(xnor_1_out), .in_9(and_4_out), .in_10(and_4_out), .in_11(and_5_out),
    .in_12(and_5_out), .in_13(xor_4_out), .in_14(and_3_out), .in_15(and_3_out), .out(Overflow));
  or or_3 (or_3_out, and_6_out, comparator_7_lt);
  or or_4 (or_4_out, and_6_out, comparator_8_lt);
  Comparator #(.Signed("true"), .Bits(16)) comparator_9 (
    .a(multiplexer_2_out), .b({16{1'b0}}), .eq(Zero), .lt(Sign));  // open: gt
  Multiplexer #(.Selector_Bits(4)) multiplexer_4 (
    .sel(OpCode), .in_0(1'b0), .in_1(1'b0), .in_2(1'b0), .in_3(1'b0), .in_4(or_3_out), .in_5(or_4_out),
    .in_6(bitselector_1_out), .in_7(bitselector_1_out), .in_8(1'b0), .in_9(add_1_c_o), .in_10(add_2_c_o),
    .in_11(sub_1_c_o), .in_12(sub_2_c_o), .in_13(comparator_4_gt), .in_14(comparator_5_gt),
    .in_15(comparator_6_gt), .out(Carry_Out));
  assign Out = ALU_En ? multiplexer_2_out : 16'bz;  // Driver driver_1
  // Probe ALU on Out

  // Notes on the sheet:
  //   Carry of SET & UST is SEL
  //   SET & UST
  //   Sign
  //   Div is unsigned, so we use DIV0 instead
  //   DIV0
  //   -B
  //   Shift
  //   Add
  //   Sub
  //   Mul
  //   Shift Over/Under
endmodule
