// Digital circuit GCPU Selection & Registers.dig as structural Verilog
module GCPU_Selection___Registers (
  input  [15:0] Data_In,
  input  Clock,
  input  [1:0] Cur_UE,
  input  [15:0] PC_In,
  input  [15:0] IO_In,
  input  [15:0] FLG_In,
  input  [3:0] Write,
  input  Write_2,
  input  [3:0] Read0,
  input  Read0_2,
  input  [3:0] Read1,
  input  Read1_2,
  input  PROR_Override,
  output CTDZ,
  output Write_PC,
  output Write_FLG,
  output [15:0] Out0,
  output [15:0] Out1,
  output PROR,
  output [15:0] HLB,
  output Read_I_O,
  output Write_IO
);

  wire and_1_out, and_3_out, and_4_out, comparator_1_gt, comparator_2_gt, comparator_3_gt, comparator_4_eq,
       comparator_5_eq, demultiplexer_1_out_0, demultiplexer_1_out_1, demultiplexer_1_out_2,
       demultiplexer_1_out_3, demultiplexer_1_out_4, demultiplexer_1_out_5, demultiplexer_1_out_6,
       demultiplexer_1_out_7, demultiplexer_1_out_11, demultiplexer_1_out_12, demultiplexer_1_out_13,
       demultiplexer_1_out_14, demultiplexer_1_out_15, or_1_out;
  wire [7:0] driverinvsel_1_out;
  wire [15:0] CTD_out, EPC_q, EXA_q, multiplexer_1_out, multiplexer_2_out, OUT__RG6_q, RA__RG7_q, RG0_q,
       RG1_q, RG2_q, RG3_q, SF0__RG4_q, SF1__RG5_q, SP_q;

  Demultiplexer #(.Selector_Bits(4)) demultiplexer_1 (
    .sel(Write), .in(Write_2), .out_0(demultiplexer_1_out_0), .out_1(demultiplexer_1_out_1),
    .out_2(demultiplexer_1_out_2), .out_3(demultiplexer_1_out_3), .out_4(demultiplexer_1_out_4),
    .out_5(demultiplexer_1_out_5), .out_6(demultiplexer_1_out_6), .out_7(demultiplexer_1_out_7),
    .out_8(Write_PC), .out_9(Write_IO), .out_10(Write_FLG), .out_11(demultiplexer_1_out_11),
    .out_12(demultiplexer_1_out_12), .out_13(demultiplexer_1_out_13), .out_14(demultiplexer_1_out_14),
    .out_15(demultiplexer_1_out_15));
  Comparator #(.Bits(4)) comparator_1 (.a(Read0), .b(4'b1101), .gt(comparator_1_gt));  // open: eq, lt
  Comparator #(.Bits(4)) comparator_2 (.a(Read1), .b(4'b1101), .gt(comparator_2_gt));  // open: eq, lt
  Comparator #(.Bits(4)) comparator_3 (.a(Write), .b(4'b1011), .gt(comparator_3_gt));  // open: eq, lt
  or or_1 (or_1_out, comparator_1_gt, comparator_2_gt, comparator_3_gt);
  Register #(.Bits(16)) RG0 (.D(Data_In), .C(Clock), .en(demultiplexer_1_out_0), .Q(RG0_q));
  Register #(.Bits(16)) RG2 (.D(Data_In), .C(Clock), .en(demultiplexer_1_out_2), .Q(RG2_q));
  Register #(.Bits(16)) SF0__RG4 (.D(Data_In), .C(Clock), .en(demultiplexer_1_out_4), .Q(SF0__RG4_q));
  Register #(.Bits(16)) OUT__RG6 (.D(Data_In), .C(Clock), .en(demultiplexer_1_out_6), .Q(OUT__RG6_q));
  Register #(.Bits(16)) SP (.D(Data_In), .C(Clock), .en(demultiplexer_1_out_11), .Q(SP_q));
  Register #(.Bits(16)) EPC (.D(Data_In), .C(Clock), .en(demultiplexer_1_out_14), .Q(EPC_q));
  Register #(.Bits(16)) RG1 (.D(Data_In), .C(Clock), .en(demultiplexer_1_out_1), .Q(RG1_q));
  Register #(.Bits(16)) RG3 (.D(Data_In), .C(Clock), .en(demultiplexer_1_out_3), .Q(RG3_q));
  Register #(.Bits(16)) SF1__RG5 (.D(Data_In), .C(Clock), .en(demultiplexer_1_out_5), .Q(SF1__RG5_q));
  Register #(.Bits(16)) RA__RG7 (.D(Data_In), .C(Clock), .en(demultiplexer_1_out_7), .Q(RA__RG7_q));
  Register #(.Bits(16)) u_HLB (.D(Data_In), .C(Clock), .en(demultiplexer_1_out_12), .Q(HLB));
  and and_1 (and_1_out, ~CTDZ, Clock);  // And
  Register #(.Bits(16)) EXA (.D(Data_In), .C(Clock), .en(demultiplexer_1_out_15), .Q(EXA_q));
  CounterPreset #(.Bits(16)) CTD (
    .en(Cur_UE[0]), .C(and_1_out), .dir(1'b1), .in(Data_In), .ld(demultiplexer_1_out_13), .clr(1'b0),
    .out(CTD_out), .ovf(CTDZ));
  assign driverinvsel_1_out = ~Cur_UE[1] ? HLB[7:0] : 8'bz;  // DriverInvSel driverinvsel_1
  PullDown #(.Bits(8)) pulldown_1 (.out(driverinvsel_1_out));
  Multiplexer #(.Selector_Bits(4), .Bits(16)) multiplexer_1 (
    .sel(Read0), .in_0(RG0_q), .in_1(RG1_q), .in_2(RG2_q), .in_3(RG3_q), .in_4(SF0__RG4_q),
    .in_5(SF1__RG5_q), .in_6(OUT__RG6_q), .in_7(RA__RG7_q), .in_8(PC_In), .in_9(IO_In), .in_10(FLG_In),
    .in_11(SP_q), .in_12({HLB[15:8], driverinvsel_1_out}), .in_13(CTD_out), .in_14(EPC_q), .in_15(EXA_q),
    .out(multiplexer_1_out));
  Multiplexer #(.Selector_Bits(4), .Bits(16)) multiplexer_2 (
    .sel(Read1), .in_0(RG0_q), .in_1(RG1_q), .in_2(RG2_q), .in_3(RG3_q), .in_4(SF0__RG4_q),
    .in_5(SF1__RG5_q), .in_6(OUT__RG6_q), .in_7(RA__RG7_q), .in_8(PC_In), .in_9(IO_In), .in_10(FLG_In),
    .in_11(SP_q), .in_12({HLB[15:8], driverinvsel_1_out}), .in_13(CTD_out), .in_14(EPC_q), .in_15(EXA_q),
    .out(multiplexer_2_out));
  assign Out0 = Read0_2 ? multiplexer_1_out : 16'bz;  // Driver driver_1
  assign Out1 = Read1_2 ? multiplexer_2_out : 16'bz;  // Driver driver_2
  and and_2 (PROR, or_1_out, Cur_UE[1], ~PROR_Override);  // And
  Comparator #(.Bits(4)) comparator_4 (.a(Read0), .b(4'b1001), .eq(comparator_4_eq));  // open: gt, lt
  Comparator #(.Bits(4)) comparator_5 (.a(Read1), .b(4'b1001), .eq(comparator_5_eq));  // open: gt, lt
  PullDown #(.Bits(16)) pulldown_2 (.out(Out0));
  PullDown #(.Bits(16)) pulldown_3 (.out(Out1));
  and and_3 (and_3_out, Read0_2, comparator_4_eq);
  and and_4 (and_4_out, comparator_5_eq, Read1_2);
  or or_2 (Read_I_O, and_3_out, and_4_out);

  // Notes on the sheet:
  //   PROR Detection
endmodule
