// Digital circuit Glass CPU.dig as structural Verilog
module Glass_CPU (
  input  Start,
  input  Pause,
  input  Clock_In,
  input  [15:0] RAM_Din,
  input  [15:0] I_O_In,
  input  I_O_Reading,
  input  I_O_Writing,
  input  [3:0] Int_Lines,
  input  [3:0] Int_Mask,
  input  Hard_Reset,
  output Running,
  output [15:0] RAM_A,
  output [15:0] RAM_Dout,
  output RAM_Str,
  output [15:0] PC,
  output [15:0] HLB,
  output Kernel,
  output Reading_I_O,
  output [15:0] I_O_Out,
  output Writing_I_O,
  output [4:0] IOP,
  output LO_Enabled
);

  wire and_1_out, and_2_out, and_4_out, and_5_out, and_6_out, delay_1_out, delay_2_out, delay_6_out,
       delay_7_out, delay_8_out, delay_9_out, delay_10_out, delay_11_out, delay_12_out, delay_13_out,
       delay_14_out, delay_15_out, gcpu_cisc_controller_1_p3, gcpu_cisc_controller_1_p5,
       gcpu_cisc_controller_1_p9, gcpu_cisc_controller_1_p10, gcpu_cisc_controller_1_p12,
       gcpu_cisc_controller_1_p13, gcpu_cisc_controller_1_p14, gcpu_cisc_controller_1_p15,
       gcpu_cisc_controller_1_p16, gcpu_cisc_controller_1_p17, gcpu_cisc_controller_1_p18,
       gcpu_cisc_controller_1_p19, gcpu_cisc_controller_1_p20, gcpu_cisc_controller_1_p23,
       gcpu_risc_decoder_1_p10, gcpu_risc_decoder_1_p11, gcpu_risc_decoder_1_p12, gcpu_risc_decoder_1_p14,
       gcpu_risc_decoder_1_p15, gcpu_risc_decoder_1_p16, gcpu_risc_decoder_1_p17, gcpu_risc_decoder_1_p18,
       gcpu_risc_decoder_1_p19, gcpu_risc_decoder_1_p22, gcpu_risc_decoder_1_p24, gcpu_risc_decoder_1_p26,
       gcpu_risc_decoder_1_p28, gcpu_selection___registers_1_pror, gcpu_selection___registers_1_read_i_o,
       gcpu_selection___registers_1_write_flg, gcpu_selection___registers_1_write_io,
       gcpu_selection___registers_1_write_pc, or_1_out, undriven;
  wire [1:0] gcpu_cisc_controller_1_p4, gcpu_cisc_controller_1_p21;
  wire [3:0] and_3_out, gcpu_alu_1_zero, gcpu_risc_decoder_1_p20, gcpu_risc_decoder_1_p21,
       gcpu_risc_decoder_1_p23, gcpu_risc_decoder_1_p25, pullup_1_out;
  wire [7:0] gcpu_cisc_controller_1_p8;
  wire [7:4] or_2_out;
  wire [15:0] delay_3_out, delay_4_out, delay_5_out, gcpu_flags_1_output, gcpu_selection___registers_1_out0,
       gcpu_selection___registers_1_out1;

  Delay delay_1 (.in(Start), .out(delay_1_out));
  Delay delay_2 (.in(Pause), .out(delay_2_out));
  and and_1 (and_1_out, Start, ~delay_1_out);  // And
  and and_2 (and_2_out, Pause, ~delay_2_out);  // And
  PRNG prng_1 (.S(1'b0), .se(1'b0), .ne(1'b1), .C(Clock_In), .R(gcpu_cisc_controller_1_p8[7]));
  // Probe IO on I_O_In
  PullUp #(.Bits(4)) pullup_1 (.out(pullup_1_out));
  assign pullup_1_out = ~gcpu_cisc_controller_1_p4[0] ? Int_Mask : 4'bz;  // DriverInvSel driverinvsel_1
  assign and_3_out = pullup_1_out & Int_Lines;  // And and_3, 4 bits wide
  // GCPU_CISC_Controller gcpu_cisc_controller_1: pin names not known; wires that end beside it: and_1_out, and_2_out, gcpu_cisc_controller_1_p3, gcpu_cisc_controller_1_p4, gcpu_cisc_controller_1_p5, RAM_Din, Clock_In, {gcpu_cisc_controller_1_p8[7], 1'b1, I_O_Writing, I_O_Reading, gcpu_cisc_controller_1_p8[3:0]}, gcpu_cisc_controller_1_p9, gcpu_cisc_controller_1_p10, Hard_Reset, gcpu_cisc_controller_1_p12, gcpu_cisc_controller_1_p13, gcpu_cisc_controller_1_p14, gcpu_cisc_controller_1_p15, gcpu_cisc_controller_1_p16, gcpu_cisc_controller_1_p17, gcpu_cisc_controller_1_p18, gcpu_cisc_controller_1_p19, gcpu_cisc_controller_1_p20, gcpu_cisc_controller_1_p21, Running, gcpu_cisc_controller_1_p23
  // GCPU_RISC_Decoder gcpu_risc_decoder_1: pin names not known; wires that end beside it: gcpu_cisc_controller_1_p12, gcpu_cisc_controller_1_p13, gcpu_cisc_controller_1_p14, gcpu_cisc_controller_1_p15, gcpu_cisc_controller_1_p16, gcpu_cisc_controller_1_p17, gcpu_cisc_controller_1_p18, gcpu_cisc_controller_1_p19, Hard_Reset, gcpu_risc_decoder_1_p10, gcpu_risc_decoder_1_p11, gcpu_risc_decoder_1_p12, RAM_Str, gcpu_risc_decoder_1_p14, gcpu_risc_decoder_1_p15, gcpu_risc_decoder_1_p16, gcpu_risc_decoder_1_p17, gcpu_risc_decoder_1_p18, gcpu_risc_decoder_1_p19, gcpu_risc_decoder_1_p20, gcpu_risc_decoder_1_p21, gcpu_risc_decoder_1_p22, gcpu_risc_decoder_1_p23, gcpu_risc_decoder_1_p24, gcpu_risc_decoder_1_p25, gcpu_risc_decoder_1_p26, or_2_out[5], gcpu_risc_decoder_1_p28
  and and_4 (and_4_out, Hard_Reset, Clock_In);
  Delay #(.Bits(16), .delayTime(2)) delay_3 (.in(RAM_Din), .out(delay_3_out));
  or or_1 (or_1_out, gcpu_cisc_controller_1_p20, and_4_out);
  or or_2 (or_2_out[6], gcpu_risc_decoder_1_p28, gcpu_selection___registers_1_pror);
  assign RAM_Dout = gcpu_risc_decoder_1_p12 ? delay_3_out : 16'bz;  // Driver driver_1
  PullDown #(.Bits(16)) pulldown_1 (.out(RAM_Dout));
  // Probe Data Bus on RAM_Dout
  GCPU_Flags gcpu_flags_1 (
    .UE_Push(gcpu_risc_decoder_1_p16), .UE_Pop(gcpu_risc_decoder_1_p15), .Input(RAM_Dout),
    .ALU_Flags(gcpu_alu_1_zero), .W_ALUF(gcpu_risc_decoder_1_p18),
    .Write_All(gcpu_selection___registers_1_write_flg), .Set_LOEn(gcpu_risc_decoder_1_p15),
    .Reset_LOEn(gcpu_risc_decoder_1_p16), .Clr_EXC_Buff(gcpu_risc_decoder_1_p16),
    .Ex_Lines({or_2_out, and_3_out}), .Clock(or_1_out), .Cur_UE(gcpu_cisc_controller_1_p4), .IOP(IOP),
    .ALUF(gcpu_cisc_controller_1_p8[3:0]), .LOEn(LO_Enabled), .Non_Ign(gcpu_cisc_controller_1_p5),
    .Exception(gcpu_cisc_controller_1_p3), .Output(gcpu_flags_1_output));
  GCPU_Addressing gcpu_addressing_1 (
    .State(gcpu_cisc_controller_1_p21), .Adder_En(undriven), .Cur_UE(gcpu_cisc_controller_1_p4),
    .LO_En(LO_Enabled), .HLB_In(HLB), .Clock(or_1_out), .PC_plus_1(gcpu_risc_decoder_1_p10),
    .PC_plus_2(gcpu_risc_decoder_1_p11), .Data_In(RAM_Dout),
    .Write_PC(gcpu_selection___registers_1_write_pc), .OOB(or_2_out[7]), .RAM_Addr(RAM_A), .PC_Out(PC));
  GCPU_Selection___Registers gcpu_selection___registers_1 (
    .Data_In(RAM_Dout), .Clock(or_1_out), .Cur_UE(gcpu_cisc_controller_1_p4), .PC_In(PC), .IO_In(I_O_In),
    .FLG_In(gcpu_flags_1_output), .Write(gcpu_risc_decoder_1_p21), .Write_2(gcpu_risc_decoder_1_p22),
    .Read0(gcpu_risc_decoder_1_p23), .Read0_2(gcpu_risc_decoder_1_p24), .Read1(gcpu_risc_decoder_1_p25),
    .Read1_2(gcpu_risc_decoder_1_p26), .PROR_Override(gcpu_cisc_controller_1_p23), .CTDZ(or_2_out[4]),
    .Write_PC(gcpu_selection___registers_1_write_pc), .Write_FLG(gcpu_selection___registers_1_write_flg),
    .Out0(gcpu_selection___registers_1_out0), .Out1(gcpu_selection___registers_1_out1),
    .PROR(gcpu_selection___registers_1_pror), .HLB(HLB), .Read_I_O(gcpu_selection___registers_1_read_i_o),
    .Write_IO(gcpu_selection___registers_1_write_io));
  GCPU_ALU gcpu_alu_1 (
    .Imm_Op(gcpu_risc_decoder_1_p19), .A_In(delay_4_out), .Carry_In(gcpu_cisc_controller_1_p8[2]),
    .OpCode(gcpu_risc_decoder_1_p20), .ALU_En(gcpu_risc_decoder_1_p17), .B_In(delay_5_out),
    .Imm_Value(gcpu_risc_decoder_1_p25), .Out(RAM_Dout), .Zero(gcpu_alu_1_zero[0]),
    .Sign(gcpu_alu_1_zero[1]), .Carry_Out(gcpu_alu_1_zero[2]), .Overflow(gcpu_alu_1_zero[3]));
  Delay #(.Bits(16)) delay_4 (.in(gcpu_selection___registers_1_out0), .out(delay_4_out));
  Delay #(.Bits(16)) delay_5 (.in(gcpu_selection___registers_1_out1), .out(delay_5_out));
  Delay #(.delayTime(6)) delay_6 (.in(gcpu_selection___registers_1_read_i_o), .out(delay_6_out));
  Delay #(.delayTime(6)) delay_7 (.in(gcpu_selection___registers_1_write_io), .out(delay_7_out));
  not not_1 (Kernel, gcpu_cisc_controller_1_p4[1]);
  and and_5 (and_5_out, gcpu_selection___registers_1_read_i_o, delay_6_out);
  and and_6 (and_6_out, gcpu_selection___registers_1_write_io, delay_7_out);
  assign RAM_Dout = RAM_Str ? delay_4_out : 16'bz;  // Driver driver_2
  assign RAM_Dout = gcpu_risc_decoder_1_p14 ? delay_5_out : 16'bz;  // Driver driver_3
  Delay delay_8 (.in(and_5_out), .out(delay_8_out));
  Delay #(.delayTime(2)) delay_9 (.in(and_5_out), .out(delay_9_out));
  Delay #(.delayTime(3)) delay_10 (.in(and_5_out), .out(delay_10_out));
  Delay #(.delayTime(4)) delay_11 (.in(and_5_out), .out(delay_11_out));
  Delay delay_12 (.in(and_6_out), .out(delay_12_out));
  Delay #(.delayTime(2)) delay_13 (.in(and_6_out), .out(delay_13_out));
  Delay #(.delayTime(3)) delay_14 (.in(and_6_out), .out(delay_14_out));
  Delay #(.delayTime(4)) delay_15 (.in(and_6_out), .out(delay_15_out));
  or or_3 (Reading_I_O, and_5_out, delay_8_out, delay_9_out, delay_10_out, delay_11_out);
  or or_4 (Writing_I_O, and_6_out, delay_12_out, delay_13_out, delay_14_out, delay_15_out);
  assign I_O_Out = Writing_I_O ? RAM_Dout : 16'bz;  // Driver driver_4

  // Notes on the sheet:
  //   Start: Starts/Resumes the execution of program memory.
  //   Only starts/resumes on rising edge (so if Start is held high the CPU can still halt)
  //   Pause: Pauses the execution of program memory.
  //   Only pauses on rising edge.
  //   Running: Only on if the CPU is currently executing program memory.
  //   RAM_A: The current memory address.
  //   RAM_Din: RAM data input
  //   I_O_In: The Input portion of I/O
  //   I_O_Reading: Should be high if the I/O wants to read from the CPU.
  //   Is a jump condition (PIR/PNR)
  //   RAM_Dout: Data output to RAM
  //   I_O_Writing: Should be high if the I/O wants to write to the CPU.
  //   Is a jump condition (PIW/PNW).
  //   RAM_Str: On if writing to RAM.
  //   PC: The current value of the program counter.
  //   HLB: The contents of the HI/LOW Bounds register.
  //   Kernel: On if the current process is kernel.
  //   I/O devices can choose whether they respond to non-kernel processes.
  //   Reading_I_O: On if the CPU is currently reading from Input.
  //   I_O_Out: The Output portion of I/O
  //   Writing_I_O: On if the CPU is currently writing to output.
  //   IOP: The currently selected I/O device.
  //   Note: I/O must be multiplexed according to this signal *outside* the CPU.
  //   Int_Mask: Each bit corresponds to one interrupt line.
  //   If the bit is on, then that interrupt is non-maskable.
  //   Hard_Reset: Effectively resets the CPU.
  //   Only clears the state counter, PC, and parts of FLG.
  //   It must be held down for at least 2 full clock cycles to work.
  //   Jump conditions
  //   Interrupt Masking
  //   Exception Lines
  //   I/O Signal Corrections
endmodule
