// Digital circuit Telescope Assembler Computer.dig as structural Verilog
module Telescope_Assembler_Computer (
  input  Assemble,
  input  Clock,
  input  [6:0] Text_Input,
  output Running,
  output [23:0] Text_Address,
  output [15:0] Output_Address,
  output [15:0] Output_Data,
  output Output_Write,
  output [6:0] Terminal_Data,
  output Terminal_Write,
  output [15:0] Stop_Code
);

  wire and_1_out, and_2_out, bootloader_machine_1_writing_i_o, demultiplexer_1_out_0;
  wire [4:0] bootloader_machine_1_iop;
  wire [15:0] Assembler_d, bootloader_machine_1_load_adr;

  Bootloader_Machine bootloader_machine_1 (
    .Boot_Start(Assemble), .Pause(1'b0), .Clock_In(Clock), .Load_Din(Assembler_d),
    .I_O_In({{9{1'b0}}, Text_Input}), .I_O_Reading(1'b0), .I_O_Writing(1'b0), .Int_Lines(4'b0000),
    .Int_Mask(4'b0000), .Hard_Reset(1'b0), .Running(Running), .Load_Adr(bootloader_machine_1_load_adr),
    .Reading_I_O(Terminal_Write), .I_O_Out(Output_Data), .Writing_I_O(bootloader_machine_1_writing_i_o),
    .IOP(bootloader_machine_1_iop));  // open: PC, HLB, Kernel
  ROM #(.AddrBits(16), .Bits(16)) Assembler (.A(bootloader_machine_1_load_adr), .sel(1'b1), .D(Assembler_d));
  and and_1 (and_1_out, bootloader_machine_1_iop[3], bootloader_machine_1_writing_i_o);
  and and_2 (and_2_out, bootloader_machine_1_writing_i_o, ~bootloader_machine_1_iop[3]);  // And
  Demultiplexer demultiplexer_1 (
    .sel(bootloader_machine_1_iop[0]), .in(and_2_out), .out_0(demultiplexer_1_out_0), .out_1(Output_Write));
  Register #(.Bits(16)) register_1 (.D(Output_Data), .C(Clock), .en(and_1_out), .Q(Stop_Code));
  Counter #(.Bits(24)) counter_1 (
    .en(Terminal_Write), .C(Clock), .clr(demultiplexer_1_out_0), .out(Text_Address));  // open: ovf
  Counter #(.Bits(16)) counter_2 (.en(Output_Write), .C(Clock), .clr(1'b0), .out(Output_Address));  // open: ovf

  assign Terminal_Data = Text_Input;

  // Notes on the sheet:
  //   contents of Assembler (hex, n*v repeats v):
  //   51a,4600,154,d9ed,3000,3,992a,4000,4,a48c,5000,2,91ec,6000,3,ca93
  //   ,7000,3,9981,8000,7,9921,9000,f,d581,a000,7,a581,b000,f,b8c1,c000
  //   ,7,b921,d000,f,d0b2,3087,0,be5a,b100,2,b2ae,b000,2,cc30,9200,2
  //   ,8dc9,b901,2,8ca4,bb01,2,8c69,9901,2,8c64,9b01,2,a270,bbb0,9,c1f0
  //   ,b9b0,9,c1a3,cb00,3,a5a3,db00,b,c1aa,4600,0,c4aa,4000,0,95ca,4800
  //   ,0,d18a,4100,0,94ea,4900,0,cf33,2000,0,b672,1000,0,d188,0,0,c1ee
  //   ,f000,0,ffff,40f2,0,44f2,1,48f2,2,4cf2,3,50f2,4,54f2,5,58f2,6
  //   ,d2af,6,5cf2,7,32,7,70,8,1e9,9,9d86,a,213,b,8988,c,9283,d,8e05
  //   ,e,8705,f,ffff,d1ee,0,91c1,1,24f,2,8993,4,8a53,5,9081,9,8ab3,b
  //   ,d0b3,6,9cae,8,c9f8,3,b2ad,d,d924,e,ea25,0,ea8c,1,c823,2,cacf
  //   ,3,9250,4,d2f0,5,d275,7,d654,6,e8ae,8,e8a7,9,c86e,a,d9ee,b,c9d0
  //   ,c,ddd0,d,91d2,7,8c81,a,8853,c,91ed,f,ffff,130*0,50a0,0,3069,3087
  //   ,50a0,0,5090,0,3087,50a0,800,3090,3087,50a0,0,5090,0,50b0,0,70bb
  //   ,146,4600,33d,b120,6022,145,b160,cb12,4900,17b,6031,c5,d636,4a00
  //   ,16b,b939,b13f,ad60,a963,b911,cb12,4800,165,b100,6000,c5,5010
  //   ,2d,cb10,4800,17b,a866,3087,b100,6000,c5,5010,3e,cb01,4800,186
  //   ,4600,1cb,b120,5010,2d,cb01,4800,18d,b921,b110,6011,145,bb11,8b12
  //   ,4800,19e,b160,a962,6066,c5,b16f,bd22,bb21,ad62,a866,3087,5000
  //   ,1,a902,6000,c5,d606,4200,1ac,5000,a,b110,a912,4600,15e,5010,78
  //   ,cb01,4800,1b8,5000,10,5010,2,a912,4600,15e,5010,62,cb01,4800
  //   ,1c4,5000,2,5010,2,a912,4600,15e,50a0,f800,5090,fff0,0,4600,154
  //   ,b100,b110,6011,146,b130,6033,145,cb01,4100,1dc,50a0,f800,5090
  //   ,fff1,0,4600,154,6020,51a,cb32,4800,1f7,5040,1,cb42,4800,1eb,a902
  //   ,6060,51a,4600,1fb,3050,a954,6055,51a,6064,c5,cb56,4800,1f7,b941
  //   ,4600,1e3,a902,b901,4600,1d2,3087,7077,205,3061,5050,ffff,6046
  //   ,0,cb40,4000,0,cb45,4000,20c,a962,4600,201,3065,3087,d606,4a00
  //   ,21f,3030,b735,5010,5b,cb31,4100,23d,5010,5e,cb31,4100,23b,b060
  //   ,3087,5030,2c,cb30,4900,229,5030,3a,cb03,4100,23d,5030,3e,cb30
  //   ,4000,23d,5030,20,cb30,4900,238,5030,28,cb03,4100,23d,9200,4000
  //   ,23d,b160,3087,b060,3087,5060,0,3059,cb50,4000,248,cb56,4800,241
  //   ,3087,bbb1,707b,0,50a0,0,3009,3078,b974,4600,20e,9260,4000,24e
  //   ,d606,4200,297,5070,24e,5010,2f,cb01,4800,264,5000,a,4600,23f
  //   ,5010,25,cb01,4000,23f,5010,0,cb01,4800,274,7000,c5,5040,1,4600
  //   ,2bf,b140,5010,27,cb01,4800,286,7004,c5,3009,b941,7004,c5,3009
  //   ,b941,7004,c5,4600,2bf,5010,22,cb01,4800,297,7004,c5,b941,3009
  //   ,cb01,4800,28b,7004,c5,b941,4600,2bf,b140,5070,2a0,7004,c5,b941
  //   ,3009,4600,20e,9260,4000,2bf,d606,4200,29a,5030,25,cb03,4800,2af
  //   ,5070,2bf,4600,23f,5030,2f,cb03,4800,2ba,5000,a,5070,2bf,4600
  //   ,23f,5030,0,cb03,4800,29a,7044,145,607b,0,b9b1,3087,b110,6011
  //   ,146,b100,6000,145,7001,51a,b911,5020,1,6032,c5,7031,51a,b911
  //   ,b921,cb20,4800,2d0,7011,146,3087,5010,1f,b160,5000,2,6000,c5
  //   ,3060,a161,b46a,d606,b100,aa00,b40f,a260,5000,1,6000,c5,a101,b405
  //   ,a260,b100,6000,c5,a101,a260,3087,bbb2,700b,0,707b,1,3078,b974
  //   ,4600,249,b100,6010,145,db12,4800,30d,b120,7021,c5,b911,7011,145
  //   ,3078,b974,4600,2dc,3006,601b,0,5020,2,3078,b974,4600,1fc,d961
  //   ,4a00,324,50a0,f800,5090,fff4,0,4600,154,b961,6066,0,607b,1,b9b2
  //   ,3087,b100,5010,1,6020,145,6031,c5,7030,c5,b901,b911,cb12,4800
  //   ,330,bb21,7022,145,3087,b100,bbb1,700b,0,3078,b974,4600,249,b100
  //   ,6000,c5,5010,0,cb01,4000,411,5010,23,cb01,4800,362,3078,b974
  //   ,4600,2c5,600b,0,b110,6011,146,7001,51a,b911,7011,146,4600,341
  //   ,5010,40,cb01,4800,38b,3078,b974,4600,2c5,3078,b974,4600,249,b100
  //   ,6000,c5,5010,27,cb01,4800,37d,5060,1,6066,c5,4600,381,3078,b974
  //   ,4600,17c,b100,6000,146,7060,51a,b901,7000,146,4600,341,5010,27
  //   ,cb01,4800,397,600b,0,b901,700b,0,4600,341,5010,22,cb01,4800,3a7
  //   ,b110,6011,145,bb11,600b,0,a901,700b,0,4600,341,5010,7e,cb01,4800
  //   ,3b7,3078,b974,4600,1cb,600b,0,a906,700b,0,4600,341,d606,4200
  //   ,3c1,600b,0,b901,700b,0,4600,341,3078,b974,4600,2dc,5010,b023
  //   ,cb16,4800,3d1,600b,0,b903,700b,0,4600,341,600b,0,b901,700b,0
  //   ,3006,5010,2,5020,3,3078,b974,4600,1fc,d961,4a00,3e9,50a0,f800
  //   ,5090,fff3,0,4600,154,b962,6006,0,bbb1,d602,4a00,3f8,700b,0,3078
  //   ,b974,4600,249,600b,0,d601,4a00,403,700b,0,3078,b974,4600,249
  //   ,600b,0,d600,4a00,40e,700b,0,3078,b974,4600,249,600b,0,b9b1,4600
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endmodule
