// Digital circuit CPU Testspace.dig as structural Verilog
module CPU_Testspace (
  input  clk,
  input  [15:0] in_2
);

  wire button_1_out, button_2_out, glass_cpu_1_ram_str, glass_cpu_1_running, glass_cpu_1_writing_i_o,
       not_1_out;
  wire [15:0] add_1_s, glass_cpu_1_i_o_out, glass_cpu_1_pc, glass_cpu_1_ram_a, glass_cpu_1_ram_dout,
       Program_Memory_d, register_1_q;
  wire [31:0] counter_1_out;

  Button button_1 (.out(button_1_out));
  Button button_2 (.out(button_2_out));
  Glass_CPU glass_cpu_1 (
    .Start(button_1_out), .Pause(button_2_out), .Clock_In(clk), .RAM_Din(Program_Memory_d), .I_O_In(in_2),
    .I_O_Reading(1'b0), .I_O_Writing(1'b0), .Int_Lines(4'b0000), .Int_Mask(4'b0000), .Hard_Reset(1'b0),
    .Running(glass_cpu_1_running), .RAM_A(glass_cpu_1_ram_a), .RAM_Dout(glass_cpu_1_ram_dout),
    .RAM_Str(glass_cpu_1_ram_str), .PC(glass_cpu_1_pc), .I_O_Out(glass_cpu_1_i_o_out),
    .Writing_I_O(glass_cpu_1_writing_i_o));  // open: HLB, Kernel, Reading_I_O, IOP, LO_Enabled
  RAMDualPort #(.AddrBits(16), .isProgramMemory("true"), .Bits(16)) Program_Memory (
    .A(glass_cpu_1_ram_a), .Din(glass_cpu_1_ram_dout), .str(glass_cpu_1_ram_str), .C(clk), .ld(1'b1),
    .D(Program_Memory_d));
  Counter #(.Bits(32)) counter_1 (.en(glass_cpu_1_running), .C(clk), .clr(1'b0), .out(counter_1_out));  // open: ovf
  Add #(.Bits(16)) add_1 (.a(glass_cpu_1_pc), .b(16'h2), .c_i(1'b0), .s(add_1_s));  // open: c_o
  Register #(.Bits(16)) register_1 (.D(glass_cpu_1_i_o_out), .C(clk), .en(glass_cpu_1_writing_i_o), .Q(register_1_q));
  Break HLT (.brk(not_1_out));
  not not_1 (not_1_out, glass_cpu_1_running);
  // Probe Cycles Used on counter_1_out
  // Probe RTL Line on add_1_s
  // Probe Test Output on register_1_q

  // Notes on the sheet:
  //   clk: Hz: 128
endmodule
