// Logisim project Computers.circ as structural Verilog: 1 circuit, main circuit Assembler Workspace
module Assembler_Workspace (
  input  [15:0] RAM_Data_In,
  input  Reset_Machine,
  input  Start,
  input  Pause,
  input  [6:0] Input_Data,
  output [15:0] RAM_Address,
  output [15:0] RAM_Data_Out,
  output RAM_Store,
  output RAM_Clock,
  output [15:0] RTL_File_Line,
  output [31:0] Cycles_Used,
  output Bad_Number,
  output Label_Not_Found,
  output Non_Empty_Stack,
  output Instruction_Not_Found,
  output Operand_Not_Found,
  output Success,
  output Is_Running,
  output [15:0] Output_Address,
  output [19:0] Input_Address,
  output [15:0] Output_Data,
  output Output_Clock,
  output Output_Store,
  output Output_Clear,
  output TTY_Clear,
  output TTY_Write,
  output [6:0] TTY_Data,
  output TTY_Clock
);

  wire demultiplexer_2_out0, glass_cpu_1_clock_out, glass_cpu_1_cpu_is_writing_i_o, not_1_out;
  wire [4:0] glass_cpu_1_selected_i_o_device;
  wire [15:0] bit_extender_1_out, controlled_buffer_1_out, glass_cpu_1_i_o_output;

  Pull_Resistor pull_resistor_1 (.node(Reset_Machine));
  assign bit_extender_1_out = {{9{1'b0}}, Input_Data};  // Bit_Extender bit_extender_1
  Clock clock_1 (.out(Output_Clock));
  Counter #(.width(20), .max('hfffff)) Current_Char_num (
    .count(TTY_Write), .Q(Input_Address), .clk(Output_Clock), .clr(TTY_Clear));  // open: load, D, carry
  Glass_CPU glass_cpu_1 (
    .Clock_Input(Output_Clock), .Reset_CPU(Reset_Machine), .Start_CPU(Start), .Pause_CPU(Pause),
    .RAM_Data_Input(RAM_Data_In), .RAM_Data_Output(RAM_Data_Out), .RAM_Write(RAM_Store),
    .RAM_Address(RAM_Address), .CPU_Is_Writing_I_O(glass_cpu_1_cpu_is_writing_i_o),
    .I_O_Output(glass_cpu_1_i_o_output), .I_O_Input(bit_extender_1_out), .CPU_Is_Reading_I_O(TTY_Write),
    .Selected_I_O_Device(glass_cpu_1_selected_i_o_device), .Is_On(Is_Running),
    .Clock_Out(glass_cpu_1_clock_out), .Mask_Int_Lines(3'b000), .Non_Msk_Int(1'b0));  // open: I_O_Is_Reading_CPU, I_O_Is_Writing_CPU, HLB_For_Current_Process, Current_Process_Is_Kernel, Program_Counter
  Demultiplexer #(.width(16), .disabled(0), .enable("false")) demultiplexer_1 (
    .out1(Output_Data), .in(glass_cpu_1_i_o_output), .sel(glass_cpu_1_selected_i_o_device[0]));  // open: out0
  Demultiplexer #(.disabled(0), .enable("false")) demultiplexer_2 (
    .out0(demultiplexer_2_out0), .out1(Output_Store), .in(glass_cpu_1_cpu_is_writing_i_o),
    .sel(glass_cpu_1_selected_i_o_device[0]));
  or or_1 (TTY_Clear, Reset_Machine, demultiplexer_2_out0);
  Bit_Extender #(.in_width(16), .out_width(7)) bit_extender_2 (.in(bit_extender_1_out), .out(TTY_Data));
  assign controlled_buffer_1_out = not_1_out ? RAM_Data_In : 16'bz;  // Controlled_Buffer controlled_buffer_1
  not not_1 (not_1_out, Is_Running);
  Adder #(.width(16)) adder_1 (.a(16'h2), .b(RAM_Address), .out(RTL_File_Line));  // open: cin, cout
  Counter #(.width(32), .max('hffffffff), .ongoal("stay")) counter_1 (
    .count(1'b1), .Q(Cycles_Used), .clk(glass_cpu_1_clock_out), .clr(Reset_Machine));  // open: load, D, carry
  Counter #(.width(16), .max('hffff)) Output_PC (
    .count(Output_Store), .Q(Output_Address), .clk(Output_Clock), .clr(Reset_Machine));  // open: load, D, carry
  Pull_Resistor pull_resistor_2 (.node(controlled_buffer_1_out));
  Comparator #(.width(16), .mode("unsigned")) comparator_1 (
    .a(controlled_buffer_1_out), .b(16'hfff0), .eq(Bad_Number));  // open: gt, lt
  Comparator #(.width(16), .mode("unsigned")) comparator_2 (
    .a(controlled_buffer_1_out), .b(16'hfff1), .eq(Label_Not_Found));  // open: gt, lt
  Comparator #(.width(16), .mode("unsigned")) comparator_3 (
    .a(controlled_buffer_1_out), .b(16'hfff2), .eq(Non_Empty_Stack));  // open: gt, lt
  Comparator #(.width(16), .mode("unsigned")) comparator_4 (
    .a(controlled_buffer_1_out), .b(16'hfff3), .eq(Instruction_Not_Found));  // open: gt, lt
  Comparator #(.width(16), .mode("unsigned")) comparator_5 (
    .a(controlled_buffer_1_out), .b(16'hfff4), .eq(Operand_Not_Found));  // open: gt, lt
  Comparator #(.width(16), .mode("unsigned")) comparator_6 (
    .a(controlled_buffer_1_out), .b(16'h1), .eq(Success));  // open: gt, lt

  assign Output_Clear = Reset_Machine;
  assign RAM_Clock = Output_Clock;
  assign TTY_Clock = Output_Clock;
endmodule
