// Logisim project Sandbox.circ as structural Verilog
module CPU_General_Test_Space (
);

  wire clock_1_out, glass_cpu_1_clock_out, glass_cpu_1_cpu_is_reading_i_o, glass_cpu_1_cpu_is_writing_i_o,
       glass_cpu_1_current_process_is_kernel, glass_cpu_1_is_on, glass_cpu_1_ram_write, Off_out, On_out,
       Ready_q, Ready_qn, Rst_out;
  wire [4:0] glass_cpu_1_selected_i_o_device;
  wire [15:0] adder_1_out, Cycles_Used_q, glass_cpu_1_i_o_output, glass_cpu_1_program_counter,
       glass_cpu_1_ram_address, glass_cpu_1_ram_data_output, ram_1_data, Test_Interface_q;

  Button On (.out(On_out));
  Button Off (.out(Off_out));
  Clock clock_1 (.out(clock_1_out));
  Button Rst (.out(Rst_out));
  LED led_1 (.in(glass_cpu_1_is_on));
  Glass_CPU glass_cpu_1 (
    .Clock_Input(clock_1_out), .Reset_CPU(Rst_out), .Start_CPU(On_out), .Pause_CPU(Off_out),
    .RAM_Data_Input(ram_1_data), .RAM_Data_Output(glass_cpu_1_ram_data_output),
    .RAM_Write(glass_cpu_1_ram_write), .RAM_Address(glass_cpu_1_ram_address), .I_O_Is_Reading_CPU(Ready_qn),
    .CPU_Is_Writing_I_O(glass_cpu_1_cpu_is_writing_i_o), .I_O_Output(glass_cpu_1_i_o_output),
    .I_O_Input(Test_Interface_q), .CPU_Is_Reading_I_O(glass_cpu_1_cpu_is_reading_i_o),
    .I_O_Is_Writing_CPU(Ready_q), .Selected_I_O_Device(glass_cpu_1_selected_i_o_device),
    .Current_Process_Is_Kernel(glass_cpu_1_current_process_is_kernel),
    .Program_Counter(glass_cpu_1_program_counter), .Is_On(glass_cpu_1_is_on),
    .Clock_Out(glass_cpu_1_clock_out), .Mask_Int_Lines(3'b000), .Non_Msk_Int(1'b0));  // open: HLB_For_Current_Process
  RAM #(.addrWidth(16), .dataWidth(16), .bus("separate")) ram_1 (
    .addr(glass_cpu_1_ram_address), .din(glass_cpu_1_ram_data_output), .data(ram_1_data),
    .str(glass_cpu_1_ram_write), .clk(clock_1_out));  // open: sel, ld, clr
  LED led_2 (.in(glass_cpu_1_current_process_is_kernel));
  // Probe on glass_cpu_1_selected_i_o_device
  // Probe on adder_1_out
  Adder #(.width(16)) adder_1 (.a(16'h2), .b(glass_cpu_1_program_counter), .out(adder_1_out));  // open: cin, cout
  // Probe on Cycles_Used_q
  Counter #(.width(16), .max('hffff)) Cycles_Used (
    .Q(Cycles_Used_q), .clk(glass_cpu_1_clock_out), .clr(Rst_out));  // open: load, D, count, carry
  Register #(.width(16)) Test_Interface (
    .D(glass_cpu_1_i_o_output), .en(glass_cpu_1_cpu_is_writing_i_o), .Q(Test_Interface_q), .clk(clock_1_out));  // open: clr
  // Probe on Test_Interface_q
  S_R_Flip_Flop Ready (
    .S(1'b0), .clk(clock_1_out), .R(glass_cpu_1_cpu_is_reading_i_o), .Q(Ready_q), .Qn(Ready_qn),
    .reset(Rst_out));  // open: preset, en
  LED led_3 (.in(Ready_q));

  // Notes on the sheet:
  //   Currently set up for: IO Test
endmodule

module Assembler_Workspace (
);

  wire clock_1_out, demultiplexer_2_out0, demultiplexer_2_out1, glass_cpu_1_clock_out,
       glass_cpu_1_cpu_is_reading_i_o, glass_cpu_1_cpu_is_writing_i_o, glass_cpu_1_is_on,
       glass_cpu_1_ram_write, or_1_out, Reset_Everything_out, Start_out, Stop_out;
  wire [4:0] glass_cpu_1_selected_i_o_device;
  wire [6:0] bit_extender_1_out;
  wire [15:0] adder_1_out, Current_Char_num_q, demultiplexer_1_out0, demultiplexer_1_out1,
       glass_cpu_1_i_o_output, glass_cpu_1_program_counter, glass_cpu_1_ram_address,
       glass_cpu_1_ram_data_output, Output_PC_q, ram_1_data, rom_1_data;
  wire [31:0] counter_1_q;

  Counter #(.width(16), .max('hffff)) Current_Char_num (
    .D(demultiplexer_1_out0), .count(glass_cpu_1_cpu_is_reading_i_o), .Q(Current_Char_num_q),
    .clk(clock_1_out), .clr(or_1_out));  // open: load, carry
  Clock clock_1 (.out(clock_1_out));
  Button Reset_Everything (.out(Reset_Everything_out));
  Button Start (.out(Start_out));
  Button Stop (.out(Stop_out));
  ROM #(.addrWidth(16), .dataWidth(16)) rom_1 (.addr(Current_Char_num_q), .data(rom_1_data));  // open: sel
  LED On (.in(glass_cpu_1_is_on));
  Glass_CPU glass_cpu_1 (
    .Clock_Input(clock_1_out), .Reset_CPU(Reset_Everything_out), .Start_CPU(Start_out), .Pause_CPU(Stop_out),
    .RAM_Data_Input(ram_1_data), .RAM_Data_Output(glass_cpu_1_ram_data_output),
    .RAM_Write(glass_cpu_1_ram_write), .RAM_Address(glass_cpu_1_ram_address),
    .CPU_Is_Writing_I_O(glass_cpu_1_cpu_is_writing_i_o), .I_O_Output(glass_cpu_1_i_o_output),
    .I_O_Input(rom_1_data), .CPU_Is_Reading_I_O(glass_cpu_1_cpu_is_reading_i_o),
    .Selected_I_O_Device(glass_cpu_1_selected_i_o_device), .Program_Counter(glass_cpu_1_program_counter),
    .Is_On(glass_cpu_1_is_on), .Clock_Out(glass_cpu_1_clock_out), .Mask_Int_Lines(3'b000), .Non_Msk_Int(1'b0));  // open: I_O_Is_Reading_CPU, I_O_Is_Writing_CPU, HLB_For_Current_Process, Current_Process_Is_Kernel
  Demultiplexer #(.width(16), .disabled(0), .enable("false")) demultiplexer_1 (
    .out0(demultiplexer_1_out0), .out1(demultiplexer_1_out1), .in(glass_cpu_1_i_o_output),
    .sel(glass_cpu_1_selected_i_o_device[0]));
  RAM #(.addrWidth(16), .dataWidth(16), .bus("separate")) ram_1 (
    .addr(glass_cpu_1_ram_address), .din(glass_cpu_1_ram_data_output), .data(ram_1_data),
    .str(glass_cpu_1_ram_write), .clk(clock_1_out));  // open: sel, ld, clr
  Demultiplexer #(.disabled(0), .enable("false")) demultiplexer_2 (
    .out0(demultiplexer_2_out0), .out1(demultiplexer_2_out1), .in(glass_cpu_1_cpu_is_writing_i_o),
    .sel(glass_cpu_1_selected_i_o_device[0]));
  or or_1 (or_1_out, Reset_Everything_out, demultiplexer_2_out0);
  Bit_Extender #(.in_width(16), .out_width(7)) bit_extender_1 (.in(rom_1_data), .out(bit_extender_1_out));
  TTY #(.rows(16), .cols(90)) tty_1 (
    .data(bit_extender_1_out), .clk(clock_1_out), .we(glass_cpu_1_cpu_is_reading_i_o), .clr(or_1_out));
  // Probe on adder_1_out
  Adder #(.width(16)) adder_1 (.a(16'h2), .b(glass_cpu_1_program_counter), .out(adder_1_out));  // open: cin, cout
  // Probe on counter_1_q
  Counter #(.width(32), .max('hffffffff), .ongoal("stay")) counter_1 (
    .count(1'b1), .Q(counter_1_q), .clk(glass_cpu_1_clock_out), .clr(Reset_Everything_out));  // open: load, D, carry
  Counter #(.width(16), .max('hffff)) Output_PC (
    .count(demultiplexer_2_out1), .Q(Output_PC_q), .clk(clock_1_out), .clr(Reset_Everything_out));  // open: load, D, carry
  RAM #(.addrWidth(16), .dataWidth(16), .bus("separate")) ram_2 (
    .addr(Output_PC_q), .din(demultiplexer_1_out1), .str(demultiplexer_2_out1), .clk(clock_1_out),
    .clr(Reset_Everything_out));  // open: data, sel, ld

  // Notes on the sheet:
  //   INPUT ASCII FILE
  //   contents of rom_1 (hex, n*v repeats v):
  //   2f 20 4c 61 72 67 65 20 74 65 73 74 20 6f 66 20 74 68 65 20 54 41 53 4c 20 76 31 20 73 70 65 63 69
  //   66 69 63 61 74 69 6f 6e 73 2e a 2f 20 4d 65 61 6e 74 20 74 6f 20 65 6e 73 75 72 65 20 74 68 65 20 43
  //   50 55 20 28 61 6e 64 2f 6f 72 20 61 73 73 65 6d 62 6c 65 72 29 20 69 73 20 77 6f 72 6b 69 6e 67 20
  //   70 72 6f 70 65 72 6c 79 2e a 2f 20 54 68 69 73 20 69 6e 63 6c 75 64 65 73 20 61 6c 6c 20 69 6e 73 74
  //   72 75 63 74 69 6f 6e 73 2c 20 61 20 66 65 77 20 72 65 67 69 73 74 65 72 73 2c 20 61 6e 64 20 61 20
  //   63 6f 75 70 6c 65 20 41 4c 55 20 6f 70 73 2e a a 2f 20 49 74 20 6d 75 6c 74 69 70 6c 69 65 73 20 38
  //   20 62 79 20 36 20 69 6e 20 74 68 72 65 65 20 64 69 66 66 65 72 65 6e 74 20 77 61 79 73 2e a 2f 20 49
  //   66 20 74 68 65 20 6e 75 6d 62 65 72 20 69 73 20 69 6e 63 6f 72 72 65 63 74 2c 20 69 74 20 77 69 6c
  //   6c 20 61 6c 73 6f 20 77 72 69 74 65 20 4e 55 4c 4c 20 74 6f 20 74 68 65 20 73 74 6f 70 20 6c 69 6e
  //   65 20 69 6e 20 52 41 4d 2e a 2f 20 49 66 20 69 74 20 77 6f 72 6b 73 20 65 76 65 72 79 20 74 69 6d 65
  //   2c 20 74 68 65 20 61 6e 73 77 65 72 20 77 69 6c 6c 20 62 65 20 77 72 69 74 74 65 6e 20 74 6f 20 74
  //   68 65 20 73 74 6f 70 20 6c 69 6e 65 2e a a 2f 20 52 47 30 20 61 6e 64 20 31 20 63 6f 6e 74 61 69 6e
  //   20 74 68 65 20 74 77 6f 20 6e 75 6d 62 65 72 73 2e a 2f 20 52 47 32 20 63 6f 6e 74 61 69 6e 73 20 74
  //   68 65 20 61 6e 73 77 65 72 20 6f 66 20 74 68 65 20 70 72 65 76 69 6f 75 73 20 61 74 74 65 6d 70 74
  //   2e a 2f 20 52 47 33 20 63 6f 6e 74 61 69 6e 73 20 61 20 72 65 74 75 72 6e 20 61 64 64 72 65 73 73 20
  //   28 66 6f 72 20 74 68 65 20 66 75 6e 63 74 69 6f 6e 29 2e a 2f 20 52 47 34 20 63 6f 6e 74 61 69 6e 73
  //   20 74 68 65 20 6e 75 6d 62 65 72 20 6f 66 20 73 75 63 63 65 73 73 66 75 6c 20 6f 70 65 72 61 74 69
  //   6f 6e 73 2e a 2f 20 52 47 37 20 63 6f 6e 74 61 69 6e 73 20 74 68 65 20 65 78 70 65 63 74 65 64 20 72
  //   65 73 75 6c 74 20 66 6f 72 20 71 75 69 63 6b 20 61 63 63 65 73 73 2e a a 2f 20 41 6e 64 20 74 6f 20
  //   72 65 61 6c 6c 79 20 6d 61 6b 65 20 73 75 72 65 20 74 68 61 74 20 79 6f 75 20 70 61 73 73 65 64 20
  //   74 68 65 20 74 65 73 74 2c 20 74 68 65 20 72 65 67 69 73 74 65 72 73 20 73 68 6f 75 6c 64 20 65 6e
  //   64 20 61 73 3a a 2f 20 38 20 36 20 33 30 20 32 34 20 33 20 30 20 30 20 33 30 20 35 20 30 20 30 20 32
  //   30 20 33 39 a 2f 20 48 65 78 61 64 65 63 69 6d 61 6c 2c 20 69 6e 20 74 68 65 20 72 65 67 69 73 74 65
  //   72 73 20 26 20 73 65 6c 65 63 74 69 6f 6e 20 63 69 72 63 75 69 74 2e a a 4a 49 46 20 54 52 55 20 3e
  //   4d 61 69 6e 2e 49 6e 69 74 a a 2f 20 41 6c 6c 20 76 61 72 69 61 62 6c 65 73 20 61 72 65 20 69 6e 20
  //   6d 65 6d 6f 72 79 2c 20 74 6f 20 65 78 65 72 63 69 73 65 20 74 68 65 20 6d 65 6d 6f 72 79 20 61 63
  //   63 65 73 73 20 63 69 72 63 75 69 74 73 2e a 23 6e 75 6d 4f 6e 65 20 3d 20 30 78 30 30 30 38 a 23 6e
  //   75 6d 54 77 6f 20 3d 20 30 78 30 30 30 36 a 23 65 78 70 65 63 74 65 64 52 65 73 75 6c 74 20 3d 20 30
  //   78 30 30 33 30 a 23 72 65 74 75 72 6e 42 75 66 66 65 72 20 3d 20 30 78 4*30 a a 2f 20 71*2d a a 23
  //   4d 61 69 6e 2e 49 6e 69 74 a 4*20 2f 20 57 65 27 72 65 20 67 6f 69 6e 67 20 74 6f 20 6c 6f 61 64 20
  //   74 68 65 20 76 61 72 69 61 62 6c 65 73 2e a 4*20 4c 4f 44 20 52 47 30 20 52 47 30 20 3e 6e 75 6d 4f
  //   6e 65 a 4*20 4c 4f 44 20 52 47 31 20 52 47 31 20 3e 6e 75 6d 54 77 6f a 4*20 4c 4f 44 20 52 47 37 20
  //   52 47 37 20 3e 65 78 70 65 63 74 65 64 52 65 73 75 6c 74 a 4*20 2f 20 4e 6f 72 6d 61 6c 6c 79 20 61
  //   74 20 74 68 65 20 73 74 61 72 74 20 6f 66 20 66 75 6e 63 74 69 6f 6e 73 2c 20 77 65 20 77 72 69 74
  //   65 20 74 6f 20 74 68 65 20 73 74 61 63 6b 2e a 4*20 2f 20 53 6f 20 77 65 27 72 65 20 67 6f 69 6e 67
  //   20 74 6f 20 64 6f 20 74 68 61 74 20 68 65 72 65 2c 20 62 75 74 20 77 69 74 68 20 73 6f 6d 65 20 66
  //   61 6e 63 79 20 74 72 69 63 6b 65 72 79 2e a 4*20 2f 20 4f 75 72 20 73 74 61 63 6b 20 77 69 6c 6c 20
  //   69 6e 73 74 65 61 64 20 62 65 20 74 68 65 20 52 65 74 75 72 6e 42 75 66 66 65 72 20 76 61 72 69 61
  //   62 6c 65 2e a 4*20 2f 20 57 65 20 75 73 65 20 4c 44 49 20 74 6f 20 67 65 74 20 74 68 65 20 61 64 64
  //   72 65 73 73 20 61 6e 64 20 6e 6f 74 20 74 68 65 20 61 63 74 75 61 6c 20 76 61 6c 75 65 2e a 4*20 4c
  //   44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
  //   THE ASSEMBLER
  //   OUTPUT MACHINE CODE
  //   INPUT FILE AS IT IS READ
endmodule

module ASCII_File_Display (
  input  Enable
);

  wire and_1_out, C_out, clock_1_out, R_out;
  wire [6:0] bit_extender_1_out;
  wire [15:0] counter_1_q, rom_1_data;

  and and_1 (and_1_out, C_out, clock_1_out);
  Clock clock_1 (.out(clock_1_out));
  Button R (.out(R_out));
  Counter #(.width(16), .max('hffff)) counter_1 (
    .count(Enable), .Q(counter_1_q), .clk(and_1_out), .clr(R_out));  // open: load, D, carry
  Button C (.out(C_out));
  ROM #(.addrWidth(16), .dataWidth(16)) rom_1 (.addr(counter_1_q), .data(rom_1_data), .sel(Enable));
  Bit_Extender #(.in_width(16), .out_width(7)) bit_extender_1 (.in(rom_1_data), .out(bit_extender_1_out));
  TTY #(.rows(48), .cols(96)) tty_1 (.data(bit_extender_1_out), .clk(and_1_out), .we(Enable), .clr(R_out));

  // Notes on the sheet:
  //   contents of rom_1 (hex, n*v repeats v):
  //   4a 49 46 20 54 52 55 20 3e 53 74 61 72 74 50 6f 69 6e 74 a a 28 2f 20 43 6f 6e 73 74 61 6e 74 73 2c
  //   20 76 61 72 69 61 62 6c 65 73 2c 20 61 6e 64 20 74 61 62 6c 65 73 2e a 40 49 4e 46 4c 47 20 3d 20 30
  //   a 40 4f 55 54 46 4c 47 20 3d 20 30 78 38 30 30 a a 40 54 41 42 4c 45 53 54 4f 50 20 3d 20 30 78 4*46
  //   20 20 2f 20 4d 75 73 74 20 73 74 61 79 20 4e 55 4c 4c 2e a a 2f 20 49 6e 73 74 72 75 63 74 69 6f 6e
  //   20 74 61 62 6c 65 20 65 6e 74 72 69 65 73 3a 20 28 6d 6e 65 6d 6f 6e 69 63 5f 68 61 73 68 2c 20 74
  //   72 61 6e 73 6c 61 74 69 6f 6e 2c 20 6f 70 65 72 61 6e 64 5f 62 69 74 6d 61 70 29 a 28 23 49 6e 73 74
  //   54 61 62 6c 65 20 3d 20 5b 30 78 64 31 38 38 2c 20 30 78 4*30 2c 20 30 62 4*30 2c 20 20 2f 20 48 4c
  //   54 a 15*20 30 78 62 36 37 32 2c 20 30 78 31 30 30 30 2c 20 30 62 4*30 2c 20 20 2f 20 52 53 4d a
  //   15*20 30 78 63 66 33 33 2c 20 30 78 32 30 30 30 2c 20 30 62 4*30 2c 20 20 2f 20 53 59 53 a 15*20 30
  //   78 64 39 65 64 2c 20 30 78 33 30 30 30 2c 20 30 62 30 30 31 31 2c 20 20 2f 20 4d 4f 56 a 15*20 30 78
  //   39 39 32 61 2c 20 30 78 34 30 30 30 2c 20 30 62 30 31 30 30 2c 20 20 2f 20 4a 49 46 a 15*20 30 78 61
  //   34 38 63 2c 20 30 78 35 30 30 30 2c 20 30 62 30 30 31 30 2c 20 20 2f 20 4c 44 49 a 15*20 30 78 39 31
  //   65 63 2c 20 30 78 36 30 30 30 2c 20 30 62 30 30 31 31 2c 20 20 2f 20 4c 4f 44 a 15*20 30 78 63 61 39
  //   33 2c 20 30 78 37 30 30 30 2c 20 30 62 30 30 31 31 2c 20 20 2f 20 53 54 52 a 15*20 30 78 39 39 38 31
  //   2c 20 30 78 38 30 30 30 2c 20 30 62 30 31 31 31 2c 20 20 2f 20 41 4c 46 a 15*20 30 78 39 39 32 31 2c
  //   20 30 78 39 30 30 30 2c 20 30 62 4*31 2c 20 20 2f 20 41 49 46 a 15*20 30 78 64 35 38 31 2c 20 30 78
  //   41 30 30 30 2c 20 30 62 30 31 31 31 2c 20 20 2f 20 41 4c 55 a 15*20 30 78 61 35 38 31 2c 20 30 78 42
  //   30 30 30 2c 20 30 62 4*31 2c 20 20 2f 20 41 4c 49 a 15*20 30 78 62 38 63 31 2c 20 30 78 43 30 30 30
  //   2c 20 30 62 30 31 31 31 2c 20 20 2f 20 41 46 4e a 15*20 30 78 62 39 32 31 2c 20 30 78 44 30 30 30 2c
  //   20 30 62 4*31 2c 20 20 2f 20 41 49 4e a 15*20 30 78 63 31 65 65 2c 20 30 78 4*46 2c 20 30 62 4*30 2c
  //   20 20 2f 20 4e 4f 50 a 15*20 3e 54 41 42 4c 45 53 54 4f 50 a 15*20 5d 29 a a 2f 20 52 65 67 69 73 74
  //   65 72 20 74 61 62 6c 65 20 65 6e 74 72 69 65 73 3a 20 28 6d 6e 65 6d 6f 6e 69 63 5f 68 61 73 68 2c
  //   20 74 72 61 6e 73 6c 61 74 69 6f 6e 29 a 28 23 52 65 67 54 61 62 6c 65 20 3d 20 5b 30 78 34 30 46 32
  //   2c 20 30 78 30 2c 20 20 2f 20 52 47 30 a 14*20 30 78 34 34 46 32 2c 20 30 78 31 2c 20 20 2f 20 52 47
  //   31 a 14*20 30 78 34 38 46 32 2c 20 30 78 32 2c 20 20 2f 20 52 47 32 a 14*20 30 78 34 43 46 32 2c 20
  //   30 78 33 2c 20 20 2f 20 52 47 33 a 14*20 30 78 35 30 46 32 2c 20 30 78 34 2c 20 20 2f 20 52 47 34 a
  //   14*20 30 78 35 34 46 32 2c 20 30 78 35 2c 20 20 2f 20 52 47 35 a 14*20 30 78 35 38 46 32 2c 20 30 78
  //   36 2c 20 20 2f 20 52 47 36 a 14*20 30 78 44 32 41 46 2c 20 30 78 36 2c 20 20 2f 20 4f 55 54 a 14*20
  //   30 78 35 43 46 32 2c 20 30 78 37 2c 20 20 2f 20 52 47 37 a 14*20 30 78 30 30 33 32 2c 20 30 78 37 2c
  //   20 20 2f 20 52 41 a 14*20 30 78 30 30 37 30 2c 20 30 78 38 2c 20 20 2f 20 50 43 a 14*20 30 78 30 31
  //   45 39 2c 20 30 78 39 2c 20 20 2f 20 49 4f a 14*20 30 78 39 44 38 36 2c 20 30 78 41 2c 20 20 2f 20 46
  //   4c 47 a 14*20 30 78 30 32 31 33 2c 20 30 78 42 2c 20 20 2f 20 53 50 a 14*20 30 78 38 39 38 38 2c 20
  //   30 78 43 2c 20 20 2f 20 48 4c 42 a 14*20 30 78 39 32 38 33 2c 20 30 78 44 2c 20 20 2f 20 43 54 44 a
  //   14*20 30 78 38 45 30 35 2c 20 30 78 45 2c 20 20 2f 20 45 50 43 a 14*20 30 78 38 37 30 35 2c 20 30 78
  //   46 2c 20 20 2f 20 45 58 41 a 14*20 3e 54 41 42 4c 45 53 54 4f 50 a 14*20 5d 29 a a 2f 20 4d 6f 64 69
  //   66 69 65 72 20 74 61 62 6c 65 20 65 6e 74 72 69 65 73 3a 20 28 6d 6e 65 6d 6f 6e 69 63 5f 68 61 73
  //   68 2c 20 74 72 61 6e 73 6c 61 74 69 6f 6e 29 a 28 23 4d 6f 64 54 61 62 6c 65 20 3d 20 5b 30 78 44 31
  //   45 45 2c 20 30 78 30 2c 20 20 2f 20 4e 4f 54 a 14*20 30 78 39 31 43 31 2c 20 30 78 31 2c 20 20 2f 20
  //   41 4e 44 a 14*20 30 78 30 32 34 46 2c 20 30 78 32 2c 20 20 2f 20 4f 52 a 14*20 30 78 43 39 46 38 2c
  //   20 30 78 33 2c 20 20 2f 20 58 4f 52 a 14*20 30 78 38 39 39 33 2c 20 30 78 34 2c 20 20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
endmodule
