// Digital circuit Sandbox.dig as structural Verilog
module Sandbox (
  input  Clock
);

  wire Ctrl__plus__Alt__plus__Del_out, Pause_out, Power_On___Resume_out, Shutdown_out,
       telescope_computing_system_1_running;
  wire [15:0] Boot_Drive__TBOS_d, eepromdualport_1_d, telescope_computing_system_1_os_adr,
       telescope_computing_system_1_status_code;
  wire [33:0] telescope_computing_system_1_d0_out;

  // Probe Status Code on telescope_computing_system_1_status_code
  Telescope_Computing_System telescope_computing_system_1 (
    .Running(telescope_computing_system_1_running), .Status_Code(telescope_computing_system_1_status_code),
    .Power_On(Power_On___Resume_out), .Clock_Input(Clock), .Pause_CPU(Pause_out),
    .PAUS(Ctrl__plus__Alt__plus__Del_out), .STOP(Shutdown_out), .OS_Adr(telescope_computing_system_1_os_adr),
    .OS_In(Boot_Drive__TBOS_d), .D0_In(eepromdualport_1_d), .D0_Out(telescope_computing_system_1_d0_out),
    .D1_In({16{1'b0}}), .D2_In({16{1'b0}}), .D3_In({16{1'b0}}), .TNET_I_0({20{1'b0}}), .TNET_I_1({20{1'b0}}),
    .TNET_I_2({20{1'b0}}), .TNET_I_3({20{1'b0}}), .K0_In({17{1'b0}}), .K1_In({17{1'b0}}), .K2_In({17{1'b0}}),
    .K3_In({17{1'b0}}), .GPI_0({18{1'b0}}), .GPI_1({18{1'b0}}), .GPI_2({18{1'b0}}), .GPI_3({18{1'b0}}));  // open: D1_Out, D2_Out, D3_Out, TNET_O_0, TNET_O_1, TNET_O_2, TNET_O_3, TK0_Out, TK1_Out, TK2_Out, TK3_Out, GPO_0, GPO_1, GPO_2, GPO_3
  LED Running_Light (.in(telescope_computing_system_1_running));
  Button Power_On___Resume (.out(Power_On___Resume_out));
  Button Pause (.out(Pause_out));
  Button Ctrl__plus__Alt__plus__Del (.out(Ctrl__plus__Alt__plus__Del_out));
  Button Shutdown (.out(Shutdown_out));
  ROM #(.AddrBits(16), .Bits(16)) Boot_Drive__TBOS (
    .A(telescope_computing_system_1_os_adr), .sel(1'b1), .D(Boot_Drive__TBOS_d));
  EEPROMDualPort #(.AddrBits(16), .Bits(16)) eepromdualport_1 (
    .A(telescope_computing_system_1_d0_out[15:0]), .Din(telescope_computing_system_1_d0_out[31:16]),
    .str(telescope_computing_system_1_d0_out[32]), .C(telescope_computing_system_1_d0_out[33]), .ld(1'b1),
    .D(eepromdualport_1_d));

  // Notes on the sheet:
  //   Clock: Hz: 2048
  //   Writable Root Drive
endmodule
