// Logisim project Workspaces.circ as structural Verilog
module CPU_General_Test_Space (
);

  wire clock_1_out, glass_cpu_1_clock_out, glass_cpu_1_cpu_is_reading_i_o, glass_cpu_1_cpu_is_writing_i_o,
       glass_cpu_1_current_process_is_kernel, glass_cpu_1_is_on, glass_cpu_1_ram_write, Off_out, On_out,
       Ready_q, Ready_qn, Rst_out;
  wire [4:0] glass_cpu_1_selected_i_o_device;
  wire [15:0] adder_1_out, Cycles_Used_q, glass_cpu_1_i_o_output, glass_cpu_1_ram_address,
       glass_cpu_1_ram_data_output, ram_1_data, Test_Interface_q;

  Button On (.out(On_out));
  Button Off (.out(Off_out));
  Clock clock_1 (.out(clock_1_out));
  Button Rst (.out(Rst_out));
  LED led_1 (.in(glass_cpu_1_is_on));
  Glass_CPU glass_cpu_1 (
    .Clock_Input(clock_1_out), .Reset_CPU(Rst_out), .Start_CPU(On_out), .Pause_CPU(Off_out),
    .RAM_Data_Input(ram_1_data), .RAM_Data_Output(glass_cpu_1_ram_data_output),
    .RAM_Write(glass_cpu_1_ram_write), .RAM_Address(glass_cpu_1_ram_address), .I_O_Is_Reading_CPU(Ready_qn),
    .CPU_Is_Writing_I_O(glass_cpu_1_cpu_is_writing_i_o), .I_O_Output(glass_cpu_1_i_o_output),
    .I_O_Input(Test_Interface_q), .CPU_Is_Reading_I_O(glass_cpu_1_cpu_is_reading_i_o),
    .I_O_Is_Writing_CPU(Ready_q), .Selected_I_O_Device(glass_cpu_1_selected_i_o_device),
    .Current_Process_Is_Kernel(glass_cpu_1_current_process_is_kernel), .Is_On(glass_cpu_1_is_on),
    .Clock_Out(glass_cpu_1_clock_out), .Mask_Int_Lines(3'b000), .Non_Msk_Int(1'b0));  // open: HLB_For_Current_Process, Program_Counter
  RAM #(.addrWidth(16), .dataWidth(16), .bus("separate")) ram_1 (
    .addr(glass_cpu_1_ram_address), .din(glass_cpu_1_ram_data_output), .data(ram_1_data),
    .str(glass_cpu_1_ram_write), .clk(clock_1_out));  // open: sel, ld, clr
  LED led_2 (.in(glass_cpu_1_current_process_is_kernel));
  // Probe on glass_cpu_1_selected_i_o_device
  // Probe on adder_1_out
  Adder #(.width(16)) adder_1 (.a(16'h2), .b(glass_cpu_1_ram_address), .out(adder_1_out));  // open: cin, cout
  // Probe on Cycles_Used_q
  Counter #(.width(16), .max('hffff)) Cycles_Used (
    .Q(Cycles_Used_q), .clk(glass_cpu_1_clock_out), .clr(Rst_out));  // open: load, D, count, carry
  Register #(.width(16)) Test_Interface (
    .D(glass_cpu_1_i_o_output), .en(glass_cpu_1_cpu_is_writing_i_o), .Q(Test_Interface_q), .clk(clock_1_out));  // open: clr
  // Probe on Test_Interface_q
  S_R_Flip_Flop Ready (
    .S(1'b0), .clk(clock_1_out), .R(glass_cpu_1_cpu_is_reading_i_o), .Q(Ready_q), .Qn(Ready_qn),
    .reset(Rst_out));  // open: preset, en
  LED led_3 (.in(Ready_q));

  // Notes on the sheet:
  //   Currently set up for: IO Test
endmodule

module Assembler_Workspace (
);

  wire assembler_workspace_1_bad_number, assembler_workspace_1_instruction_not_found,
       assembler_workspace_1_is_running, assembler_workspace_1_label_not_found,
       assembler_workspace_1_non_empty_stack, assembler_workspace_1_operand_not_found,
       assembler_workspace_1_output_clear, assembler_workspace_1_output_clock,
       assembler_workspace_1_output_store, assembler_workspace_1_ram_clock, assembler_workspace_1_ram_store,
       assembler_workspace_1_success, assembler_workspace_1_tty_clear, assembler_workspace_1_tty_clock,
       assembler_workspace_1_tty_write, I_out, O_out, R_out;
  wire [6:0] assembler_workspace_1_tty_data, rom_1_data;
  wire [15:0] assembler_workspace_1_output_address, assembler_workspace_1_output_data,
       assembler_workspace_1_ram_address, assembler_workspace_1_ram_data_out,
       assembler_workspace_1_rtl_file_line, ram_1_data;
  wire [19:0] assembler_workspace_1_input_address;
  wire [31:0] assembler_workspace_1_cycles_used;

  Button R (.out(R_out));
  Button I (.out(I_out));
  Button O (.out(O_out));
  LED On (.in(assembler_workspace_1_is_running));
  ROM #(.addrWidth(20), .dataWidth(7)) rom_1 (
    .addr(assembler_workspace_1_input_address), .data(rom_1_data));  // open: sel
  TTY #(.rows(20), .cols(100)) tty_1 (
    .data(assembler_workspace_1_tty_data), .clk(assembler_workspace_1_tty_clock),
    .we(assembler_workspace_1_tty_write), .clr(assembler_workspace_1_tty_clear));
  RAM #(.addrWidth(16), .dataWidth(16), .bus("separate")) ram_1 (
    .addr(assembler_workspace_1_ram_address), .din(assembler_workspace_1_ram_data_out), .data(ram_1_data),
    .str(assembler_workspace_1_ram_store), .clk(assembler_workspace_1_ram_clock));  // open: sel, ld, clr
  Computers_Assembler_Workspace assembler_workspace_1 (
    .Reset_Machine(R_out), .Start(I_out), .Pause(O_out), .Is_Running(assembler_workspace_1_is_running),
    .Input_Data(rom_1_data), .Input_Address(assembler_workspace_1_input_address),
    .Bad_Number(assembler_workspace_1_bad_number), .Label_Not_Found(assembler_workspace_1_label_not_found),
    .Non_Empty_Stack(assembler_workspace_1_non_empty_stack),
    .Instruction_Not_Found(assembler_workspace_1_instruction_not_found),
    .Operand_Not_Found(assembler_workspace_1_operand_not_found), .Success(assembler_workspace_1_success),
    .Output_Address(assembler_workspace_1_output_address), .Output_Data(assembler_workspace_1_output_data),
    .Output_Clock(assembler_workspace_1_output_clock), .Output_Store(assembler_workspace_1_output_store),
    .Output_Clear(assembler_workspace_1_output_clear), .RAM_Address(assembler_workspace_1_ram_address),
    .RAM_Data_Out(assembler_workspace_1_ram_data_out), .RAM_Store(assembler_workspace_1_ram_store),
    .RAM_Clock(assembler_workspace_1_ram_clock), .RAM_Data_In(ram_1_data),
    .RTL_File_Line(assembler_workspace_1_rtl_file_line), .Cycles_Used(assembler_workspace_1_cycles_used),
    .TTY_Clear(assembler_workspace_1_tty_clear), .TTY_Write(assembler_workspace_1_tty_write),
    .TTY_Data(assembler_workspace_1_tty_data), .TTY_Clock(assembler_workspace_1_tty_clock));
  // Probe on assembler_workspace_1_rtl_file_line
  // Probe on assembler_workspace_1_cycles_used
  LED led (.in(assembler_workspace_1_bad_number));
  LED Lb (.in(assembler_workspace_1_label_not_found));
  LED led_2 (.in(assembler_workspace_1_non_empty_stack));
  LED In (.in(assembler_workspace_1_instruction_not_found));
  LED Op (.in(assembler_workspace_1_operand_not_found));
  LED led_3 (.in(assembler_workspace_1_success));
  RAM #(.addrWidth(16), .dataWidth(16), .bus("separate")) ram_2 (
    .addr(assembler_workspace_1_output_address), .din(assembler_workspace_1_output_data),
    .str(assembler_workspace_1_output_store), .clk(assembler_workspace_1_output_clock),
    .clr(assembler_workspace_1_output_clear));  // open: data, sel, ld

  // Notes on the sheet:
  //   contents of rom_1 (hex, n*v repeats v):
  //   2f 20 54 65 73 74 20 63 6f 6d 6d 65 6e 74 a 2f 20 54 68 69 73 20 69 73 20 61 20 73 69 6d 70 6c 65 2c
  //   20 69 6e 63 72 65 6d 65 6e 74 61 6c 20 74 65 73 74 20 66 69 6c 65 20 66 6f 72 20 74 68 65 20 61 73
  //   73 65 6d 62 6c 65 72 2e a 2f 20 54 68 69 73 20 69 73 20 6e 6f 74 20 6d 65 61 6e 74 20 74 6f 20 61 63
  //   74 75 61 6c 6c 79 20 72 75 6e 20 6f 6e 20 74 68 65 20 43 50 55 2e a 2f 20 54 65 73 74 20 65 6d 70 74
  //   79 20 6c 69 6e 65 a a 2f 20 54 65 73 74 20 63 6f 6d 6d 61 6e 64 a 25 54 45 53 54 20 43 4f 4d 4d 41
  //   4e 44 25 a a 2f 20 54 65 73 74 20 63 6f 6e 73 74 61 6e 74 a 40 43 4f 4e 53 54 41 4e 54 20 3d 20 32 a
  //   a 2f 20 54 65 73 74 20 6c 61 62 65 6c a 23 4d 79 4c 61 62 65 6c a a 2f 20 54 65 73 74 20 69 6e 73 74
  //   72 75 63 74 69 6f 6e 73 a 4d 4f 56 20 52 47 30 20 52 47 31 a 41 4c 55 20 41 44 44 20 52 47 30 20 52
  //   47 31 a a 2f 20 54 65 73 74 20 68 65 78 20 6e 75 6d 62 65 72 a 30 78 30 32 32 32 a a 2f 20 54 65 73
  //   74 20 64 65 63 20 6e 75 6d 62 65 72 a 35 a a 2f 20 54 65 73 74 20 62 69 6e 61 72 79 20 6e 75 6d 62
  //   65 72 a 30 62 30 31 30 31 30 a a 2f 20 54 65 73 74 20 63 68 61 72 61 63 74 65 72 a 27 61 27 a a 2f
  //   20 54 65 73 74 20 6e 65 77 6c 69 6e 65 20 61 73 20 63 68 61 72 61 63 74 65 72 a 27 a 27 a a 2f 20 54
  //   65 73 74 20 63 6f 6d 6d 65 6e 74 20 61 73 20 63 68 61 72 61 63 74 65 72 a 27 2f 27 a a 2f 20 54 65
  //   73 74 20 63 68 61 72 61 63 74 65 72 20 73 79 6d 62 6f 6c 20 61 73 20 63 68 61 72 61 63 74 65 72 a 27
  //   27 27 20 2f 27 a a 2f 20 54 65 73 74 20 6c 61 62 65 6c 20 72 65 66 65 72 65 6e 63 65 a 3e 4d 79 4c
  //   61 62 65 6c a a 2f 20 54 65 73 74 20 63 6f 6e 73 74 61 6e 74 20 72 65 66 65 72 65 6e 63 65 a 3e 43
  //   4f 4e 53 54 41 4e 54 a a 2f 20 54 65 73 74 20 65 6d 70 74 79 20 61 72 72 61 79 20 63 6f 6e 73 74 72
  //   75 63 74 69 6f 6e a 23 4d 79 41 72 72 61 79 20 3d 20 28 7e 35 29 a 30 78 4*46 a a 2f 20 54 65 73 74
  //   20 73 61 6d 65 6c 69 6e 65 20 69 6e 73 74 72 75 63 74 69 6f 6e 73 a 4c 44 49 20 52 41 20 3e 4d 79 52
  //   65 74 75 72 6e 3b 20 4d 4f 56 20 50 43 20 52 41 3b 20 23 4d 79 52 65 74 75 72 6e a a 2f 20 54 65 73
  //   74 20 73 74 6f 70 20 61 73 73 65 6d 62 6c 65 72 20 77 69 74 68 6f 75 74 20 6e 65 77 6c 69 6e 65 20
  //   61 74 20 65 6e 64 20 6f 66 20 66 69 6c 65 2e
endmodule

module ASCII_File_Display (
  input  Enable
);

  wire and_1_out, C_out, clock_1_out, R_out;
  wire [6:0] bit_extender_1_out;
  wire [15:0] counter_1_q, rom_1_data;

  and and_1 (and_1_out, C_out, clock_1_out);
  Clock clock_1 (.out(clock_1_out));
  Button R (.out(R_out));
  Counter #(.width(16), .max('hffff)) counter_1 (
    .count(Enable), .Q(counter_1_q), .clk(and_1_out), .clr(R_out));  // open: load, D, carry
  Button C (.out(C_out));
  ROM #(.addrWidth(16), .dataWidth(16)) rom_1 (.addr(counter_1_q), .data(rom_1_data), .sel(Enable));
  Bit_Extender #(.in_width(16), .out_width(7)) bit_extender_1 (.in(rom_1_data), .out(bit_extender_1_out));
  TTY #(.rows(48), .cols(96)) tty_1 (.data(bit_extender_1_out), .clk(and_1_out), .we(Enable), .clr(R_out));

  // Notes on the sheet:
  //   contents of rom_1 (hex, n*v repeats v):
  //   4a 49 46 20 54 52 55 20 3e 53 74 61 72 74 50 6f 69 6e 74 a a 28 2f 20 43 6f 6e 73 74 61 6e 74 73 2c
  //   20 76 61 72 69 61 62 6c 65 73 2c 20 61 6e 64 20 74 61 62 6c 65 73 2e a 40 49 4e 46 4c 47 20 3d 20 30
  //   a 40 4f 55 54 46 4c 47 20 3d 20 30 78 38 30 30 a a 40 54 41 42 4c 45 53 54 4f 50 20 3d 20 30 78 4*46
  //   20 20 2f 20 4d 75 73 74 20 73 74 61 79 20 4e 55 4c 4c 2e a a 2f 20 49 6e 73 74 72 75 63 74 69 6f 6e
  //   20 74 61 62 6c 65 20 65 6e 74 72 69 65 73 3a 20 28 6d 6e 65 6d 6f 6e 69 63 5f 68 61 73 68 2c 20 74
  //   72 61 6e 73 6c 61 74 69 6f 6e 2c 20 6f 70 65 72 61 6e 64 5f 62 69 74 6d 61 70 29 a 28 23 49 6e 73 74
  //   54 61 62 6c 65 20 3d 20 5b 30 78 64 31 38 38 2c 20 30 78 4*30 2c 20 30 62 4*30 2c 20 20 2f 20 48 4c
  //   54 a 15*20 30 78 62 36 37 32 2c 20 30 78 31 30 30 30 2c 20 30 62 4*30 2c 20 20 2f 20 52 53 4d a
  //   15*20 30 78 63 66 33 33 2c 20 30 78 32 30 30 30 2c 20 30 62 4*30 2c 20 20 2f 20 53 59 53 a 15*20 30
  //   78 64 39 65 64 2c 20 30 78 33 30 30 30 2c 20 30 62 30 30 31 31 2c 20 20 2f 20 4d 4f 56 a 15*20 30 78
  //   39 39 32 61 2c 20 30 78 34 30 30 30 2c 20 30 62 30 31 30 30 2c 20 20 2f 20 4a 49 46 a 15*20 30 78 61
  //   34 38 63 2c 20 30 78 35 30 30 30 2c 20 30 62 30 30 31 30 2c 20 20 2f 20 4c 44 49 a 15*20 30 78 39 31
  //   65 63 2c 20 30 78 36 30 30 30 2c 20 30 62 30 30 31 31 2c 20 20 2f 20 4c 4f 44 a 15*20 30 78 63 61 39
  //   33 2c 20 30 78 37 30 30 30 2c 20 30 62 30 30 31 31 2c 20 20 2f 20 53 54 52 a 15*20 30 78 39 39 38 31
  //   2c 20 30 78 38 30 30 30 2c 20 30 62 30 31 31 31 2c 20 20 2f 20 41 4c 46 a 15*20 30 78 39 39 32 31 2c
  //   20 30 78 39 30 30 30 2c 20 30 62 4*31 2c 20 20 2f 20 41 49 46 a 15*20 30 78 64 35 38 31 2c 20 30 78
  //   41 30 30 30 2c 20 30 62 30 31 31 31 2c 20 20 2f 20 41 4c 55 a 15*20 30 78 61 35 38 31 2c 20 30 78 42
  //   30 30 30 2c 20 30 62 4*31 2c 20 20 2f 20 41 4c 49 a 15*20 30 78 62 38 63 31 2c 20 30 78 43 30 30 30
  //   2c 20 30 62 30 31 31 31 2c 20 20 2f 20 41 46 4e a 15*20 30 78 62 39 32 31 2c 20 30 78 44 30 30 30 2c
  //   20 30 62 4*31 2c 20 20 2f 20 41 49 4e a 15*20 30 78 63 31 65 65 2c 20 30 78 4*46 2c 20 30 62 4*30 2c
  //   20 20 2f 20 4e 4f 50 a 15*20 3e 54 41 42 4c 45 53 54 4f 50 a 15*20 5d 29 a a 2f 20 52 65 67 69 73 74
  //   65 72 20 74 61 62 6c 65 20 65 6e 74 72 69 65 73 3a 20 28 6d 6e 65 6d 6f 6e 69 63 5f 68 61 73 68 2c
  //   20 74 72 61 6e 73 6c 61 74 69 6f 6e 29 a 28 23 52 65 67 54 61 62 6c 65 20 3d 20 5b 30 78 34 30 46 32
  //   2c 20 30 78 30 2c 20 20 2f 20 52 47 30 a 14*20 30 78 34 34 46 32 2c 20 30 78 31 2c 20 20 2f 20 52 47
  //   31 a 14*20 30 78 34 38 46 32 2c 20 30 78 32 2c 20 20 2f 20 52 47 32 a 14*20 30 78 34 43 46 32 2c 20
  //   30 78 33 2c 20 20 2f 20 52 47 33 a 14*20 30 78 35 30 46 32 2c 20 30 78 34 2c 20 20 2f 20 52 47 34 a
  //   14*20 30 78 35 34 46 32 2c 20 30 78 35 2c 20 20 2f 20 52 47 35 a 14*20 30 78 35 38 46 32 2c 20 30 78
  //   36 2c 20 20 2f 20 52 47 36 a 14*20 30 78 44 32 41 46 2c 20 30 78 36 2c 20 20 2f 20 4f 55 54 a 14*20
  //   30 78 35 43 46 32 2c 20 30 78 37 2c 20 20 2f 20 52 47 37 a 14*20 30 78 30 30 33 32 2c 20 30 78 37 2c
  //   20 20 2f 20 52 41 a 14*20 30 78 30 30 37 30 2c 20 30 78 38 2c 20 20 2f 20 50 43 a 14*20 30 78 30 31
  //   45 39 2c 20 30 78 39 2c 20 20 2f 20 49 4f a 14*20 30 78 39 44 38 36 2c 20 30 78 41 2c 20 20 2f 20 46
  //   4c 47 a 14*20 30 78 30 32 31 33 2c 20 30 78 42 2c 20 20 2f 20 53 50 a 14*20 30 78 38 39 38 38 2c 20
  //   30 78 43 2c 20 20 2f 20 48 4c 42 a 14*20 30 78 39 32 38 33 2c 20 30 78 44 2c 20 20 2f 20 43 54 44 a
  //   14*20 30 78 38 45 30 35 2c 20 30 78 45 2c 20 20 2f 20 45 50 43 a 14*20 30 78 38 37 30 35 2c 20 30 78
  //   46 2c 20 20 2f 20 45 58 41 a 14*20 3e 54 41 42 4c 45 53 54 4f 50 a 14*20 5d 29 a a 2f 20 4d 6f 64 69
  //   66 69 65 72 20 74 61 62 6c 65 20 65 6e 74 72 69 65 73 3a 20 28 6d 6e 65 6d 6f 6e 69 63 5f 68 61 73
  //   68 2c 20 74 72 61 6e 73 6c 61 74 69 6f 6e 29 a 28 23 4d 6f 64 54 61 62 6c 65 20 3d 20 5b 30 78 44 31
  //   45 45 2c 20 30 78 30 2c 20 20 2f 20 4e 4f 54 a 14*20 30 78 39 31 43 31 2c 20 30 78 31 2c 20 20 2f 20
  //   41 4e 44 a 14*20 30 78 30 32 34 46 2c 20 30 78 32 2c 20 20 2f 20 4f 52 a 14*20 30 78 43 39 46 38 2c
  //   20 30 78 33 2c 20 20 2f 20 58 4f 52 a 14*20 30 78 38 39 39 33 2c 20 30 78 34 2c 20 20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
endmodule
